// Logisim project Computer_Diagram.circ as structural Verilog: 22 circuits, main circuit main
module main (
  input  in_1,
  input  in_2,
  input  in_3,
  input  in_4,
  input  in_5
);

  wire and_1_out, and_2_out, and_3_out, and_4_out, and_5_out, cpu_1_dev_eout, cpu_1_mrw_out, not_1_out,
       not_2_out, not_3_out, not_4_out, undriven;
  wire [7:0] controlled_buffer_1_out, controlled_buffer_2_out, cpu_1_dev_dout, cpu_1_mdat_out,
       pull_resistor_1_node, ram_1_dout, ram_2_dout, rom_1_data, undriven_2;
  wire [15:0] cpu_1_addr_out;

  CPU cpu_1 (
    .ADDR_OUT(cpu_1_addr_out), .MRW_OUT(cpu_1_mrw_out), .MDAT_OUT(cpu_1_mdat_out), .DEV_DOUT(cpu_1_dev_dout),
    .DEV_EOUT(cpu_1_dev_eout), .EX_CLOCK(in_1), .HALT(in_5), .POWER(in_5), .RESET(in_4),
    .MD_IN(pull_resistor_1_node), .DEV_DIN(undriven_2), .DEV_EIN(undriven), .IRQ(in_2), .NMI(in_3));  // open: INTP, IRQE, ERR, UUSD, PCS
  not not_1 (not_1_out, cpu_1_mrw_out);
  not not_2 (not_2_out, cpu_1_mrw_out);
  and and_1 (and_1_out, not_1_out, in_1, not_3_out);
  not not_3 (not_3_out, cpu_1_addr_out[15]);
  not not_4 (not_4_out, cpu_1_addr_out[14]);
  and and_2 (and_2_out, not_4_out, cpu_1_addr_out[15]);
  and and_3 (and_3_out, and_2_out, in_1);
  and and_4 (and_4_out, cpu_1_addr_out[14], cpu_1_addr_out[15]);
  and and_5 (and_5_out, and_4_out, in_1);
  ROM #(.addrWidth(15)) rom_1 (.addr(cpu_1_addr_out[14:0]), .data(rom_1_data));
  RAM #(.addrWidth(14), .trigger("high")) ram_1 (
    .addr(cpu_1_addr_out[13:0]), .we(cpu_1_mrw_out), .oe(not_2_out), .din(controlled_buffer_1_out),
    .dout(ram_1_dout));
  assign controlled_buffer_1_out = and_3_out ? cpu_1_mdat_out : 8'bz;  // Controlled_Buffer controlled_buffer_1
  RAM #(.addrWidth(14), .trigger("high")) ram_2 (
    .addr(cpu_1_addr_out[13:0]), .we(cpu_1_mrw_out), .oe(not_2_out), .din(controlled_buffer_2_out),
    .dout(ram_2_dout));
  assign controlled_buffer_2_out = and_5_out ? cpu_1_mdat_out : 8'bz;  // Controlled_Buffer controlled_buffer_2
  Pull_Resistor pull_resistor_1 (.node(pull_resistor_1_node));
  assign pull_resistor_1_node = and_1_out ? rom_1_data : 8'bz;  // Controlled_Buffer controlled_buffer_3
  assign pull_resistor_1_node = and_2_out ? ram_1_dout : 8'bz;  // Controlled_Buffer controlled_buffer_4
  assign pull_resistor_1_node = and_4_out ? ram_2_dout : 8'bz;  // Controlled_Buffer controlled_buffer_5

  // Notes on the sheet:
  //   contents of rom_1 (hex, n*v repeats v):
  //   8 0 e8 1 0 f0 0 10
endmodule

module CPU (
  input  EX_CLOCK,
  input  [7:0] MD_IN,
  input  [7:0] DEV_DIN,
  input  DEV_EIN,
  input  IRQ,
  input  NMI,
  input  HALT,
  input  POWER,
  input  RESET,
  output [15:0] ADDR_OUT,
  output MRW_OUT,
  output [7:0] MDAT_OUT,
  output [7:0] DEV_DOUT,
  output DEV_EOUT,
  output INTP,
  output IRQE,
  output ERR,
  output UUSD,
  output PCS
);

  wire addressing_module_1_read_out, and_1_out, and_2_out, and_3_out, and_4_out, and_6_out, and_7_out, CLK,
       clock_1_out, DB_RCTX, DB_WCTX, HALT_t, HIRQ_out, IMM1_BUS, INB_out, instruction_buffer_1_buff_full,
       instruction_buffer_1_err, instruction_buffer_1_irq_t, instruction_buffer_1_nmi_t,
       instruction_buffer_1_rdy, instruction_buffer_1_rst_t, instruction_buffer_1_unused,
       instruction_decoder_1_c_irq, instruction_decoder_1_c_nmi, instruction_decoder_1_c_rst,
       instruction_decoder_1_cbuff, instruction_decoder_1_cclt, instruction_decoder_1_db_irctx,
       instruction_decoder_1_dbus_cpy, instruction_decoder_1_edat1, instruction_decoder_1_edat2,
       instruction_decoder_1_flags_e, instruction_decoder_1_id_pc, instruction_decoder_1_id_sp,
       instruction_decoder_1_iob_cpy, instruction_decoder_1_ir_qt, instruction_decoder_1_lc_pc,
       instruction_decoder_1_ld_xf, instruction_decoder_1_ldy, instruction_decoder_1_mdspec,
       instruction_decoder_1_memb_cpy, instruction_decoder_1_pcm_e, instruction_decoder_1_rhle,
       instruction_decoder_1_rpc_h, instruction_decoder_1_rpc_l, instruction_decoder_1_rread,
       instruction_decoder_1_rwrite, instruction_decoder_1_spm_e, INT_out, io_interface_1_input_declare_out,
       IRQ_E, IRT_out, JNE_out, LDM_out, not_1_out, not_2_out, not_3_out, not_4_out, not_5_out, not_6_out,
       not_7_out, not_8_out, not_9_out, not_10_out, or_1_out, or_2_out, or_3_out, or_4_out, or_5_out,
       or_6_out, or_7_out, or_8_out, or_9_out, or_11_out, or_12_out, or_13_out, or_14_out, or_15_out,
       OUB_out, pull_resistor_4_node, pull_resistor_6_node, RESET_t, SDB_out, SIRQ_out, STM_out,
       temp_test_1_out_2, VCC, WDB_out, xor_1_out, xor_2_out;
  wire [2:0] ADD3_BUS, AOP_BUS;
  wire [7:0] D_IN, DATA_BUS, instruction_buffer_1_instruction, io_interface_1_input_data_out, ram_1_dout,
       ram_2_dout, register_1_q, rom_1_data, STATE_BUS;
  wire [13:0] pull_resistor_8_node, pull_resistor_9_node;
  wire [14:0] controlled_buffer_3_out, pull_resistor_7_node;
  wire [15:0] ADD16_BUS, aux_registers_1_sp_out;

  Clock clock_1 (.out(clock_1_out));
  and HIRQ (HIRQ_out, IRQ_E, IRQ);
  and SIRQ (SIRQ_out, IRQ_E, INT_out);
  LED led_1 (.in(CLK));
  CPU_CLOCK cpu_clock_1 (
    .INTERNAL_CLOCK(clock_1_out), .VCC(VCC), .EXTERNAL_CLOCK(EX_CLOCK), .HALT_IN(HALT_t), .CLOCK_OUT(CLK));
  Instruction_Buffer instruction_buffer_1 (
    .UNUSED(instruction_buffer_1_unused), .MBUS_DOUT(DATA_BUS),
    .INSTRUCTION(instruction_buffer_1_instruction), .ARG_8BIT(DATA_BUS), .ARG_16BIT(ADD16_BUS),
    .REG_ADD(ADD3_BUS), .ALU_OPC(AOP_BUS), .INT_VAL(IMM1_BUS), .RDY(instruction_buffer_1_rdy),
    .BUFF_FULL(instruction_buffer_1_buff_full), .ERR(instruction_buffer_1_err),
    .RST_T(instruction_buffer_1_rst_t), .IRQ_T(instruction_buffer_1_irq_t),
    .NMI_T(instruction_buffer_1_nmi_t), .CLOCK(CLK), .MBUS_OE(and_3_out), .STB_BUFF(not_4_out), .DAT(D_IN),
    .CLEAR_BUFF(instruction_decoder_1_cbuff), .ARG1_E(instruction_decoder_1_edat1),
    .ARG2_E(instruction_decoder_1_edat2), .S_IRQ(SIRQ_out), .IRQ(HIRQ_out),
    .C_IRQ(instruction_decoder_1_c_irq), .NMI(NMI), .C_NMI(instruction_decoder_1_c_nmi), .RST(RESET_t),
    .C_RST(instruction_decoder_1_c_rst), .DBO_TRUE(or_13_out));
  ALU alu_1 (
    .DATA_OUT(DATA_BUS), .FOUT(STATE_BUS), .CLOCK(CLK), .CALCULATE(instruction_decoder_1_cclt),
    .GET_FLAGS(instruction_decoder_1_flags_e), .LDF(instruction_decoder_1_ld_xf),
    .LDX(instruction_decoder_1_ld_xf), .LDY(instruction_decoder_1_ldy), .OPERATION(AOP_BUS),
    .STATE_IN(STATE_BUS), .DATA_IN(DATA_BUS), .RESET(instruction_decoder_1_c_rst));
  Registers registers_1 (
    .DATA_OUT(DATA_BUS), .HL_OUT(ADD16_BUS), .F_OUT(STATE_BUS), .CLOCK(CLK),
    .Write(instruction_decoder_1_rwrite), .Read(instruction_decoder_1_rread), .Address(ADD3_BUS),
    .DATA_IN(DATA_BUS), .RESET(instruction_decoder_1_c_rst), .HLE(instruction_decoder_1_rhle),
    .FIN(STATE_BUS), .EFIN(instruction_decoder_1_flags_e));
  AUX_Registers aux_registers_1 (
    .PC_OUT(ADD16_BUS), .SP_OUT(aux_registers_1_sp_out), .PC_HOUT(DATA_BUS), .PC_LOUT(DATA_BUS),
    .RESET(instruction_decoder_1_c_rst), .EChangePC(instruction_decoder_1_pcm_e),
    .IN_DEC_PC(instruction_decoder_1_id_pc), .LOAD_COUNT(or_4_out), .IMM16_DATA(ADD16_BUS),
    .PC_EH(instruction_decoder_1_rpc_h), .PC_EL(instruction_decoder_1_rpc_l), .CLOCK(CLK),
    .IN_DEC_SP(instruction_decoder_1_id_sp), .EChangeSP(instruction_decoder_1_spm_e));
  not not_1 (not_1_out, instruction_decoder_1_c_rst);
  not not_2 (not_2_out, IRT_out);
  not not_3 (not_3_out, instruction_decoder_1_c_rst);
  and and_1 (and_1_out, or_3_out, not_1_out, not_2_out);
  and and_2 (and_2_out, IMM1_BUS, not_3_out);
  or or_1 (or_1_out, or_3_out, or_2_out);
  or or_2 (or_2_out, IRT_out, instruction_decoder_1_c_rst);
  Pull_Resistor pull_resistor_1 (.node(DATA_BUS));
  not not_4 (not_4_out, instruction_buffer_1_buff_full);
  or or_3 (or_3_out, instruction_buffer_1_irq_t, instruction_buffer_1_nmi_t);
  temp_test temp_test_1 (.in_1(DATA_BUS), .out_2(temp_test_1_out_2));
  assign DATA_BUS = WDB_out ? register_1_q : 8'bz;  // Controlled_Buffer controlled_buffer_1
  Register register_1 (.D(DATA_BUS), .en(SDB_out), .clk(CLK), .Q(register_1_q));  // open: clr
  PSR_Register psr_register_1 (
    .INTP_D(and_1_out), .IRQE_D(and_2_out), .ERR_D(instruction_buffer_1_err),
    .UN_D(instruction_buffer_1_unused), .INTP_E(or_1_out), .IRQE_E(or_2_out), .ERR_E(1'b1), .UN_E(1'b1),
    .CLOCK(CLK), .HALT(HALT), .VCC(POWER), .RESET(RESET), .HALT_OUT(HALT_t), .VCC_OUT(VCC),
    .RESET_OUT(RESET_t), .INTP(INTP), .IRQE(IRQE), .ERR(ERR), .UUSD(UUSD), .PCS(PCS));
  assign DATA_BUS = INB_out ? io_interface_1_input_data_out : 8'bz;  // Controlled_Buffer controlled_buffer_2
  and and_3 (and_3_out, instruction_buffer_1_buff_full, addressing_module_1_read_out);
  Pull_Resistor #(.pull(1)) pull_resistor_2 (.node(STATE_BUS[2]));
  not not_5 (not_5_out, STATE_BUS[2]);
  and JNE (JNE_out, not_5_out, instruction_decoder_1_lc_pc, or_5_out);
  or or_4 (or_4_out, JNE_out, and_4_out);
  IO_INTERFACE io_interface_1 (
    .INPUT_DATA_IN(DEV_DIN), .INPUT_DECLARE_IN(DEV_EIN), .OUTPUT_DATA_IN(DATA_BUS),
    .OUTPUT_DECLARE_IN(OUB_out), .INPUT_DATA_OUT(io_interface_1_input_data_out),
    .INPUT_DECLARE_OUT(io_interface_1_input_declare_out), .OUTPUT_DECLARE_OUT(DEV_EOUT),
    .OUTPUT_DATA_OUT(DEV_DOUT));
  and and_4 (and_4_out, or_6_out, instruction_decoder_1_lc_pc);
  Hex_Digit_Display hex_digit_display_1 (.value(ADDR_OUT[15:12]));  // open: dp
  Hex_Digit_Display hex_digit_display_2 (.value(ADDR_OUT[11:8]));  // open: dp
  Hex_Digit_Display hex_digit_display_3 (.value(ADDR_OUT[7:4]));  // open: dp
  Hex_Digit_Display hex_digit_display_4 (.value(ADDR_OUT[3:0]));  // open: dp
  Register #(.trigger("high")) DB_REG (.D(DATA_BUS), .en(1'b1), .clk(1'b1));  // open: Q, clr
  Addressing_Module addressing_module_1 (
    .CLOCK(CLK), .BIT16_D(ADD16_BUS), .SP_16bit(aux_registers_1_sp_out),
    .MASpec(instruction_decoder_1_mdspec), .READ(LDM_out), .WRITE(STM_out), .DATA_IN(DATA_BUS),
    .ADDRESS_OUT(ADDR_OUT), .DATA_OUT(MDAT_OUT), .READ_OUT(addressing_module_1_read_out), .WRITE_OUT(MRW_OUT));
  Instruction_Decoder instruction_decoder_1 (
    .ID_SP(instruction_decoder_1_id_sp), .SPM_E(instruction_decoder_1_spm_e),
    .LD_XF(instruction_decoder_1_ld_xf), .LDY(instruction_decoder_1_ldy), .CCLT(instruction_decoder_1_cclt),
    .FLAGS_E(instruction_decoder_1_flags_e), .IOB_CPY(instruction_decoder_1_iob_cpy),
    .ID_PC(instruction_decoder_1_id_pc), .PCM_E(instruction_decoder_1_pcm_e),
    .LC_PC(instruction_decoder_1_lc_pc), .RPC_H(instruction_decoder_1_rpc_h),
    .RPC_L(instruction_decoder_1_rpc_l), .RHLE(instruction_decoder_1_rhle),
    .MEMB_CPY(instruction_decoder_1_memb_cpy), .C_RST(instruction_decoder_1_c_rst),
    .DB_IRCTX(instruction_decoder_1_db_irctx), .ADD_16(ADD16_BUS), .C_IRQ(instruction_decoder_1_c_irq),
    .C_NMI(instruction_decoder_1_c_nmi), .CBUFF(instruction_decoder_1_cbuff),
    .RREAD(instruction_decoder_1_rread), .RWRITE(instruction_decoder_1_rwrite),
    .MDSpec(instruction_decoder_1_mdspec), .EDAT1(instruction_decoder_1_edat1),
    .EDAT2(instruction_decoder_1_edat2), .IR_QT(instruction_decoder_1_ir_qt),
    .DBUS_CPY(instruction_decoder_1_dbus_cpy), .EXECUTE(instruction_buffer_1_buff_full),
    .RESET_DECODER(instruction_buffer_1_rdy), .IRQ(instruction_buffer_1_irq_t),
    .NMI(instruction_buffer_1_nmi_t), .RESET_CPU(instruction_buffer_1_rst_t), .ADD_8(DATA_BUS), .CLOCK(CLK),
    .Instruction_IN(instruction_buffer_1_instruction));
  or or_5 (or_5_out, instruction_decoder_1_rhle, instruction_decoder_1_edat2);
  or or_6 (or_6_out, instruction_decoder_1_c_irq, instruction_decoder_1_c_nmi, instruction_decoder_1_c_rst);
  and and_5 (IRQ_E, IRQE, not_6_out);
  not not_6 (not_6_out, INTP);
  Register #(.trigger("high"), .width(3)) AOP_REG (.D(AOP_BUS), .en(1'b1), .clk(1'b1));  // open: Q, clr
  Register #(.trigger("high"), .width(3)) RAD_REG (.D(ADD3_BUS), .en(1'b1), .clk(1'b1));  // open: Q, clr
  Register #(.trigger("high")) SB_REG (.D(STATE_BUS), .en(1'b1), .clk(1'b1));  // open: Q, clr
  Register #(.trigger("high"), .width(16)) D16_REG (.D(ADD16_BUS), .en(1'b1), .clk(1'b1));  // open: Q, clr
  and INT (INT_out, instruction_decoder_1_mdspec, instruction_decoder_1_ir_qt);
  Register #(.trigger("high")) MO_REG (.D(MDAT_OUT), .en(1'b1), .clk(1'b1));  // open: Q, clr
  not not_7 (not_7_out, instruction_decoder_1_mdspec);
  and IRT (IRT_out, not_7_out, instruction_decoder_1_ir_qt);
  and SDB (SDB_out, instruction_decoder_1_dbus_cpy, or_7_out);
  Register #(.trigger("high")) MI_REG (.D(D_IN), .en(1'b1), .clk(1'b1));  // open: Q, clr
  and WDB (WDB_out, instruction_decoder_1_dbus_cpy, DB_RCTX);
  and OUB (OUB_out, instruction_decoder_1_iob_cpy, or_7_out);
  and INB (INB_out, instruction_decoder_1_iob_cpy, DB_RCTX);
  and STM (STM_out, instruction_decoder_1_memb_cpy, or_7_out);
  and and_6 (and_6_out, instruction_decoder_1_rpc_h, instruction_decoder_1_rpc_l);
  xor xor_1 (xor_1_out, instruction_decoder_1_ld_xf, instruction_decoder_1_ldy);
  xor xor_2 (xor_2_out, instruction_decoder_1_rpc_h, instruction_decoder_1_rpc_l);
  or or_7 (or_7_out, instruction_decoder_1_edat1, DB_WCTX);
  and LDM (LDM_out, instruction_decoder_1_memb_cpy, DB_RCTX);
  or or_8 (or_8_out, xor_2_out, instruction_decoder_1_rread);
  or or_9 (or_9_out, instruction_decoder_1_cclt, or_8_out);
  or or_10 (DB_WCTX, instruction_decoder_1_rhle, or_9_out);
  or or_11 (or_11_out, LDM_out, DB_WCTX);
  or or_12 (or_12_out, INB_out, or_11_out);
  or or_13 (or_13_out, WDB_out, or_12_out);
  or or_14 (or_14_out, instruction_decoder_1_rwrite, instruction_decoder_1_db_irctx);
  or or_15 (or_15_out, and_6_out, or_14_out);
  or or_16 (DB_RCTX, xor_1_out, or_15_out);
  not not_8 (not_8_out, MRW_OUT);
  Pull_Resistor pull_resistor_3 (.node(D_IN));
  assign controlled_buffer_3_out = ADDR_OUT[15] ? ADDR_OUT[14:0] : 15'bz;  // Controlled_Buffer controlled_buffer_3
  Pull_Resistor pull_resistor_4 (.node(pull_resistor_4_node));
  assign pull_resistor_4_node = and_7_out ? MRW_OUT : 1'bz;  // Controlled_Buffer controlled_buffer_4
  not not_9 (not_9_out, ADDR_OUT[15]);
  Pull_Resistor pull_resistor_5 (.node(controlled_buffer_3_out));
  not not_10 (not_10_out, controlled_buffer_3_out[14]);
  Pull_Resistor pull_resistor_6 (.node(pull_resistor_6_node));
  assign pull_resistor_6_node = controlled_buffer_3_out[14] ? MRW_OUT : 1'bz;  // Controlled_Buffer controlled_buffer_5
  ROM #(.addrWidth(15)) rom_1 (.addr(pull_resistor_7_node), .data(rom_1_data));
  Pull_Resistor pull_resistor_7 (.node(pull_resistor_7_node));
  assign pull_resistor_7_node = not_9_out ? ADDR_OUT[14:0] : 15'bz;  // Controlled_Buffer controlled_buffer_6
  and and_7 (and_7_out, ADDR_OUT[15], not_10_out);
  Pull_Resistor pull_resistor_8 (.node(pull_resistor_8_node));
  assign pull_resistor_8_node = and_7_out ? controlled_buffer_3_out[13:0] : 14'bz;  // Controlled_Buffer controlled_buffer_7
  Pull_Resistor pull_resistor_9 (.node(pull_resistor_9_node));
  assign pull_resistor_9_node = controlled_buffer_3_out[14] ? controlled_buffer_3_out[13:0] : 14'bz;  // Controlled_Buffer controlled_buffer_8
  RAM #(.addrWidth(14), .trigger("high")) ram_1 (
    .addr(pull_resistor_8_node), .we(pull_resistor_4_node), .oe(not_8_out), .din(MDAT_OUT), .dout(ram_1_dout));
  RAM #(.addrWidth(14), .trigger("high")) ram_2 (
    .addr(pull_resistor_9_node), .we(pull_resistor_6_node), .oe(not_8_out), .din(MDAT_OUT), .dout(ram_2_dout));
  assign D_IN = not_9_out ? rom_1_data : 8'bz;  // Controlled_Buffer controlled_buffer_9
  assign D_IN = and_7_out ? ram_1_dout : 8'bz;  // Controlled_Buffer controlled_buffer_10
  assign D_IN = controlled_buffer_3_out[14] ? ram_2_dout : 8'bz;  // Controlled_Buffer controlled_buffer_11

  // Notes on the sheet:
  //   contents of rom_1 (hex, n*v repeats v):
  //   8 40 c8 1 51 e9 ff f8 1 0 79 70
endmodule

module Registers (
  input  CLOCK,
  input  Write,
  input  Read,
  input  [2:0] Address,
  input  [7:0] DATA_IN,
  input  RESET,
  input  HLE,
  input  [7:0] FIN,
  input  EFIN,
  output [7:0] DATA_OUT,
  output [15:0] HL_OUT,
  output [7:0] F_OUT
);

  wire and_1_out, and_2_out, and_3_out, and_4_out, and_5_out, and_6_out, and_7_out, and_8_out, and_9_out,
       and_10_out, and_11_out, and_12_out, and_13_out, and_14_out, and_15_out, and_16_out, and_17_out,
       latch_1_dout, latch_2_dout, latch_3_dout, latch_4_dout, latch_5_dout, not_1_out, not_2_out, not_3_out,
       not_4_out, not_5_out, not_6_out, not_7_out, not_8_out, not_9_out, not_10_out, not_11_out, or_1_out;
  wire [7:0] AX_q, BX_q, controlled_buffer_1_out, controlled_buffer_2_out, CX_q, DX_q, EX_q, F_q, H_q, L_q,
       multiplexer_1_out;

  Latch latch_1 (.DOUT(latch_1_dout), .LOCK_E(CLOCK), .DIN(Write));
  Latch latch_2 (.DOUT(latch_2_dout), .LOCK_E(CLOCK), .DIN(Read));
  Latch latch_3 (.DOUT(latch_3_dout), .LOCK_E(CLOCK), .DIN(RESET));
  Latch latch_4 (.DOUT(latch_4_dout), .LOCK_E(CLOCK), .DIN(HLE));
  Latch latch_5 (.DOUT(latch_5_dout), .LOCK_E(CLOCK), .DIN(EFIN));
  and and_1 (and_1_out, latch_1_dout, not_1_out);
  not not_1 (not_1_out, latch_2_dout);
  assign controlled_buffer_1_out = latch_5_dout ? FIN : 8'bz;  // Controlled_Buffer controlled_buffer_1
  not not_2 (not_2_out, Address[2]);
  not not_3 (not_3_out, Address[0]);
  not not_4 (not_4_out, Address[1]);
  not not_5 (not_5_out, Address[1]);
  not not_6 (not_6_out, Address[0]);
  and and_2 (and_2_out, not_3_out, not_4_out, not_2_out);
  and and_3 (and_3_out, Address[0], not_5_out, not_2_out);
  and and_4 (and_4_out, not_6_out, Address[1], not_2_out);
  and and_5 (and_5_out, Address[0], Address[1], not_2_out);
  Register #(.trigger("high")) AX (.D(DATA_IN), .en(and_6_out), .clk(CLOCK), .Q(AX_q), .clr(latch_3_dout));
  and and_6 (and_6_out, and_1_out, and_2_out);
  Register #(.trigger("high")) BX (.D(DATA_IN), .en(and_7_out), .clk(CLOCK), .Q(BX_q), .clr(latch_3_dout));
  and and_7 (and_7_out, and_1_out, and_3_out);
  Register #(.trigger("high")) CX (.D(DATA_IN), .en(and_8_out), .clk(CLOCK), .Q(CX_q), .clr(latch_3_dout));
  and and_8 (and_8_out, and_1_out, and_4_out);
  Register #(.trigger("high")) DX (.D(DATA_IN), .en(and_9_out), .clk(CLOCK), .Q(DX_q), .clr(latch_3_dout));
  and and_9 (and_9_out, and_1_out, and_5_out);
  assign controlled_buffer_2_out = and_2_out ? AX_q : 8'bz;  // Controlled_Buffer controlled_buffer_2
  assign controlled_buffer_2_out = and_3_out ? BX_q : 8'bz;  // Controlled_Buffer controlled_buffer_3
  assign controlled_buffer_2_out = and_4_out ? CX_q : 8'bz;  // Controlled_Buffer controlled_buffer_4
  assign controlled_buffer_2_out = and_5_out ? DX_q : 8'bz;  // Controlled_Buffer controlled_buffer_5
  not not_7 (not_7_out, Address[0]);
  and and_10 (and_10_out, not_7_out, not_8_out, Address[2]);
  not not_8 (not_8_out, Address[1]);
  and and_11 (and_11_out, Address[0], not_9_out, Address[2]);
  not not_9 (not_9_out, Address[1]);
  not not_10 (not_10_out, Address[0]);
  and and_12 (and_12_out, not_10_out, Address[1], Address[2]);
  and and_13 (and_13_out, Address[0], Address[1], Address[2]);
  and and_14 (and_14_out, and_1_out, and_10_out);
  and and_15 (and_15_out, and_1_out, and_11_out);
  and and_16 (and_16_out, and_1_out, and_12_out);
  and and_17 (and_17_out, and_13_out, and_1_out);
  or or_1 (or_1_out, and_17_out, latch_5_dout);
  Register #(.trigger("high")) EX (.D(DATA_IN), .en(and_14_out), .clk(CLOCK), .Q(EX_q), .clr(latch_3_dout));
  Register #(.trigger("high")) L (.D(DATA_IN), .en(and_15_out), .clk(CLOCK), .Q(L_q), .clr(latch_3_dout));
  Register #(.trigger("high")) H (.D(DATA_IN), .en(and_16_out), .clk(CLOCK), .Q(H_q), .clr(latch_3_dout));
  Register #(.trigger("high")) F (.D(multiplexer_1_out), .en(or_1_out), .clk(CLOCK), .Q(F_q), .clr(latch_3_dout));
  Multiplexer #(.enable("true"), .width(8)) multiplexer_1 (
    .in0(controlled_buffer_1_out), .in1(DATA_IN), .out(multiplexer_1_out), .sel(and_17_out), .en(or_1_out));
  assign controlled_buffer_2_out = and_10_out ? EX_q : 8'bz;  // Controlled_Buffer controlled_buffer_6
  assign controlled_buffer_2_out = and_11_out ? L_q : 8'bz;  // Controlled_Buffer controlled_buffer_7
  assign controlled_buffer_2_out = and_12_out ? H_q : 8'bz;  // Controlled_Buffer controlled_buffer_8
  assign F_OUT = not_11_out ? F_q : 8'bz;  // Controlled_Buffer controlled_buffer_9
  assign controlled_buffer_2_out = and_13_out ? F_q : 8'bz;  // Controlled_Buffer controlled_buffer_10
  not not_11 (not_11_out, latch_5_dout);
  assign DATA_OUT = latch_2_dout ? controlled_buffer_2_out : 8'bz;  // Controlled_Buffer controlled_buffer_11
  assign HL_OUT = latch_4_dout ? {H_q, L_q} : 16'bz;  // Controlled_Buffer controlled_buffer_12
endmodule

module ALU (
  input  CLOCK,
  input  CALCULATE,
  input  GET_FLAGS,
  input  LDF,
  input  LDX,
  input  LDY,
  input  [2:0] OPERATION,
  input  [7:0] STATE_IN,
  input  [7:0] DATA_IN,
  input  RESET,
  output [7:0] DATA_OUT,
  output [7:0] FOUT
);

  wire adder_1_cout, and_2_out, and_3_out, and_4_out, and_5_out, and_6_out, and_7_out, and_8_out,
       comparator_2_eq, d_ff_1_q, decoder_1_out0, decoder_1_out1, decoder_1_out2, decoder_1_out3,
       decoder_1_out4, decoder_1_out5, decoder_1_out6, latch_1_dout, latch_2_dout, latch_3_dout,
       latch_4_dout, latch_5_dout, latch_6_dout, not_2_out, not_3_out, not_4_out, or_2_out, subtractor_1_bout;
  wire [5:0] or_3_out;
  wire [7:0] adder_1_out, and_1_out, controlled_buffer_1_out, not_1_out, or_1_out, register_1_q,
       register_2_q, register_3_q, subtractor_1_out;

  Latch latch_1 (.DOUT(latch_1_dout), .LOCK_E(CLOCK), .DIN(CALCULATE));
  Latch latch_2 (.DOUT(latch_2_dout), .LOCK_E(CLOCK), .DIN(GET_FLAGS));
  Latch latch_3 (.DOUT(latch_3_dout), .LOCK_E(CLOCK), .DIN(LDF));
  Latch latch_4 (.DOUT(latch_4_dout), .LOCK_E(CLOCK), .DIN(LDX));
  Latch latch_5 (.DOUT(latch_5_dout), .LOCK_E(CLOCK), .DIN(LDY));
  Latch latch_6 (.DOUT(latch_6_dout), .LOCK_E(CLOCK), .DIN(RESET));
  Register #(.trigger("high")) register_1 (
    .D(STATE_IN), .en(latch_3_dout), .clk(CLOCK), .Q(register_1_q), .clr(latch_6_dout));
  Register #(.trigger("high")) register_2 (
    .D(DATA_IN), .en(latch_4_dout), .clk(CLOCK), .Q(register_2_q), .clr(latch_6_dout));
  Register #(.trigger("high")) register_3 (
    .D(DATA_IN), .en(latch_5_dout), .clk(CLOCK), .Q(register_3_q), .clr(latch_6_dout));
  Decoder #(.select(3)) decoder_1 (
    .out0(decoder_1_out0), .out1(decoder_1_out1), .out2(decoder_1_out2), .out3(decoder_1_out3),
    .out4(decoder_1_out4), .out5(decoder_1_out5), .out6(decoder_1_out6), .sel(OPERATION), .en(1'b1));  // open: out7
  assign and_1_out = register_2_q & register_3_q;  // AND_Gate and_1, 8 bits wide
  assign or_1_out = register_2_q | register_3_q;  // OR_Gate or_1, 8 bits wide
  assign not_1_out = ~register_2_q;  // NOT_Gate not_1, 8 bits wide
  Subtractor subtractor_1 (
    .a(register_2_q), .b(register_3_q), .out(subtractor_1_out), .bin(register_1_q[0]),
    .bout(subtractor_1_bout));
  and and_2 (and_2_out, register_1_q[1], decoder_1_out3);
  or or_2 (or_2_out, decoder_1_out3, decoder_1_out4);
  Adder adder_1 (.a(register_2_q), .b(register_3_q), .out(adder_1_out), .cin(and_2_out), .cout(adder_1_cout));
  Comparator comparator_1 (.a(register_2_q), .b(register_3_q), .gt(or_3_out[4]), .eq(or_3_out[2]), .lt(or_3_out[3]));
  assign controlled_buffer_1_out = decoder_1_out0 ? and_1_out : 8'bz;  // Controlled_Buffer controlled_buffer_1
  assign controlled_buffer_1_out = decoder_1_out1 ? or_1_out : 8'bz;  // Controlled_Buffer controlled_buffer_2
  assign controlled_buffer_1_out = decoder_1_out2 ? not_1_out : 8'bz;  // Controlled_Buffer controlled_buffer_3
  assign controlled_buffer_1_out = decoder_1_out5 ? subtractor_1_out : 8'bz;  // Controlled_Buffer controlled_buffer_4
  and and_3 (and_3_out, decoder_1_out5, subtractor_1_bout);
  not not_2 (not_2_out, decoder_1_out5);
  and and_4 (and_4_out, not_2_out, register_1_q[0]);
  assign controlled_buffer_1_out = or_2_out ? adder_1_out : 8'bz;  // Controlled_Buffer controlled_buffer_5
  and and_5 (and_5_out, or_2_out, adder_1_cout);
  not not_3 (not_3_out, or_2_out);
  and and_6 (and_6_out, not_3_out, register_1_q[1]);
  assign DATA_OUT = latch_1_dout ? controlled_buffer_1_out : 8'bz;  // Controlled_Buffer controlled_buffer_6
  or or_3 (or_3_out[0], and_3_out, and_4_out);
  or or_4 (or_3_out[1], and_5_out, and_6_out);
  Comparator comparator_2 (.a(controlled_buffer_1_out), .b({8{1'b0}}), .eq(comparator_2_eq));  // open: gt, lt
  and and_7 (and_7_out, d_ff_1_q, not_4_out);
  not not_4 (not_4_out, decoder_1_out6);
  D_Flip_Flop d_ff_1 (.clk(latch_1_dout), .D(comparator_2_eq), .Q(d_ff_1_q), .preset(1'b0), .reset(1'b0));  // open: Qn
  Register #(.trigger("high")) RES (.D(controlled_buffer_1_out), .en(1'b1), .clk(1'b1));  // open: Q, clr
  assign FOUT = latch_2_dout ? {2'b00, or_3_out} : 8'bz;  // Controlled_Buffer controlled_buffer_7
  or or_5 (or_3_out[5], and_7_out, and_8_out);
  and and_8 (and_8_out, register_1_q[5], decoder_1_out6);
  Register #(.trigger("high")) FOUT_REG (.D({2'b00, or_3_out}), .en(1'b1), .clk(1'b1));  // open: Q, clr
endmodule

module Instruction_Decoder (
  input  CLOCK,
  input  [7:0] Instruction_IN,
  input  EXECUTE,
  input  RESET_DECODER,
  input  IRQ,
  input  NMI,
  input  RESET_CPU,
  input  [7:0] ADD_8,
  output CBUFF,
  output RREAD,
  output RWRITE,
  output MDSpec,
  output EDAT1,
  output EDAT2,
  output IR_QT,
  output DBUS_CPY,
  output ID_SP,
  output ID_PC,
  output SPM_E,
  output PCM_E,
  output LD_XF,
  output LC_PC,
  output LDY,
  output RPC_H,
  output CCLT,
  output RPC_L,
  output FLAGS_E,
  output RHLE,
  output IOB_CPY,
  output MEMB_CPY,
  output C_IRQ,
  output C_NMI,
  output C_RST,
  output DB_IRCTX,
  output [15:0] ADD_16
);

  wire and_1_out, and_2_out, and_3_out, and_4_out, and_5_out, and_6_out, and_7_out, and_8_out, and_9_out,
       and_10_out, and_11_out, and_12_out, and_20_out, and_21_out, and_22_out, d_ff_1_q, d_ff_2_q, d_ff_2_qn,
       d_ff_3_q, latch_1_dout, latch_2_dout, latch_3_dout, latch_4_dout, latch_5_dout, nor_1_out, not_1_out,
       not_3_out, not_4_out, not_5_out, not_6_out, not_7_out, not_8_out, not_9_out, or_1_out, or_2_out,
       or_3_out, or_4_out;
  wire [2:0] counter_1_q;
  wire [6:4] pull_resistor_3_node, pull_resistor_4_node;
  wire [7:0] H_q, L_q;
  wire [15:0] IRQ_ROM_data, NMI_ROM_data, pull_resistor_2_node, rom_1_data, RST_ROM_data;
  wire [15:8] pull_resistor_1_node;
  wire [15:15] not_2_out;

  Latch latch_1 (.DOUT(latch_1_dout), .LOCK_E(CLOCK), .DIN(EXECUTE));
  Latch latch_2 (.DOUT(latch_2_dout), .LOCK_E(CLOCK), .DIN(RESET_DECODER));
  Latch latch_3 (.DOUT(latch_3_dout), .LOCK_E(CLOCK), .DIN(IRQ));
  Latch latch_4 (.DOUT(latch_4_dout), .LOCK_E(CLOCK), .DIN(NMI));
  Latch latch_5 (.DOUT(latch_5_dout), .LOCK_E(CLOCK), .DIN(RESET_CPU));
  Register #(.trigger("high")) register_1 (.D(Instruction_IN), .en(1'b1), .clk(1'b1));  // open: Q, clr
  not not_1 (not_1_out, CLOCK);
  and and_1 (and_1_out, DB_IRCTX, CLOCK, d_ff_2_q);
  and and_2 (and_2_out, d_ff_2_qn, CLOCK, DB_IRCTX);
  nor nor_1 (nor_1_out, latch_3_dout, latch_4_dout, latch_5_dout);
  not not_2 (not_2_out[15], latch_1_dout);
  Register #(.trigger("high")) H (.D(ADD_8), .en(and_1_out), .clk(1'b1), .Q(H_q), .clr(or_1_out));
  or or_1 (or_1_out, latch_2_dout, d_ff_1_q);
  not not_3 (not_3_out, CLOCK);
  and and_3 (and_3_out, not_3_out, d_ff_1_q);
  D_Flip_Flop d_ff_1 (.Q(d_ff_1_q), .preset(and_2_out), .reset(d_ff_2_q));  // open: clk, D, Qn
  Register #(.trigger("high")) L (.D(ADD_8), .en(and_2_out), .clk(1'b1), .Q(L_q), .clr(latch_2_dout));
  Counter #(.max('h7), .width(3)) counter_1 (
    .load(1'b0), .count(latch_1_dout), .Q(counter_1_q), .up(1'b1), .clk(not_1_out), .clr(latch_2_dout));  // open: D, carry
  and and_4 (and_4_out, latch_1_dout, nor_1_out);
  and and_5 (and_5_out, latch_1_dout, not_4_out);
  not not_4 (not_4_out, nor_1_out);
  D_Flip_Flop d_ff_2 (.Q(d_ff_2_q), .Qn(d_ff_2_qn), .preset(and_3_out), .reset(or_2_out));  // open: clk, D
  or or_2 (or_2_out, and_6_out, latch_2_dout);
  ROM #(.dataWidth(16)) rom_1 (.addr({Instruction_IN[7:3], counter_1_q}), .data(rom_1_data));
  D_Flip_Flop d_ff_3 (.Q(d_ff_3_q), .preset(and_1_out), .reset(d_ff_2_qn));  // open: clk, D, Qn
  not not_5 (not_5_out, CLOCK);
  and and_6 (and_6_out, d_ff_3_q, not_5_out);
  ROM #(.addrWidth(3), .dataWidth(16)) IRQ_ROM (.addr(counter_1_q), .data(IRQ_ROM_data));
  ROM #(.addrWidth(3), .dataWidth(16)) NMI_ROM (.addr(counter_1_q), .data(NMI_ROM_data));
  ROM #(.addrWidth(3), .dataWidth(16)) RST_ROM (.addr(counter_1_q), .data(RST_ROM_data));
  assign ADD_16 = and_7_out ? 16'hfffa : 16'bz;  // Controlled_Buffer controlled_buffer_1
  assign ADD_16 = and_8_out ? 16'hfffb : 16'bz;  // Controlled_Buffer controlled_buffer_2
  assign ADD_16 = and_9_out ? 16'hfffc : 16'bz;  // Controlled_Buffer controlled_buffer_3
  assign ADD_16 = and_10_out ? 16'hfffd : 16'bz;  // Controlled_Buffer controlled_buffer_4
  assign ADD_16 = and_11_out ? 16'hfffe : 16'bz;  // Controlled_Buffer controlled_buffer_5
  assign ADD_16 = and_12_out ? {16{1'b1}} : 16'bz;  // Controlled_Buffer controlled_buffer_6
  assign ADD_16 = or_3_out ? {H_q, L_q} : 16'bz;  // Controlled_Buffer controlled_buffer_7
  Pull_Resistor pull_resistor_1 (.node({pull_resistor_1_node, DBUS_CPY, IR_QT, EDAT2, EDAT1, MDSpec, RWRITE, RREAD, CBUFF}));
  assign {pull_resistor_1_node, DBUS_CPY, IR_QT, EDAT2, EDAT1, MDSpec, RWRITE, RREAD, CBUFF} = and_4_out ? rom_1_data : 16'bz;  // Controlled_Buffer controlled_buffer_8
  assign {pull_resistor_1_node, DBUS_CPY, IR_QT, EDAT2, EDAT1, MDSpec, RWRITE, RREAD, CBUFF} = and_5_out ? {pull_resistor_2_node[15:8], 4'b0000, pull_resistor_2_node[3:0]} : 16'bz;  // Controlled_Buffer controlled_buffer_9
  Hex_Digit_Display hex_digit_display_1 (.value(pull_resistor_1_node[15:12]));  // open: dp
  and and_7 (and_7_out, not_7_out, pull_resistor_2_node[4]);
  and and_8 (and_8_out, not_7_out, pull_resistor_2_node[5]);
  and and_9 (and_9_out, not_8_out, pull_resistor_3_node[4]);
  and and_10 (and_10_out, not_8_out, pull_resistor_3_node[5]);
  and and_11 (and_11_out, not_9_out, pull_resistor_4_node[4]);
  and and_12 (and_12_out, not_9_out, pull_resistor_4_node[5]);
  Hex_Digit_Display hex_digit_display_2 (.value(pull_resistor_1_node[11:8]));  // open: dp
  Hex_Digit_Display hex_digit_display_3 (.value({DBUS_CPY, IR_QT, EDAT2, EDAT1}));  // open: dp
  not not_6 (not_6_out, pull_resistor_1_node[8]);
  and and_13 (ID_SP, not_6_out, pull_resistor_1_node[9]);
  and and_14 (SPM_E, not_6_out, pull_resistor_1_node[10]);
  and and_15 (LD_XF, not_6_out, pull_resistor_1_node[11]);
  and and_16 (LDY, not_6_out, pull_resistor_1_node[12]);
  and and_17 (CCLT, not_6_out, pull_resistor_1_node[13]);
  and and_18 (FLAGS_E, not_6_out, pull_resistor_1_node[14]);
  and and_19 (IOB_CPY, not_6_out, pull_resistor_1_node[15]);
  Pull_Resistor pull_resistor_2 (.node({pull_resistor_2_node[15:8], C_IRQ, pull_resistor_2_node[6:0]}));
  assign {pull_resistor_2_node[15:8], C_IRQ, pull_resistor_2_node[6:0]} = latch_3_dout ? IRQ_ROM_data : 16'bz;  // Controlled_Buffer controlled_buffer_10
  Pull_Resistor pull_resistor_3 (.node({pull_resistor_2_node[15:8], C_NMI, pull_resistor_3_node, pull_resistor_2_node[3:0]}));
  assign {pull_resistor_2_node[15:8], C_NMI, pull_resistor_3_node, pull_resistor_2_node[3:0]} = latch_4_dout ? NMI_ROM_data : 16'bz;  // Controlled_Buffer controlled_buffer_11
  Pull_Resistor pull_resistor_4 (.node({pull_resistor_2_node[15:8], C_RST, pull_resistor_4_node, pull_resistor_2_node[3:0]}));
  assign {pull_resistor_2_node[15:8], C_RST, pull_resistor_4_node, pull_resistor_2_node[3:0]} = latch_5_dout ? RST_ROM_data : 16'bz;  // Controlled_Buffer controlled_buffer_12
  Hex_Digit_Display hex_digit_display_4 (.value({MDSpec, RWRITE, RREAD, CBUFF}));  // open: dp
  not not_7 (not_7_out, and_20_out);
  and and_20 (and_20_out, pull_resistor_2_node[4], pull_resistor_2_node[5]);
  not not_8 (not_8_out, and_21_out);
  and and_21 (and_21_out, pull_resistor_3_node[4], pull_resistor_3_node[5]);
  not not_9 (not_9_out, and_22_out);
  and and_22 (and_22_out, pull_resistor_4_node[4], pull_resistor_4_node[5]);
  or or_3 (or_3_out, and_20_out, and_21_out, and_22_out);
  or or_4 (or_4_out, pull_resistor_3_node[6], pull_resistor_2_node[6]);
  or or_5 (DB_IRCTX, pull_resistor_4_node[6], or_4_out);
  assign {pull_resistor_1_node, DBUS_CPY, IR_QT, EDAT2, EDAT1, MDSpec, RWRITE, RREAD, CBUFF} = not_2_out[15] ? {not_2_out[15], 1'b0, {2{not_2_out[15]}}, 1'b0, {3{not_2_out[15]}}, 4'b0000, not_2_out[15], 3'b000} : 16'bz;  // Controlled_Buffer controlled_buffer_13
  and and_23 (ID_PC, pull_resistor_1_node[8], pull_resistor_1_node[9]);
  and and_24 (PCM_E, pull_resistor_1_node[8], pull_resistor_1_node[10]);
  and and_25 (LC_PC, pull_resistor_1_node[8], pull_resistor_1_node[11]);
  and and_26 (RPC_H, pull_resistor_1_node[8], pull_resistor_1_node[12]);
  and and_27 (RPC_L, pull_resistor_1_node[8], pull_resistor_1_node[13]);
  and and_28 (RHLE, pull_resistor_1_node[8], pull_resistor_1_node[14]);
  and and_29 (MEMB_CPY, pull_resistor_1_node[8], pull_resistor_1_node[15]);
  PLA pla_1 ();  // open: in, out

  // Notes on the sheet:
  //   For the sake of logsim, an easier representation will be built.
  //   A PLA (Programmable Logic Array) can also be used.
  //   The same can however be achieved with the diagram show under the main one. (suppressed)
  //   contents of rom_1 (hex, n*v repeats v):
  //   8*0 1 7*0 c10d 7*0 812d 7*0 92 85 6*0 15 7*0 c10b 7*0 812b 7*0 8102 601 6*0 8110 601 6*0 400 8105
  //   14*0 8005 7*0 8003 7*0 49 7*0 41 7*0 802 1012 6005 5*0 802 1010 6005 5*0 802 1012 6005 5*0 802 1010
  //   6005 5*0 812 6005 6*0 810 6005 6*0 802 1012 6005 5*0 802 1010 6005 5*0 802 1012 6005 5*0 802 1010
  //   6005 5*0 802 1012 6005 5*0 802 1010 6005 5*0 802 1012 4001 5*0 802 1010 4001 5*0 4901 7*0 921
  //   contents of IRQ_ROM (hex, n*v repeats v):
  //   9100 600 a100 600 8158 8168 9b0
  //   contents of NMI_ROM (hex, n*v repeats v):
  //   9100 600 a100 600 8158 8168 9b0
  //   contents of RST_ROM (hex, n*v repeats v):
  //   8158 8168 9b0
endmodule
module Instruction_Buffer (
  input  CLOCK,
  input  MBUS_OE,
  input  STB_BUFF,
  input  [7:0] DAT,
  input  CLEAR_BUFF,
  input  ARG1_E,
  input  ARG2_E,
  input  S_IRQ,
  input  IRQ,
  input  C_IRQ,
  input  NMI,
  input  C_NMI,
  input  RST,
  input  C_RST,
  input  DBO_TRUE,
  output [7:0] MBUS_DOUT,
  output [7:0] INSTRUCTION,
  output [7:0] ARG_8BIT,
  output [15:0] ARG_16BIT,
  output [2:0] REG_ADD,
  output [2:0] ALU_OPC,
  output INT_VAL,
  output RDY,
  output BUFF_FULL,
  output ERR,
  output RST_T,
  output IRQ_T,
  output NMI_T,
  output UNUSED
);

  wire and_1_out, and_2_out, and_3_out, and_4_out, and_5_out, and_6_out, and_7_out, and_8_out, and_9_out,
       and_10_out, and_11_out, and_12_out, and_13_out, and_14_out, and_15_out, and_16_out, and_17_out,
       and_18_out, and_19_out, and_20_out, and_21_out, and_22_out, and_23_out, and_24_out, and_25_out,
       and_26_out, and_27_out, and_28_out, and_29_out, and_30_out, and_31_out, and_32_out, and_33_out,
       and_34_out, and_35_out, and_36_out, and_37_out, and_38_out, and_39_out, and_40_out, and_41_out,
       and_42_out, and_43_out, and_44_out, and_45_out, and_46_out, and_48_out, and_49_out, and_50_out,
       and_51_out, and_52_out, and_53_out, and_54_out, and_55_out, and_56_out, and_57_out, and_58_out,
       and_59_out, and_60_out, and_61_out, and_62_out, and_63_out, and_64_out, and_65_out, and_66_out,
       and_67_out, and_68_out, and_69_out, and_70_out, and_71_out, and_72_out, and_73_out, and_74_out,
       and_75_out, and_76_out, and_77_out, and_78_out, and_79_out, and_80_out, and_81_out, and_82_out,
       and_83_out, and_84_out, and_85_out, and_86_out, and_87_out, and_88_out, and_89_out, and_90_out,
       and_91_out, and_92_out, and_93_out, and_94_out, and_95_out, and_96_out, and_97_out, and_98_out,
       and_99_out, and_100_out, and_101_out, and_102_out, and_103_out, and_104_out, and_105_out, and_106_out,
       and_107_out, and_108_out, and_109_out, and_111_out, and_112_out, and_113_out, ARGC_1, ARGC_1t, ARGC_2,
       ARGC_2t, ARGC_3, ARGC_3t, d_ff_1_q, d_ff_1_qn, d_ff_2_q, d_ff_2_qn, d_ff_3_q, d_ff_4_q, d_ff_5_q,
       d_ff_6_q, d_ff_7_q, d_ff_7_qn, d_ff_8_q, decoder_1_out0, decoder_1_out1, decoder_1_out2,
       decoder_1_out3, decoder_1_out4, decoder_1_out5, decoder_1_out6, decoder_1_out7, decoder_2_out0,
       decoder_2_out1, decoder_2_out2, decoder_2_out3, decoder_2_out4, decoder_2_out5, decoder_2_out6,
       decoder_2_out7, decoder_3_out0, decoder_3_out1, decoder_3_out2, decoder_3_out3, decoder_3_out4,
       decoder_3_out5, decoder_3_out6, decoder_3_out7, decoder_4_out0, decoder_4_out1, decoder_4_out2,
       decoder_4_out3, decoder_4_out4, decoder_4_out5, decoder_4_out6, decoder_4_out7, decoder_5_out0,
       decoder_5_out1, decoder_5_out2, decoder_5_out3, decoder_5_out4, decoder_5_out5, decoder_5_out6,
       decoder_5_out7, decoder_6_out0, decoder_6_out1, decoder_6_out2, decoder_6_out3, decoder_6_out4,
       decoder_6_out5, decoder_6_out6, decoder_6_out7, decoder_7_out0, decoder_7_out1, decoder_7_out2,
       decoder_7_out3, decoder_7_out4, decoder_7_out5, decoder_7_out6, decoder_7_out7, decoder_8_out0,
       decoder_8_out1, decoder_8_out2, decoder_8_out3, decoder_8_out4, decoder_8_out5, decoder_8_out6,
       decoder_8_out7, decoder_9_out0, decoder_9_out1, decoder_9_out2, decoder_9_out3, decoder_9_out4,
       decoder_9_out5, decoder_9_out6, decoder_9_out7, decoder_10_out0, decoder_10_out1, decoder_10_out2,
       decoder_10_out3, decoder_10_out4, decoder_10_out5, decoder_10_out6, decoder_10_out7, decoder_11_out0,
       decoder_11_out1, decoder_11_out2, decoder_11_out3, decoder_11_out4, decoder_11_out5, decoder_11_out6,
       decoder_11_out7, decoder_12_out0, decoder_12_out1, decoder_12_out2, decoder_12_out3, decoder_12_out4,
       decoder_12_out5, decoder_12_out6, decoder_12_out7, decoder_13_out0, decoder_13_out1, decoder_13_out2,
       decoder_13_out3, decoder_13_out4, decoder_13_out5, decoder_13_out6, decoder_13_out7, decoder_14_out0,
       decoder_14_out1, decoder_14_out2, decoder_14_out3, decoder_14_out4, decoder_14_out5, decoder_14_out6,
       decoder_14_out7, decoder_15_out0, decoder_15_out1, decoder_15_out2, decoder_15_out3, decoder_15_out4,
       decoder_15_out5, decoder_15_out6, decoder_15_out7, decoder_16_out0, decoder_16_out1, decoder_16_out2,
       decoder_16_out3, decoder_16_out4, decoder_16_out5, decoder_16_out6, decoder_16_out7, decoder_17_out0,
       decoder_17_out1, decoder_17_out2, decoder_17_out3, decoder_17_out4, decoder_17_out5, decoder_17_out6,
       decoder_17_out7, decoder_18_out0, decoder_18_out1, decoder_18_out2, decoder_18_out3, decoder_19_out0,
       decoder_19_out1, decoder_19_out2, decoder_19_out3, decoder_20_out0, decoder_20_out1, decoder_20_out2,
       decoder_20_out3, decoder_21_out0, decoder_21_out1, decoder_21_out2, decoder_21_out3, decoder_22_out0,
       decoder_22_out1, decoder_22_out2, decoder_22_out3, decoder_23_out0, decoder_23_out1, decoder_23_out2,
       decoder_23_out3, decoder_24_out0, decoder_24_out1, decoder_24_out2, decoder_24_out3, decoder_25_out0,
       decoder_25_out1, decoder_25_out2, decoder_25_out3, decoder_26_out0, decoder_26_out1, decoder_26_out2,
       decoder_26_out3, decoder_27_out0, decoder_27_out1, decoder_27_out2, decoder_27_out3, decoder_28_out0,
       decoder_28_out1, decoder_28_out2, decoder_28_out3, decoder_29_out0, decoder_29_out1, decoder_29_out2,
       decoder_29_out3, decoder_30_out0, decoder_30_out1, decoder_30_out2, decoder_30_out3, decoder_31_out0,
       decoder_31_out1, decoder_31_out2, decoder_31_out3, decoder_32_out0, decoder_32_out1, decoder_32_out2,
       decoder_32_out3, ILLEGALt, latch_1_dout, latch_2_dout, latch_3_dout, n7404_16_pin9, n7404_16_pin11,
       nand_1_out, nand_2_out, nand_3_out, nand_4_out, nand_5_out, nand_6_out, nand_7_out, nand_8_out,
       nand_9_out, nand_10_out, nand_11_out, nand_12_out, nand_13_out, nand_14_out, nand_15_out, nand_18_out,
       nand_19_out, nand_22_out, nand_23_out, nand_24_out, nand_25_out, nand_28_out, nand_29_out,
       nand_30_out, nand_31_out, nand_32_out, nand_33_out, nand_34_out, nand_35_out, nand_36_out,
       nand_37_out, nand_38_out, nand_39_out, nand_41_out, nand_42_out, nor_1_out, nor_2_out, nor_3_out,
       nor_4_out, nor_5_out, nor_7_out, nor_10_out, nor_11_out, nor_12_out, nor_13_out, nor_14_out,
       nor_15_out, nor_18_out, nor_19_out, nor_20_out, nor_21_out, nor_23_out, nor_24_out, nor_25_out,
       nor_26_out, nor_28_out, nor_30_out, nor_31_out, nor_32_out, nor_33_out, nor_36_out, nor_37_out,
       nor_38_out, nor_39_out, nor_40_out, nor_44_out, nor_45_out, nor_46_out, nor_47_out, nor_48_out,
       nor_49_out, nor_50_out, nor_51_out, nor_52_out, nor_53_out, nor_55_out, nor_56_out, nor_57_out,
       nor_58_out, nor_59_out, nor_60_out, nor_61_out, nor_62_out, nor_63_out, nor_64_out, nor_65_out,
       nor_66_out, nor_67_out, nor_72_out, nor_73_out, nor_74_out, nor_75_out, nor_76_out, nor_77_out,
       nor_78_out, nor_79_out, nor_83_out, not_1_out, not_2_out, not_3_out, not_4_out, not_5_out, not_6_out,
       not_7_out, not_8_out, not_9_out, not_10_out, not_11_out, not_12_out, not_13_out, not_14_out,
       not_15_out, not_16_out, not_17_out, not_18_out, not_19_out, not_20_out, not_21_out, not_22_out,
       not_23_out, not_24_out, not_25_out, not_26_out, not_27_out, not_28_out, not_29_out, not_30_out,
       not_31_out, not_32_out, not_33_out, not_34_out, not_35_out, not_36_out, not_37_out, not_38_out,
       not_39_out, not_40_out, not_41_out, not_42_out, not_43_out, not_44_out, not_45_out, not_46_out,
       not_47_out, not_48_out, not_49_out, not_50_out, not_51_out, not_52_out, not_53_out, not_55_out,
       not_56_out, not_57_out, not_58_out, not_59_out, not_60_out, not_62_out, not_63_out, not_64_out,
       not_65_out, not_66_out, not_67_out, not_68_out, not_70_out, not_71_out, not_72_out, not_73_out,
       not_74_out, not_75_out, not_76_out, not_77_out, not_78_out, not_79_out, not_80_out, not_81_out,
       not_82_out, not_83_out, not_84_out, not_85_out, not_86_out, not_87_out, not_88_out, not_89_out,
       not_90_out, not_91_out, not_92_out, not_93_out, not_94_out, not_95_out, not_96_out, not_98_out,
       not_99_out, not_100_out, not_101_out, not_102_out, not_103_out, not_104_out, not_105_out, not_106_out,
       not_107_out, not_108_out, not_109_out, not_110_out, not_111_out, not_112_out, not_113_out,
       not_114_out, not_116_out, not_119_out, not_121_out, not_122_out, not_124_out, not_125_out,
       not_128_out, not_130_out, not_132_out, not_133_out, not_137_out, not_138_out, not_139_out,
       not_140_out, not_141_out, not_142_out, not_143_out, not_145_out, not_146_out, not_147_out,
       not_148_out, not_150_out, not_151_out, not_153_out, not_154_out, not_155_out, not_157_out,
       not_158_out, not_160_out, not_161_out, not_164_out, not_165_out, not_166_out, not_167_out,
       not_168_out, not_169_out, not_170_out, not_171_out, not_172_out, not_173_out, not_174_out,
       not_175_out, not_176_out, not_177_out, not_178_out, not_179_out, not_180_out, not_181_out,
       not_182_out, not_183_out, not_184_out, not_185_out, not_186_out, not_187_out, not_188_out,
       not_189_out, not_190_out, not_191_out, not_192_out, not_193_out, not_194_out, not_195_out,
       not_196_out, not_197_out, not_198_out, not_199_out, not_200_out, not_201_out, not_202_out,
       not_203_out, not_204_out, not_205_out, not_206_out, not_207_out, not_208_out, not_209_out,
       not_210_out, not_211_out, not_212_out, not_213_out, not_214_out, not_215_out, not_216_out,
       not_217_out, not_218_out, not_219_out, not_220_out, not_221_out, not_222_out, not_223_out,
       not_224_out, not_225_out, not_226_out, not_227_out, not_228_out, not_229_out, not_230_out,
       not_231_out, not_232_out, not_233_out, not_234_out, not_235_out, not_238_out, not_239_out,
       not_240_out, not_243_out, not_244_out, not_247_out, not_248_out, not_249_out, not_250_out,
       not_251_out, not_252_out, not_253_out, not_254_out, not_255_out, not_256_out, not_257_out,
       not_258_out, not_259_out, not_260_out, not_261_out, not_262_out, not_263_out, not_264_out,
       not_265_out, not_266_out, not_267_out, not_268_out, not_269_out, not_270_out, not_271_out,
       not_272_out, not_273_out, not_274_out, not_275_out, not_276_out, not_277_out, not_278_out,
       not_279_out, not_280_out, not_281_out, not_282_out, not_283_out, not_284_out, not_285_out,
       not_286_out, not_287_out, not_288_out, not_289_out, not_290_out, not_291_out, not_292_out,
       not_293_out, not_294_out, not_295_out, not_296_out, not_297_out, not_298_out, not_299_out,
       not_300_out, not_301_out, not_302_out, not_303_out, not_304_out, not_305_out, not_306_out,
       not_307_out, not_308_out, not_309_out, not_310_out, not_311_out, not_312_out, not_313_out,
       not_314_out, not_315_out, not_316_out, not_317_out, not_318_out, not_319_out, not_320_out,
       not_321_out, not_322_out, not_323_out, not_324_out, not_325_out, or_1_out, or_2_out, or_3_out,
       or_4_out, or_5_out, or_6_out, or_8_out, or_9_out, or_10_out, or_11_out, or_12_out, or_13_out,
       or_14_out, or_15_out, or_16_out, or_17_out, or_21_out, or_29_out, or_30_out, or_31_out, or_32_out,
       or_33_out, or_34_out, or_35_out, or_36_out, or_37_out, or_38_out, or_39_out, or_40_out, or_41_out,
       or_42_out, or_43_out, or_44_out, or_45_out, or_46_out, or_47_out, or_48_out, or_49_out, or_51_out,
       or_52_out, or_53_out, or_54_out, or_55_out, or_56_out, or_57_out, or_58_out, or_59_out, or_60_out,
       or_61_out, or_62_out, or_63_out, or_64_out, or_65_out, or_66_out, or_67_out, or_68_out, or_69_out,
       or_70_out, or_71_out, or_72_out, or_73_out, or_74_out, or_75_out, or_76_out, or_77_out, or_78_out,
       or_79_out, or_80_out, or_81_out, or_85_out, or_86_out, or_87_out, or_88_out, or_89_out, or_90_out,
       or_91_out, or_92_out, or_93_out, or_96_out, or_97_out, or_98_out, or_99_out, or_100_out, or_101_out,
       or_102_out, or_106_out, or_107_out, or_108_out, or_110_out, or_111_out, undriven, undriven_2, UNUSEDt;
  wire [0:0] nor_6_out, nor_8_out, nor_9_out, or_18_out, or_19_out, or_28_out;
  wire [1:0] counter_1_q;
  wire [1:1] or_7_out, or_20_out, or_22_out, or_23_out, or_24_out, or_25_out, or_26_out, or_27_out;
  wire [7:0] register_2_q, register_3_q;

  _74377 u_74377_1 ();  // open: pin1, pin2, pin3, pin4, pin5, pin6, pin7, pin8, pin9, pin19, pin18, pin17, pin16, pin15, pin14, pin13, pin12, pin11
  _74377 u_74377_2 ();  // open: pin1, pin2, pin3, pin4, pin5, pin6, pin7, pin8, pin9, pin19, pin18, pin17, pin16, pin15, pin14, pin13, pin12, pin11
  _74377 u_74377_3 ();  // open: pin1, pin2, pin3, pin4, pin5, pin6, pin7, pin8, pin9, pin19, pin18, pin17, pin16, pin15, pin14, pin13, pin12, pin11
  _74377 u_74377_4 ();  // open: pin1, pin2, pin3, pin4, pin5, pin6, pin7, pin8, pin9, pin19, pin18, pin17, pin16, pin15, pin14, pin13, pin12, pin11
  _74377 u_74377_5 ();  // open: pin1, pin2, pin3, pin4, pin5, pin6, pin7, pin8, pin9, pin19, pin18, pin17, pin16, pin15, pin14, pin13, pin12, pin11
  _74377 u_74377_6 ();  // open: pin1, pin2, pin3, pin4, pin5, pin6, pin7, pin8, pin9, pin19, pin18, pin17, pin16, pin15, pin14, pin13, pin12, pin11
  _74377 u_74377_7 ();  // open: pin1, pin2, pin3, pin4, pin5, pin6, pin7, pin8, pin9, pin19, pin18, pin17, pin16, pin15, pin14, pin13, pin12, pin11
  _74377 u_74377_8 ();  // open: pin1, pin2, pin3, pin4, pin5, pin6, pin7, pin8, pin9, pin19, pin18, pin17, pin16, pin15, pin14, pin13, pin12, pin11
  _74377 u_74377_9 ();  // open: pin1, pin2, pin3, pin4, pin5, pin6, pin7, pin8, pin9, pin19, pin18, pin17, pin16, pin15, pin14, pin13, pin12, pin11
  _74377 u_74377_10 ();  // open: pin1, pin2, pin3, pin4, pin5, pin6, pin7, pin8, pin9, pin19, pin18, pin17, pin16, pin15, pin14, pin13, pin12, pin11
  _74377 u_74377_11 ();  // open: pin1, pin2, pin3, pin4, pin5, pin6, pin7, pin8, pin9, pin19, pin18, pin17, pin16, pin15, pin14, pin13, pin12, pin11
  _74377 u_74377_12 ();  // open: pin1, pin2, pin3, pin4, pin5, pin6, pin7, pin8, pin9, pin19, pin18, pin17, pin16, pin15, pin14, pin13, pin12, pin11
  _74377 u_74377_13 ();  // open: pin1, pin2, pin3, pin4, pin5, pin6, pin7, pin8, pin9, pin19, pin18, pin17, pin16, pin15, pin14, pin13, pin12, pin11
  _74377 u_74377_14 ();  // open: pin1, pin2, pin3, pin4, pin5, pin6, pin7, pin8, pin9, pin19, pin18, pin17, pin16, pin15, pin14, pin13, pin12, pin11
  _74377 u_74377_15 ();  // open: pin1, pin2, pin3, pin4, pin5, pin6, pin7, pin8, pin9, pin19, pin18, pin17, pin16, pin15, pin14, pin13, pin12, pin11
  _74377 u_74377_16 ();  // open: pin1, pin2, pin3, pin4, pin5, pin6, pin7, pin8, pin9, pin19, pin18, pin17, pin16, pin15, pin14, pin13, pin12, pin11
  not not_1 (not_1_out, ALU_OPC[2]);
  or or_1 (or_1_out, INSTRUCTION[0], INSTRUCTION[1]);
  or or_2 (or_2_out, ALU_OPC[0], ALU_OPC[1]);
  or or_3 (or_3_out, or_2_out, ALU_OPC[2]);
  or or_4 (or_4_out, or_3_out, INSTRUCTION[3]);
  or or_5 (or_5_out, ALU_OPC[0], ALU_OPC[1], ALU_OPC[2]);
  or or_6 (or_6_out, or_5_out, INSTRUCTION[3]);
  nor nor_1 (nor_1_out, ALU_OPC[0], ALU_OPC[1], ALU_OPC[2]);
  nor nor_2 (nor_2_out, ALU_OPC[0], ALU_OPC[1], ALU_OPC[2]);
  nand nand_1 (nand_1_out, nor_2_out, not_215_out);
  nor nor_3 (nor_3_out, ALU_OPC[0], ALU_OPC[1], ALU_OPC[2]);
  and and_1 (and_1_out, nor_3_out, not_217_out);
  nor nor_4 (nor_4_out, ALU_OPC[0], ALU_OPC[1], ALU_OPC[2]);
  and and_2 (and_2_out, nor_4_out, not_218_out);
  not not_2 (not_2_out, INSTRUCTION[7]);
  Decoder #(.select(3)) decoder_1 (
    .out0(decoder_1_out0), .out1(decoder_1_out1), .out2(decoder_1_out2), .out3(decoder_1_out3),
    .out4(decoder_1_out4), .out5(decoder_1_out5), .out6(decoder_1_out6), .out7(decoder_1_out7),
    .sel(ALU_OPC), .en(not_2_out));
  not not_3 (not_3_out, decoder_1_out0);
  not not_4 (not_4_out, decoder_1_out1);
  or or_7 (or_7_out[1], INSTRUCTION[0], INSTRUCTION[1], INSTRUCTION[2]);
  or or_8 (or_8_out, INSTRUCTION[0], INSTRUCTION[1]);
  and and_3 (and_3_out, INSTRUCTION[7], ALU_OPC[2], ALU_OPC[1], ALU_OPC[0]);
  not not_5 (not_5_out, and_3_out);
  nor nor_5 (nor_5_out, ALU_OPC[2], ALU_OPC[1], ALU_OPC[0]);
  or or_9 (or_9_out, INSTRUCTION[0], INSTRUCTION[1]);
  not not_6 (not_6_out, ALU_OPC[2]);
  not not_7 (not_7_out, ALU_OPC[0]);
  not not_8 (not_8_out, ALU_OPC[1]);
  and and_4 (and_4_out, not_6_out, not_8_out, not_7_out);
  not not_9 (not_9_out, INSTRUCTION[7]);
  or or_10 (or_10_out, INSTRUCTION[0], INSTRUCTION[1]);
  not not_10 (not_10_out, ALU_OPC[2]);
  not not_11 (not_11_out, ALU_OPC[0]);
  not not_12 (not_12_out, ALU_OPC[1]);
  nand nand_2 (nand_2_out, not_10_out, not_12_out, not_11_out, and_26_out);
  or or_11 (or_11_out, INSTRUCTION[0], INSTRUCTION[1]);
  not not_13 (not_13_out, ALU_OPC[2]);
  not not_14 (not_14_out, ALU_OPC[0]);
  not not_15 (not_15_out, ALU_OPC[1]);
  nand nand_3 (nand_3_out, not_13_out, not_15_out, not_14_out, and_27_out);
  or or_12 (or_12_out, INSTRUCTION[0], INSTRUCTION[1]);
  not not_16 (not_16_out, ALU_OPC[0]);
  not not_17 (not_17_out, ALU_OPC[1]);
  nand nand_4 (nand_4_out, not_1_out, not_17_out, not_16_out, and_18_out);
  or or_13 (or_13_out, INSTRUCTION[0], INSTRUCTION[1]);
  not not_18 (not_18_out, ALU_OPC[2]);
  not not_19 (not_19_out, ALU_OPC[0]);
  not not_20 (not_20_out, ALU_OPC[1]);
  nand nand_5 (nand_5_out, not_18_out, not_20_out, not_19_out, and_28_out);
  or or_14 (or_14_out, INSTRUCTION[0], INSTRUCTION[1]);
  or or_15 (or_15_out, ALU_OPC[0], ALU_OPC[1]);
  or or_16 (or_16_out, or_15_out, ALU_OPC[2]);
  or or_17 (or_17_out, or_16_out, INSTRUCTION[3]);
  or or_18 (or_18_out[0], or_1_out, INSTRUCTION[2]);
  Decoder #(.select(3)) decoder_2 (
    .out0(decoder_2_out0), .out1(decoder_2_out1), .out2(decoder_2_out2), .out3(decoder_2_out3),
    .out4(decoder_2_out4), .out5(decoder_2_out5), .out6(decoder_2_out6), .out7(decoder_2_out7),
    .sel(ALU_OPC), .en(not_21_out));
  not not_21 (not_21_out, INSTRUCTION[7]);
  not not_22 (not_22_out, decoder_2_out0);
  not not_23 (not_23_out, decoder_2_out2);
  not not_24 (not_24_out, decoder_2_out4);
  not not_25 (not_25_out, decoder_2_out1);
  not not_26 (not_26_out, decoder_2_out3);
  or or_19 (or_19_out[0], INSTRUCTION[0], INSTRUCTION[1], INSTRUCTION[2]);
  Decoder #(.select(3)) decoder_3 (
    .out0(decoder_3_out0), .out1(decoder_3_out1), .out2(decoder_3_out2), .out3(decoder_3_out3),
    .out4(decoder_3_out4), .out5(decoder_3_out5), .out6(decoder_3_out6), .out7(decoder_3_out7),
    .sel(ALU_OPC), .en(not_27_out));
  not not_27 (not_27_out, INSTRUCTION[7]);
  not not_28 (not_28_out, decoder_3_out0);
  not not_29 (not_29_out, decoder_3_out2);
  not not_30 (not_30_out, decoder_3_out4);
  not not_31 (not_31_out, decoder_3_out1);
  not not_32 (not_32_out, decoder_3_out3);
  nor nor_6 (nor_6_out[0], INSTRUCTION[0], INSTRUCTION[1], INSTRUCTION[2]);
  Decoder #(.select(3)) decoder_4 (
    .out0(decoder_4_out0), .out1(decoder_4_out1), .out2(decoder_4_out2), .out3(decoder_4_out3),
    .out4(decoder_4_out4), .out5(decoder_4_out5), .out6(decoder_4_out6), .out7(decoder_4_out7),
    .sel(ALU_OPC), .en(not_33_out));
  not not_33 (not_33_out, INSTRUCTION[7]);
  not not_34 (not_34_out, decoder_4_out0);
  not not_35 (not_35_out, decoder_4_out1);
  nand nand_6 (nand_6_out, nor_1_out, not_213_out);
  _7474 u_7474_1 ();  // open: pin1, pin2, pin3, pin4, pin5, pin6, pin13, pin12, pin11, pin10, pin9, pin8
  nor nor_7 (nor_7_out, INSTRUCTION[0], INSTRUCTION[1], INSTRUCTION[2]);
  Decoder #(.select(3)) decoder_5 (
    .out0(decoder_5_out0), .out1(decoder_5_out1), .out2(decoder_5_out2), .out3(decoder_5_out3),
    .out4(decoder_5_out4), .out5(decoder_5_out5), .out6(decoder_5_out6), .out7(decoder_5_out7),
    .sel(ALU_OPC), .en(not_36_out));
  not not_36 (not_36_out, INSTRUCTION[7]);
  not not_37 (not_37_out, decoder_5_out0);
  not not_38 (not_38_out, decoder_5_out2);
  not not_39 (not_39_out, decoder_5_out4);
  not not_40 (not_40_out, decoder_5_out1);
  not not_41 (not_41_out, decoder_5_out3);
  nor nor_8 (nor_8_out[0], INSTRUCTION[0], INSTRUCTION[1], INSTRUCTION[2]);
  Decoder #(.select(3)) decoder_6 (
    .out0(decoder_6_out0), .out1(decoder_6_out1), .out2(decoder_6_out2), .out3(decoder_6_out3),
    .out4(decoder_6_out4), .out5(decoder_6_out5), .out6(decoder_6_out6), .out7(decoder_6_out7),
    .sel(ALU_OPC), .en(not_42_out));
  not not_42 (not_42_out, INSTRUCTION[7]);
  not not_43 (not_43_out, decoder_6_out0);
  not not_44 (not_44_out, decoder_6_out2);
  not not_45 (not_45_out, decoder_6_out1);
  nor nor_9 (nor_9_out[0], INSTRUCTION[0], INSTRUCTION[1], INSTRUCTION[2]);
  Decoder #(.select(3)) decoder_7 (
    .out0(decoder_7_out0), .out1(decoder_7_out1), .out2(decoder_7_out2), .out3(decoder_7_out3),
    .out4(decoder_7_out4), .out5(decoder_7_out5), .out6(decoder_7_out6), .out7(decoder_7_out7),
    .sel(ALU_OPC), .en(not_46_out));
  not not_46 (not_46_out, INSTRUCTION[7]);
  not not_47 (not_47_out, decoder_7_out0);
  not not_48 (not_48_out, decoder_7_out2);
  not not_49 (not_49_out, decoder_7_out4);
  not not_50 (not_50_out, decoder_7_out1);
  not not_51 (not_51_out, decoder_7_out3);
  not not_52 (not_52_out, decoder_7_out5);
  not not_53 (not_53_out, INSTRUCTION[7]);
  // NOT_Gate not_54 has open pins: in=decoder_1_out2, out=open
  not not_55 (not_55_out, decoder_1_out4);
  not not_56 (not_56_out, decoder_1_out6);
  not not_57 (not_57_out, decoder_1_out3);
  not not_58 (not_58_out, decoder_1_out5);
  not not_59 (not_59_out, decoder_1_out7);
  Decoder #(.select(3)) decoder_8 (
    .out0(decoder_8_out0), .out1(decoder_8_out1), .out2(decoder_8_out2), .out3(decoder_8_out3),
    .out4(decoder_8_out4), .out5(decoder_8_out5), .out6(decoder_8_out6), .out7(decoder_8_out7),
    .sel(ALU_OPC), .en(1'b1));
  not not_60 (not_60_out, decoder_8_out0);
  // NOT_Gate not_61 has open pins: in=decoder_8_out2, out=open
  not not_62 (not_62_out, decoder_8_out4);
  not not_63 (not_63_out, decoder_8_out6);
  not not_64 (not_64_out, decoder_8_out1);
  not not_65 (not_65_out, decoder_8_out3);
  not not_66 (not_66_out, decoder_8_out5);
  or or_20 (or_20_out[1], or_8_out, INSTRUCTION[2]);
  not not_67 (not_67_out, INSTRUCTION[7]);
  Decoder #(.select(3)) decoder_9 (
    .out0(decoder_9_out0), .out1(decoder_9_out1), .out2(decoder_9_out2), .out3(decoder_9_out3),
    .out4(decoder_9_out4), .out5(decoder_9_out5), .out6(decoder_9_out6), .out7(decoder_9_out7),
    .sel(ALU_OPC), .en(not_67_out));
  not not_68 (not_68_out, decoder_9_out0);
  // NOT_Gate not_69 has open pins: in=decoder_9_out2, out=open
  not not_70 (not_70_out, decoder_9_out4);
  not not_71 (not_71_out, decoder_9_out1);
  not not_72 (not_72_out, decoder_9_out3);
  or or_21 (or_21_out, INSTRUCTION[0], INSTRUCTION[1]);
  or or_22 (or_22_out[1], or_21_out, INSTRUCTION[2]);
  not not_73 (not_73_out, INSTRUCTION[7]);
  Decoder #(.select(3)) decoder_10 (
    .out0(decoder_10_out0), .out1(decoder_10_out1), .out2(decoder_10_out2), .out3(decoder_10_out3),
    .out4(decoder_10_out4), .out5(decoder_10_out5), .out6(decoder_10_out6), .out7(decoder_10_out7),
    .sel(ALU_OPC), .en(not_73_out));
  not not_74 (not_74_out, decoder_10_out0);
  not not_75 (not_75_out, INSTRUCTION[7]);
  or or_23 (or_23_out[1], or_9_out, INSTRUCTION[2]);
  not not_76 (not_76_out, INSTRUCTION[7]);
  Decoder #(.select(3)) decoder_11 (
    .out0(decoder_11_out0), .out1(decoder_11_out1), .out2(decoder_11_out2), .out3(decoder_11_out3),
    .out4(decoder_11_out4), .out5(decoder_11_out5), .out6(decoder_11_out6), .out7(decoder_11_out7),
    .sel(ALU_OPC), .en(not_76_out));
  not not_77 (not_77_out, decoder_11_out0);
  not not_78 (not_78_out, decoder_11_out2);
  not not_79 (not_79_out, decoder_11_out4);
  not not_80 (not_80_out, decoder_11_out1);
  not not_81 (not_81_out, decoder_11_out3);
  or or_24 (or_24_out[1], or_10_out, INSTRUCTION[2]);
  not not_82 (not_82_out, INSTRUCTION[7]);
  Decoder #(.select(3)) decoder_12 (
    .out0(decoder_12_out0), .out1(decoder_12_out1), .out2(decoder_12_out2), .out3(decoder_12_out3),
    .out4(decoder_12_out4), .out5(decoder_12_out5), .out6(decoder_12_out6), .out7(decoder_12_out7),
    .sel(ALU_OPC), .en(not_82_out));
  not not_83 (not_83_out, decoder_12_out0);
  not not_84 (not_84_out, decoder_12_out2);
  not not_85 (not_85_out, decoder_12_out4);
  not not_86 (not_86_out, decoder_12_out1);
  not not_87 (not_87_out, decoder_12_out3);
  or or_25 (or_25_out[1], or_11_out, INSTRUCTION[2]);
  not not_88 (not_88_out, INSTRUCTION[7]);
  Decoder #(.select(3)) decoder_13 (
    .out0(decoder_13_out0), .out1(decoder_13_out1), .out2(decoder_13_out2), .out3(decoder_13_out3),
    .out4(decoder_13_out4), .out5(decoder_13_out5), .out6(decoder_13_out6), .out7(decoder_13_out7),
    .sel(ALU_OPC), .en(not_88_out));
  not not_89 (not_89_out, decoder_13_out0);
  not not_90 (not_90_out, decoder_13_out2);
  not not_91 (not_91_out, decoder_13_out1);
  not not_92 (not_92_out, decoder_13_out3);
  or or_26 (or_26_out[1], or_12_out, INSTRUCTION[2]);
  not not_93 (not_93_out, INSTRUCTION[7]);
  Decoder #(.select(3)) decoder_14 (
    .out0(decoder_14_out0), .out1(decoder_14_out1), .out2(decoder_14_out2), .out3(decoder_14_out3),
    .out4(decoder_14_out4), .out5(decoder_14_out5), .out6(decoder_14_out6), .out7(decoder_14_out7),
    .sel(ALU_OPC), .en(not_93_out));
  not not_94 (not_94_out, decoder_14_out0);
  not not_95 (not_95_out, decoder_14_out2);
  not not_96 (not_96_out, decoder_14_out4);
  // NOT_Gate not_97 has open pins: in=decoder_14_out6, out=open
  not not_98 (not_98_out, decoder_14_out1);
  not not_99 (not_99_out, decoder_14_out3);
  not not_100 (not_100_out, decoder_14_out5);
  not not_101 (not_101_out, decoder_14_out7);
  or or_27 (or_27_out[1], or_13_out, INSTRUCTION[2]);
  not not_102 (not_102_out, INSTRUCTION[7]);
  Decoder #(.select(3)) decoder_15 (
    .out0(decoder_15_out0), .out1(decoder_15_out1), .out2(decoder_15_out2), .out3(decoder_15_out3),
    .out4(decoder_15_out4), .out5(decoder_15_out5), .out6(decoder_15_out6), .out7(decoder_15_out7),
    .sel(ALU_OPC), .en(not_102_out));
  not not_103 (not_103_out, decoder_15_out0);
  not not_104 (not_104_out, decoder_15_out2);
  not not_105 (not_105_out, decoder_15_out4);
  not not_106 (not_106_out, decoder_15_out1);
  not not_107 (not_107_out, decoder_15_out3);
  or or_28 (or_28_out[0], or_14_out, INSTRUCTION[2]);
  Decoder #(.select(3)) decoder_16 (
    .out0(decoder_16_out0), .out1(decoder_16_out1), .out2(decoder_16_out2), .out3(decoder_16_out3),
    .out4(decoder_16_out4), .out5(decoder_16_out5), .out6(decoder_16_out6), .out7(decoder_16_out7),
    .sel(ALU_OPC), .en(not_108_out));
  not not_108 (not_108_out, INSTRUCTION[7]);
  not not_109 (not_109_out, decoder_16_out0);
  not not_110 (not_110_out, decoder_16_out2);
  not not_111 (not_111_out, decoder_16_out4);
  not not_112 (not_112_out, decoder_16_out1);
  not not_113 (not_113_out, decoder_16_out3);
  not not_114 (not_114_out, decoder_16_out5);
  // NOT_Gate not_115 has open pins: in=decoder_2_out6, out=open
  not not_116 (not_116_out, decoder_2_out5);
  // NOT_Gate not_117 has open pins: in=decoder_2_out7, out=open
  _7474 u_7474_2 ();  // open: pin1, pin2, pin3, pin4, pin5, pin6, pin13, pin12, pin11, pin10, pin9, pin8
  // NOT_Gate not_118 has open pins: in=decoder_3_out6, out=open
  not not_119 (not_119_out, decoder_3_out5);
  // NOT_Gate not_120 has open pins: in=decoder_3_out7, out=open
  _7474 u_7474_3 ();  // open: pin1, pin2, pin3, pin4, pin5, pin6, pin13, pin12, pin11, pin10, pin9, pin8
  not not_121 (not_121_out, decoder_4_out2);
  not not_122 (not_122_out, decoder_4_out4);
  // NOT_Gate not_123 has open pins: in=decoder_4_out6, out=open
  not not_124 (not_124_out, decoder_4_out3);
  not not_125 (not_125_out, decoder_4_out5);
  // NOT_Gate not_126 has open pins: in=decoder_4_out7, out=open
  // NOT_Gate not_127 has open pins: in=decoder_5_out6, out=open
  not not_128 (not_128_out, decoder_5_out5);
  // NOT_Gate not_129 has open pins: in=decoder_5_out7, out=open
  not not_130 (not_130_out, decoder_6_out4);
  // NOT_Gate not_131 has open pins: in=decoder_6_out6, out=open
  not not_132 (not_132_out, decoder_6_out3);
  not not_133 (not_133_out, decoder_6_out5);
  // NOT_Gate not_134 has open pins: in=decoder_6_out7, out=open
  _7474 u_7474_4 ();  // open: pin1, pin2, pin3, pin4, pin5, pin6, pin13, pin12, pin11, pin10, pin9, pin8
  // NOT_Gate not_135 has open pins: in=decoder_7_out6, out=open
  // NOT_Gate not_136 has open pins: in=decoder_7_out7, out=open
  _7474 u_7474_5 ();  // open: pin1, pin2, pin3, pin4, pin5, pin6, pin13, pin12, pin11, pin10, pin9, pin8
  and and_5 (and_5_out, CLOCK, C_IRQ);
  and and_6 (and_6_out, CLOCK, C_NMI);
  and and_7 (and_7_out, CLOCK, C_RST);
  not not_137 (not_137_out, INSTRUCTION[2]);
  not not_138 (not_138_out, decoder_8_out7);
  not not_139 (not_139_out, decoder_9_out6);
  not not_140 (not_140_out, decoder_9_out5);
  not not_141 (not_141_out, decoder_9_out7);
  not not_142 (not_142_out, decoder_10_out2);
  not not_143 (not_143_out, decoder_10_out4);
  // NOT_Gate not_144 has open pins: in=decoder_10_out6, out=open
  not not_145 (not_145_out, decoder_10_out1);
  not not_146 (not_146_out, decoder_10_out3);
  not not_147 (not_147_out, decoder_10_out5);
  not not_148 (not_148_out, decoder_10_out7);
  // NOT_Gate not_149 has open pins: in=decoder_11_out6, out=open
  not not_150 (not_150_out, decoder_11_out5);
  not not_151 (not_151_out, decoder_11_out7);
  // NOT_Gate not_152 has open pins: in=decoder_12_out6, out=open
  not not_153 (not_153_out, decoder_12_out5);
  not not_154 (not_154_out, decoder_12_out7);
  not not_155 (not_155_out, decoder_13_out4);
  // NOT_Gate not_156 has open pins: in=decoder_13_out6, out=open
  not not_157 (not_157_out, decoder_13_out5);
  not not_158 (not_158_out, decoder_13_out7);
  // NOT_Gate not_159 has open pins: in=decoder_15_out6, out=open
  not not_160 (not_160_out, decoder_15_out5);
  not not_161 (not_161_out, decoder_15_out7);
  // NOT_Gate not_162 has open pins: in=decoder_16_out6, out=open
  // NOT_Gate not_163 has open pins: in=decoder_16_out7, out=open
  _7474 u_7474_6 ();  // open: pin1, pin2, pin3, pin4, pin5, pin6, pin13, pin12, pin11, pin10, pin9, pin8
  not not_164 (not_164_out, STB_BUFF);
  not not_165 (not_165_out, ARG2_E);
  Decoder #(.select(3)) decoder_17 (
    .out0(decoder_17_out0), .out1(decoder_17_out1), .out2(decoder_17_out2), .out3(decoder_17_out3),
    .out4(decoder_17_out4), .out5(decoder_17_out5), .out6(decoder_17_out6), .out7(decoder_17_out7),
    .sel({INSTRUCTION[1:0], INSTRUCTION[3]}), .en(not_137_out));
  not not_166 (not_166_out, decoder_17_out0);
  not not_167 (not_167_out, decoder_17_out1);
  Decoder #(.select(2)) decoder_18 (
    .out0(decoder_18_out0), .out1(decoder_18_out1), .out2(decoder_18_out2), .out3(decoder_18_out3),
    .sel({or_7_out[1], INSTRUCTION[3]}), .en(1'b1));
  not not_168 (not_168_out, decoder_18_out0);
  not not_169 (not_169_out, decoder_18_out1);
  Decoder #(.select(2)) decoder_19 (
    .out0(decoder_19_out0), .out1(decoder_19_out1), .out2(decoder_19_out2), .out3(decoder_19_out3),
    .sel({or_26_out[1], INSTRUCTION[3]}), .en(1'b1));
  not not_170 (not_170_out, decoder_19_out0);
  not not_171 (not_171_out, decoder_19_out2);
  not not_172 (not_172_out, decoder_19_out1);
  or or_29 (or_29_out, not_170_out, not_94_out);
  or or_30 (or_30_out, not_172_out, not_94_out);
  or or_31 (or_31_out, not_197_out, not_103_out);
  and and_8 (and_8_out, MBUS_OE, not_164_out);
  and and_9 (and_9_out, ARG1_E, not_165_out);
  D_Flip_Flop d_ff_1 (.clk(1'b0), .D(1'b0), .Q(d_ff_1_q), .Qn(d_ff_1_qn), .preset(S_IRQ), .reset(and_11_out));
  and and_10 (and_10_out, d_ff_5_q, d_ff_2_qn);
  and and_11 (and_11_out, and_10_out, and_5_out);
  D_Flip_Flop d_ff_2 (.clk(1'b0), .D(1'b0), .Q(d_ff_2_q), .Qn(d_ff_2_qn), .preset(IRQ), .reset(and_5_out));
  D_Flip_Flop d_ff_3 (.clk(1'b0), .D(1'b0), .Q(d_ff_3_q), .preset(NMI), .reset(and_6_out));  // open: Qn
  D_Flip_Flop d_ff_4 (.clk(1'b0), .D(1'b0), .Q(d_ff_4_q), .preset(RST), .reset(and_7_out));  // open: Qn
  or or_32 (or_32_out, and_7_out, and_6_out, and_5_out);
  nand nand_7 (nand_7_out, not_166_out, not_167_out);
  not not_173 (not_173_out, decoder_18_out2);
  not not_174 (not_174_out, decoder_18_out3);
  nand nand_8 (nand_8_out, not_168_out, not_169_out);
  _7474 u_7474_7 ();  // open: pin1, pin2, pin3, pin4, pin5, pin6, pin13, pin12, pin11, pin10, pin9, pin8
  Decoder #(.select(2)) decoder_20 (
    .out0(decoder_20_out0), .out1(decoder_20_out1), .out2(decoder_20_out2), .out3(decoder_20_out3),
    .sel({or_20_out[1], INSTRUCTION[3]}), .en(1'b1));
  not not_175 (not_175_out, decoder_20_out0);
  not not_176 (not_176_out, decoder_20_out2);
  not not_177 (not_177_out, decoder_20_out1);
  not not_178 (not_178_out, decoder_20_out3);
  nand nand_9 (nand_9_out, not_175_out, not_177_out);
  Decoder #(.select(2)) decoder_21 (
    .out0(decoder_21_out0), .out1(decoder_21_out1), .out2(decoder_21_out2), .out3(decoder_21_out3),
    .sel({or_22_out[1], INSTRUCTION[3]}), .en(1'b1));
  not not_179 (not_179_out, decoder_21_out0);
  not not_180 (not_180_out, decoder_21_out2);
  not not_181 (not_181_out, decoder_21_out1);
  not not_182 (not_182_out, decoder_21_out3);
  _7474 u_7474_8 ();  // open: pin1, pin2, pin3, pin4, pin5, pin6, pin13, pin12, pin11, pin10, pin9, pin8
  Decoder #(.select(2)) decoder_22 (
    .out0(decoder_22_out0), .out1(decoder_22_out1), .out2(decoder_22_out2), .out3(decoder_22_out3),
    .sel({or_23_out[1], INSTRUCTION[3]}), .en(1'b1));
  not not_183 (not_183_out, decoder_22_out0);
  not not_184 (not_184_out, decoder_22_out2);
  not not_185 (not_185_out, decoder_22_out1);
  not not_186 (not_186_out, decoder_22_out3);
  nand nand_10 (nand_10_out, not_183_out, not_185_out);
  _7474 u_7474_9 ();  // open: pin1, pin2, pin3, pin4, pin5, pin6, pin13, pin12, pin11, pin10, pin9, pin8
  Decoder #(.select(2)) decoder_23 (
    .out0(decoder_23_out0), .out1(decoder_23_out1), .out2(decoder_23_out2), .out3(decoder_23_out3),
    .sel({or_24_out[1], INSTRUCTION[3]}), .en(1'b1));
  not not_187 (not_187_out, decoder_23_out0);
  not not_188 (not_188_out, decoder_23_out2);
  not not_189 (not_189_out, decoder_23_out1);
  not not_190 (not_190_out, decoder_23_out3);
  and and_12 (and_12_out, not_187_out, not_189_out);
  not not_191 (not_191_out, and_12_out);
  _7474 u_7474_10 ();  // open: pin1, pin2, pin3, pin4, pin5, pin6, pin13, pin12, pin11, pin10, pin9, pin8
  Decoder #(.select(2)) decoder_24 (
    .out0(decoder_24_out0), .out1(decoder_24_out1), .out2(decoder_24_out2), .out3(decoder_24_out3),
    .sel({or_25_out[1], INSTRUCTION[3]}), .en(1'b1));
  not not_192 (not_192_out, decoder_24_out0);
  not not_193 (not_193_out, decoder_24_out2);
  not not_194 (not_194_out, decoder_24_out1);
  not not_195 (not_195_out, decoder_24_out3);
  _7474 u_7474_11 ();  // open: pin1, pin2, pin3, pin4, pin5, pin6, pin13, pin12, pin11, pin10, pin9, pin8
  not not_196 (not_196_out, decoder_19_out3);
  nand nand_11 (nand_11_out, not_170_out, not_172_out);
  _7474 u_7474_12 ();  // open: pin1, pin2, pin3, pin4, pin5, pin6, pin13, pin12, pin11, pin10, pin9, pin8
  Decoder #(.select(2)) decoder_25 (
    .out0(decoder_25_out0), .out1(decoder_25_out1), .out2(decoder_25_out2), .out3(decoder_25_out3),
    .sel({or_27_out[1], INSTRUCTION[3]}), .en(1'b1));
  not not_197 (not_197_out, decoder_25_out0);
  not not_198 (not_198_out, decoder_25_out2);
  not not_199 (not_199_out, decoder_25_out1);
  not not_200 (not_200_out, decoder_25_out3);
  nand nand_12 (nand_12_out, not_197_out, not_199_out);
  or or_33 (or_33_out, not_199_out, not_103_out);
  not not_201 (not_201_out, INSTRUCTION[3]);
  not not_202 (not_202_out, not_24_out);
  not not_203 (not_203_out, not_22_out);
  Decoder #(.select(2)) decoder_26 (
    .out0(decoder_26_out0), .out1(decoder_26_out1), .out2(decoder_26_out2), .out3(decoder_26_out3),
    .sel({INSTRUCTION[3], or_18_out[0]}), .en(not_203_out));
  not not_204 (not_204_out, decoder_26_out0);
  not not_205 (not_205_out, decoder_26_out2);
  not not_206 (not_206_out, decoder_26_out1);
  not not_207 (not_207_out, INSTRUCTION[3]);
  not not_208 (not_208_out, not_30_out);
  not not_209 (not_209_out, not_28_out);
  Decoder #(.select(2)) decoder_27 (
    .out0(decoder_27_out0), .out1(decoder_27_out1), .out2(decoder_27_out2), .out3(decoder_27_out3),
    .sel({INSTRUCTION[3], or_19_out[0]}), .en(not_209_out));
  not not_210 (not_210_out, decoder_27_out0);
  not not_211 (not_211_out, decoder_27_out2);
  not not_212 (not_212_out, decoder_27_out1);
  not not_213 (not_213_out, INSTRUCTION[3]);
  not not_214 (not_214_out, INSTRUCTION[7]);
  not not_215 (not_215_out, INSTRUCTION[3]);
  not not_216 (not_216_out, INSTRUCTION[7]);
  not not_217 (not_217_out, INSTRUCTION[3]);
  not not_218 (not_218_out, INSTRUCTION[3]);
  and and_13 (and_13_out, d_ff_2_qn, not_219_out);
  not not_219 (not_219_out, and_5_out);
  Latch latch_1 (.DOUT(latch_1_dout), .LOCK_E(CLOCK), .DIN(d_ff_3_q));
  Latch latch_2 (.DOUT(latch_2_dout), .LOCK_E(CLOCK), .DIN(d_ff_4_q));
  or or_34 (or_34_out, INSTRUCTION[0], INSTRUCTION[1], INSTRUCTION[2]);
  not not_220 (not_220_out, INSTRUCTION[7]);
  and and_14 (and_14_out, not_168_out, not_173_out);
  and and_15 (and_15_out, not_169_out, not_174_out);
  and and_16 (and_16_out, not_175_out, not_176_out);
  _7474 u_7474_13 ();  // open: pin1, pin2, pin3, pin4, pin5, pin6, pin13, pin12, pin11, pin10, pin9, pin8
  nand nand_13 (nand_13_out, not_179_out, not_181_out);
  and and_17 (and_17_out, not_192_out, not_194_out);
  not not_221 (not_221_out, and_17_out);
  not not_222 (not_222_out, not_193_out);
  and and_18 (and_18_out, not_172_out, not_196_out);
  not not_223 (not_223_out, not_171_out);
  nand nand_14 (nand_14_out, or_29_out, or_30_out);
  not not_224 (not_224_out, not_198_out);
  not not_225 (not_225_out, INSTRUCTION[3]);
  not not_226 (not_226_out, not_109_out);
  Decoder #(.select(2)) decoder_28 (
    .out0(decoder_28_out0), .out1(decoder_28_out1), .out2(decoder_28_out2), .out3(decoder_28_out3),
    .sel({INSTRUCTION[3], or_28_out[0]}), .en(not_226_out));
  not not_227 (not_227_out, decoder_28_out0);
  not not_228 (not_228_out, decoder_28_out2);
  not not_229 (not_229_out, decoder_28_out1);
  not not_230 (not_230_out, decoder_28_out3);
  not not_231 (not_231_out, decoder_26_out3);
  not not_232 (not_232_out, not_205_out);
  not not_233 (not_233_out, decoder_27_out3);
  not not_234 (not_234_out, not_211_out);
  not not_235 (not_235_out, not_34_out);
  Decoder #(.select(2)) decoder_29 (
    .out0(decoder_29_out0), .out1(decoder_29_out1), .out2(decoder_29_out2), .out3(decoder_29_out3),
    .sel({INSTRUCTION[3], nor_6_out[0]}), .en(not_235_out));
  // NOT_Gate not_236 has open pins: in=decoder_29_out0, out=open
  // NOT_Gate not_237 has open pins: in=decoder_29_out2, out=open
  not not_238 (not_238_out, decoder_29_out1);
  not not_239 (not_239_out, decoder_29_out3);
  not not_240 (not_240_out, not_43_out);
  Decoder #(.select(2)) decoder_30 (
    .out0(decoder_30_out0), .out1(decoder_30_out1), .out2(decoder_30_out2), .out3(decoder_30_out3),
    .sel({INSTRUCTION[3], nor_8_out[0]}), .en(not_240_out));
  // NOT_Gate not_241 has open pins: in=decoder_30_out0, out=open
  // NOT_Gate not_242 has open pins: in=decoder_30_out2, out=open
  not not_243 (not_243_out, decoder_30_out1);
  not not_244 (not_244_out, not_47_out);
  Decoder #(.select(2)) decoder_31 (
    .out0(decoder_31_out0), .out1(decoder_31_out1), .out2(decoder_31_out2), .out3(decoder_31_out3),
    .sel({INSTRUCTION[3], nor_9_out[0]}), .en(not_244_out));
  // NOT_Gate not_245 has open pins: in=decoder_31_out0, out=open
  // NOT_Gate not_246 has open pins: in=decoder_31_out2, out=open
  not not_247 (not_247_out, decoder_31_out1);
  not not_248 (not_248_out, decoder_31_out3);
  D_Flip_Flop d_ff_5 (.Q(d_ff_5_q), .preset(and_13_out), .reset(or_35_out));  // open: clk, D, Qn
  or or_35 (or_35_out, d_ff_2_q, d_ff_1_qn);
  Latch latch_3 (.DOUT(latch_3_dout), .LOCK_E(CLOCK), .DIN(or_37_out));
  not not_249 (not_249_out, INSTRUCTION[7]);
  not not_250 (not_250_out, ALU_OPC[0]);
  not not_251 (not_251_out, ALU_OPC[2]);
  not not_252 (not_252_out, ALU_OPC[1]);
  and and_19 (and_19_out, not_220_out, not_251_out, not_252_out, not_250_out);
  and and_20 (and_20_out, and_19_out, INSTRUCTION[3], not_253_out);
  not not_253 (not_253_out, or_34_out);
  and and_21 (and_21_out, and_19_out, or_34_out);
  and and_22 (and_22_out, and_19_out, not_254_out);
  not not_254 (not_254_out, INSTRUCTION[3]);
  nor nor_10 (nor_10_out, not_3_out, not_167_out);
  nor nor_11 (nor_11_out, not_3_out, nand_7_out);
  nor nor_12 (nor_12_out, not_3_out, not_166_out);
  and and_23 (and_23_out, not_177_out, not_178_out);
  and and_24 (and_24_out, not_181_out, not_182_out);
  and and_25 (and_25_out, not_185_out, not_186_out);
  not not_255 (not_255_out, not_183_out);
  and and_26 (and_26_out, not_189_out, not_190_out);
  not not_256 (not_256_out, not_187_out);
  and and_27 (and_27_out, not_194_out, not_195_out);
  not not_257 (not_257_out, and_18_out);
  and and_28 (and_28_out, not_199_out, not_200_out);
  nand nand_15 (nand_15_out, or_31_out, or_33_out);
  not not_258 (not_258_out, not_109_out);
  and and_29 (and_29_out, not_25_out, not_23_out);
  nor nor_13 (nor_13_out, not_232_out, not_22_out);
  nand nand_16 (UNUSEDt, not_205_out, not_204_out);
  not not_259 (not_259_out, not_31_out);
  nor nor_14 (nor_14_out, not_234_out, not_28_out);
  nand nand_17 (UNUSEDt, not_211_out, not_210_out);
  not not_260 (not_260_out, not_239_out);
  not not_261 (not_261_out, INSTRUCTION[3]);
  not not_262 (not_262_out, nor_6_out[0]);
  and and_30 (and_30_out, not_40_out, not_38_out);
  nor nor_15 (nor_15_out, nor_7_out, INSTRUCTION[3], not_37_out);
  not not_263 (not_263_out, nor_7_out);
  nor nor_16 (UNUSEDt, not_263_out, not_37_out);
  not not_264 (not_264_out, nor_8_out[0]);
  not not_265 (not_265_out, decoder_30_out3);
  not not_266 (not_266_out, not_265_out);
  and and_31 (and_31_out, not_50_out, not_48_out);
  and and_32 (and_32_out, and_31_out, not_51_out);
  not not_267 (not_267_out, not_248_out);
  or or_36 (or_36_out, CLEAR_BUFF, or_32_out);
  or or_37 (or_37_out, d_ff_2_q, d_ff_1_q);
  not not_268 (not_268_out, ERR);
  not not_269 (not_269_out, ALU_OPC[2]);
  not not_270 (not_270_out, ALU_OPC[1]);
  and and_33 (and_33_out, not_249_out, not_269_out, not_270_out, ALU_OPC[0]);
  not not_271 (not_271_out, INSTRUCTION[3]);
  and and_34 (and_34_out, and_33_out, not_271_out);
  not not_272 (not_272_out, not_271_out);
  and and_35 (and_35_out, and_33_out, not_272_out);
  or or_38 (or_38_out, and_21_out, and_22_out);
  and and_36 (and_36_out, not_64_out, or_99_out, not_65_out);
  // NOR_Gate nor_17 has open pins: in0=not_60_out, in1=not_169_out, out=open
  and and_37 (and_37_out, or_68_out, not_60_out, or_99_out);
  nor nor_18 (nor_18_out, and_37_out, nand_8_out);
  nor nor_19 (nor_19_out, not_60_out, and_14_out);
  or or_39 (or_39_out, not_68_out, not_177_out);
  and and_38 (and_38_out, not_68_out, not_5_out);
  or or_40 (or_40_out, not_68_out, and_16_out);
  or or_41 (or_41_out, not_74_out, not_273_out);
  not not_273 (not_273_out, not_179_out);
  and and_39 (and_39_out, not_77_out, not_78_out);
  or or_42 (or_42_out, not_77_out, not_255_out);
  and and_40 (and_40_out, not_83_out, not_84_out);
  or or_43 (or_43_out, not_83_out, not_256_out);
  and and_41 (and_41_out, not_89_out, not_90_out);
  or or_44 (or_44_out, not_89_out, and_27_out);
  not not_274 (not_274_out, not_98_out);
  not not_275 (not_275_out, not_95_out);
  nor nor_20 (nor_20_out, not_274_out, not_275_out);
  nand nand_18 (nand_18_out, nor_20_out, not_99_out);
  and and_42 (and_42_out, not_94_out, not_95_out);
  or or_45 (or_45_out, and_42_out, nand_11_out);
  not not_276 (not_276_out, not_106_out);
  nor nor_21 (nor_21_out, not_276_out, not_291_out);
  and and_43 (and_43_out, not_103_out, not_104_out);
  and and_44 (and_44_out, not_112_out, not_110_out);
  and and_45 (and_45_out, and_44_out, not_113_out);
  nand nand_19 (nand_19_out, not_228_out, not_258_out);
  nand nand_20 (UNUSEDt, not_228_out, not_227_out);
  and and_46 (and_46_out, and_29_out, not_26_out);
  nor nor_22 (ARGC_3t, and_46_out, not_201_out);
  not not_277 (not_277_out, not_29_out);
  not not_278 (not_278_out, not_32_out);
  or or_46 (or_46_out, not_259_out, not_277_out, not_278_out);
  and and_47 (ARGC_3t, or_46_out, INSTRUCTION[3]);
  not not_279 (not_279_out, not_121_out);
  not not_280 (not_280_out, not_35_out);
  not not_281 (not_281_out, not_124_out);
  nor nor_23 (nor_23_out, not_280_out, not_279_out, not_281_out);
  nor nor_24 (nor_24_out, not_260_out, not_34_out);
  nand nand_21 (UNUSEDt, not_239_out, not_238_out);
  nor nor_25 (nor_25_out, nor_6_out[0], not_261_out, not_34_out);
  nor nor_26 (nor_26_out, not_262_out, not_34_out);
  not not_282 (not_282_out, not_40_out);
  and and_48 (and_48_out, and_30_out, not_41_out);
  nor nor_27 (ARGC_3t, and_48_out, not_215_out);
  and and_49 (and_49_out, not_45_out, not_44_out);
  and and_50 (and_50_out, and_49_out, not_132_out);
  nor nor_28 (nor_28_out, nor_8_out[0], INSTRUCTION[3], not_43_out);
  nor nor_29 (UNUSEDt, not_264_out, not_43_out);
  nor nor_30 (nor_30_out, not_266_out, not_43_out);
  and and_51 (and_51_out, not_265_out, not_243_out);
  or or_47 (or_47_out, and_32_out, not_218_out);
  nor nor_31 (nor_31_out, not_267_out, not_47_out);
  and and_52 (and_52_out, not_248_out, not_247_out);
  not not_283 (not_283_out, and_52_out);
  D_Flip_Flop d_ff_6 (.Q(d_ff_6_q), .preset(or_36_out), .reset(and_54_out));  // open: clk, D, Qn
  and and_53 (and_53_out, d_ff_6_q, CLOCK);
  and and_54 (and_54_out, and_76_out, not_284_out);
  not not_284 (not_284_out, CLOCK);
  not not_285 (not_285_out, INSTRUCTION[7]);
  not not_286 (not_286_out, ALU_OPC[2]);
  and and_55 (and_55_out, not_285_out, not_286_out, ALU_OPC[1], ALU_OPC[0]);
  not not_287 (not_287_out, INSTRUCTION[3]);
  and and_56 (and_56_out, and_55_out, not_287_out);
  or or_48 (or_48_out, and_34_out, and_20_out);
  or or_49 (or_49_out, and_56_out, or_48_out);
  not not_288 (not_288_out, not_287_out);
  and and_57 (and_57_out, and_55_out, not_288_out);
  or or_50 (UNUSED, and_20_out, and_22_out);
  nor nor_32 (nor_32_out, not_4_out, not_166_out);
  nor nor_33 (nor_33_out, not_4_out, not_167_out);
  // NOR_Gate nor_34 has open pins: in0=and_36_out, in1=and_14_out, out=open
  // NOR_Gate nor_35 has open pins: in0=and_36_out, in1=and_15_out, out=open
  and and_58 (and_58_out, not_71_out, not_5_out, not_72_out, not_70_out);
  or or_51 (or_51_out, and_58_out, and_16_out);
  nor nor_36 (nor_36_out, and_58_out, and_23_out);
  or or_52 (or_52_out, and_38_out, nand_9_out);
  and and_59 (and_59_out, not_145_out, not_142_out, not_146_out);
  and and_60 (and_60_out, not_74_out, not_142_out);
  or or_53 (or_53_out, and_60_out, nand_13_out);
  and and_61 (and_61_out, not_80_out, not_78_out, not_81_out);
  nor nor_37 (nor_37_out, and_61_out, and_25_out);
  or or_54 (or_54_out, and_39_out, nand_10_out);
  not not_289 (not_289_out, or_42_out);
  and and_62 (and_62_out, not_86_out, not_84_out, not_87_out);
  nor nor_38 (nor_38_out, and_62_out, and_26_out);
  or or_55 (or_55_out, and_40_out, not_191_out);
  not not_290 (not_290_out, or_43_out);
  and and_63 (and_63_out, not_91_out, not_90_out, not_92_out);
  nor nor_39 (nor_39_out, and_63_out, and_27_out);
  or or_56 (or_56_out, and_41_out, not_221_out);
  and and_64 (and_64_out, nand_18_out, not_257_out);
  not not_291 (not_291_out, not_104_out);
  and and_65 (and_65_out, nor_21_out, not_107_out);
  nor nor_40 (nor_40_out, and_65_out, and_28_out);
  or or_57 (or_57_out, and_43_out, nand_12_out);
  nor nor_41 (ARGC_3t, and_45_out, not_225_out);
  and and_66 (and_66_out, not_35_out, not_121_out);
  and and_67 (and_67_out, and_66_out, not_124_out);
  nor nor_42 (ARGC_3t, nor_23_out, not_213_out);
  not not_292 (not_292_out, not_38_out);
  not not_293 (not_293_out, not_41_out);
  or or_58 (or_58_out, not_282_out, not_292_out);
  or or_59 (or_59_out, or_58_out, not_293_out);
  nand nand_22 (nand_22_out, or_59_out, INSTRUCTION[3]);
  nor nor_43 (ARGC_3t, and_50_out, not_217_out);
  not not_294 (not_294_out, and_51_out);
  Register #(.trigger("high")) register_1 (
    .D(DAT), .en(and_72_out), .clk(CLOCK), .Q({INSTRUCTION[7], ALU_OPC, INSTRUCTION[3:0]}), .clr(and_76_out));
  Register #(.trigger("high")) register_2 (.D(DAT), .en(and_73_out), .clk(CLOCK), .Q(register_2_q), .clr(and_76_out));
  Register #(.trigger("high")) register_3 (.D(DAT), .en(and_74_out), .clk(CLOCK), .Q(register_3_q), .clr(and_76_out));
  and and_68 (and_68_out, not_268_out, not_314_out);
  not not_295 (not_295_out, CLOCK);
  D_Flip_Flop d_ff_7 (.Q(d_ff_7_q), .Qn(d_ff_7_qn), .preset(and_53_out), .reset(and_69_out));  // open: clk, D
  and and_69 (and_69_out, d_ff_8_q, CLOCK);
  not not_296 (not_296_out, INSTRUCTION[7]);
  not not_297 (not_297_out, INSTRUCTION[3]);
  not not_298 (not_298_out, ALU_OPC[0]);
  not not_299 (not_299_out, ALU_OPC[1]);
  and and_70 (and_70_out, not_296_out, ALU_OPC[2], not_297_out, not_299_out, not_298_out);
  not not_300 (not_300_out, or_34_out);
  and and_71 (and_71_out, or_39_out, or_51_out);
  nand nand_23 (nand_23_out, or_39_out, or_40_out);
  nor nor_44 (nor_44_out, and_59_out, and_24_out);
  not not_301 (not_301_out, or_41_out);
  not not_302 (not_302_out, or_44_out);
  _7427 u_7427_1 ();  // open: pin1, pin2, pin3, pin4, pin5, pin6, pin13, pin12, pin11, pin10, pin9, pin8
  _7402 u_7402_1 ();  // open: pin1, pin2, pin3, pin4, pin5, pin6, pin13, pin12, pin11, pin10, pin9, pin8
  not not_303 (not_303_out, nand_22_out);
  and and_72 (and_72_out, and_75_out, decoder_32_out0);
  and and_73 (and_73_out, and_75_out, decoder_32_out1);
  and and_74 (and_74_out, and_75_out, decoder_32_out2);
  and and_75 (and_75_out, not_314_out, STB_BUFF);
  Counter #(.max('h3), .width(2)) counter_1 (
    .load(1'b0), .count(and_68_out), .Q(counter_1_q), .up(1'b1), .clk(not_295_out), .clr(and_76_out));  // open: D, carry
  not not_304 (not_304_out, CLOCK);
  and and_76 (and_76_out, not_304_out, d_ff_7_q);
  not not_305 (not_305_out, INSTRUCTION[7]);
  not not_306 (not_306_out, ALU_OPC[1]);
  and and_77 (and_77_out, not_305_out, ALU_OPC[2], not_306_out, ALU_OPC[0]);
  and and_78 (and_78_out, and_70_out, not_300_out);
  not not_307 (not_307_out, INSTRUCTION[3]);
  or or_60 (or_60_out, and_78_out, or_49_out);
  or or_61 (or_61_out, and_35_out, and_57_out);
  not not_308 (not_308_out, not_307_out);
  and and_79 (and_79_out, and_70_out, or_34_out);
  or or_62 (or_62_out, and_79_out, or_38_out);
  nor nor_45 (nor_45_out, not_57_out, not_166_out);
  nor nor_46 (nor_46_out, not_57_out, not_167_out);
  or or_63 (or_63_out, not_100_out, and_18_out);
  nor nor_47 (nor_47_out, not_116_out, not_201_out);
  nor nor_48 (nor_48_out, not_119_out, not_207_out);
  _7427 u_7427_2 ();  // open: pin1, pin2, pin3, pin4, pin5, pin6, pin13, pin12, pin11, pin10, pin9, pin8
  _7400 u_7400_1 ();  // open: pin1, pin2, pin3, pin4, pin5, pin6, pin13, pin12, pin11, pin10, pin9, pin8
  _7402 u_7402_2 ();  // open: pin1, pin2, pin3, pin4, pin5, pin6, pin13, pin12, pin11, pin10, pin9, pin8
  _7404 u_7404_1 ();  // open: pin1, pin2, pin3, pin4, pin5, pin6, pin13, pin12, pin11, pin10, pin9, pin8
  _7432 u_7432_1 ();  // open: pin1, pin2, pin3, pin4, pin5, pin6, pin13, pin12, pin11, pin10, pin9, pin8
  _7408 u_7408_1 ();  // open: pin1, pin2, pin3, pin4, pin5, pin6, pin13, pin12, pin11, pin10, pin9, pin8
  nor nor_49 (nor_49_out, not_125_out, not_213_out);
  _7400 u_7400_2 ();  // open: pin1, pin2, pin3, pin4, pin5, pin6, pin13, pin12, pin11, pin10, pin9, pin8
  _7404 u_7404_2 ();  // open: pin1, pin2, pin3, pin4, pin5, pin6, pin13, pin12, pin11, pin10, pin9, pin8
  _7432 u_7432_2 ();  // open: pin1, pin2, pin3, pin4, pin5, pin6, pin13, pin12, pin11, pin10, pin9, pin8
  _7408 u_7408_2 ();  // open: pin1, pin2, pin3, pin4, pin5, pin6, pin13, pin12, pin11, pin10, pin9, pin8
  nor nor_50 (nor_50_out, not_128_out, not_215_out);
  nor nor_51 (nor_51_out, not_133_out, not_217_out);
  or or_64 (or_64_out, not_49_out, not_218_out);
  nor nor_52 (nor_52_out, not_52_out, not_218_out);
  and and_80 (and_80_out, and_9_out, not_309_out);
  not not_309 (not_309_out, DBO_TRUE);
  and and_81 (and_81_out, DBO_TRUE, and_9_out);
  Decoder #(.select(2)) decoder_32 (
    .out0(decoder_32_out0), .out1(decoder_32_out1), .out2(decoder_32_out2), .out3(decoder_32_out3),
    .sel(counter_1_q), .en(1'b1));
  D_Flip_Flop d_ff_8 (.Q(d_ff_8_q), .preset(and_76_out), .reset(d_ff_7_qn));  // open: clk, D, Qn
  not not_310 (not_310_out, INSTRUCTION[7]);
  and and_82 (and_82_out, not_310_out, ALU_OPC[2], ALU_OPC[1], not_315_out);
  and and_83 (and_83_out, and_77_out, not_307_out);
  or or_65 (or_65_out, and_83_out, or_60_out);
  and and_84 (and_84_out, and_77_out, not_308_out);
  or or_66 (or_66_out, and_84_out, or_62_out);
  or or_67 (or_67_out, not_55_out, not_166_out);
  or or_68 (or_68_out, not_66_out, and_14_out);
  nor nor_53 (nor_53_out, not_62_out, and_14_out);
  // NOR_Gate nor_54 has open pins: in0=not_62_out, in1=and_15_out, out=open
  or or_69 (or_69_out, not_140_out, and_23_out);
  and and_85 (and_85_out, nor_5_out, and_24_out);
  or or_70 (or_70_out, not_147_out, and_24_out);
  and and_86 (and_86_out, and_4_out, and_25_out);
  or or_71 (or_71_out, not_150_out, and_25_out);
  or or_72 (or_72_out, not_153_out, and_26_out);
  or or_73 (or_73_out, not_157_out, and_27_out);
  nor nor_55 (nor_55_out, not_96_out, not_172_out);
  and and_87 (and_87_out, INSTRUCTION[7], nand_4_out);
  or or_74 (or_74_out, not_160_out, and_28_out);
  and and_88 (and_88_out, INSTRUCTION[7], or_17_out);
  or or_75 (or_75_out, not_114_out, not_225_out);
  and and_89 (and_89_out, not_202_out, INSTRUCTION[3]);
  and and_90 (and_90_out, INSTRUCTION[7], or_4_out);
  and and_91 (and_91_out, not_208_out, INSTRUCTION[3]);
  and and_92 (and_92_out, INSTRUCTION[7], or_6_out);
  or or_76 (or_76_out, not_122_out, not_213_out);
  nand nand_24 (nand_24_out, not_214_out, nand_6_out);
  or or_77 (or_77_out, not_39_out, not_215_out);
  nand nand_25 (nand_25_out, not_216_out, nand_1_out);
  or or_78 (or_78_out, not_130_out, not_217_out);
  not not_311 (not_311_out, or_78_out);
  or or_79 (or_79_out, INSTRUCTION[7], and_1_out);
  not not_312 (not_312_out, or_79_out);
  not not_313 (not_313_out, or_64_out);
  nor nor_56 (nor_56_out, not_53_out, and_2_out);
  and and_93 (and_93_out, ARGC_1, decoder_32_out1);
  and and_94 (and_94_out, ARGC_2, decoder_32_out2);
  and and_95 (and_95_out, ARGC_3, decoder_32_out3);
  not not_314 (not_314_out, BUFF_FULL);
  not not_315 (not_315_out, ALU_OPC[0]);
  not not_316 (not_316_out, INSTRUCTION[7]);
  and and_96 (and_96_out, not_316_out, ALU_OPC[2], ALU_OPC[1], ALU_OPC[0]);
  or or_80 (or_80_out, and_82_out, or_65_out);
  not not_317 (not_317_out, INSTRUCTION[3]);
  nor nor_57 (nor_57_out, or_67_out, nor_58_out);
  nor nor_58 (nor_58_out, or_67_out, nand_7_out);
  nor nor_59 (nor_59_out, not_143_out, not_181_out);
  nor nor_60 (nor_60_out, not_79_out, not_185_out);
  nor nor_61 (nor_61_out, not_9_out, and_86_out);
  nor nor_62 (nor_62_out, not_85_out, not_189_out);
  and and_97 (and_97_out, INSTRUCTION[7], nand_2_out);
  nor nor_63 (nor_63_out, not_155_out, not_194_out);
  and and_98 (and_98_out, INSTRUCTION[7], nand_3_out);
  or or_81 (or_81_out, nor_55_out, and_87_out);
  nor nor_64 (nor_64_out, not_105_out, not_199_out);
  and and_99 (and_99_out, INSTRUCTION[7], nand_5_out);
  nor nor_65 (nor_65_out, not_111_out, not_225_out);
  or or_82 (ARGC_2t, and_89_out, and_90_out);
  or or_83 (ARGC_2t, and_91_out, and_92_out);
  nand nand_26 (ARGC_2t, or_76_out, nand_24_out);
  nand nand_27 (ARGC_2t, or_77_out, nand_25_out);
  or or_84 (ARGC_2t, not_311_out, not_312_out);
  nor nor_66 (nor_66_out, not_313_out, nor_56_out);
  Multiplexer #(.enable("true"), .width(3)) multiplexer_1 (
    .in0(INSTRUCTION[2:0]), .in1(register_2_q[7:5]), .out(REG_ADD), .sel(and_81_out), .en(1'b1));
  or or_85 (or_85_out, and_93_out, and_94_out, and_95_out);
  and and_100 (and_100_out, INSTRUCTION[7], ALU_OPC[2], ALU_OPC[1], ALU_OPC[0]);
  not not_318 (not_318_out, INSTRUCTION[3]);
  or or_86 (or_86_out, and_96_out, or_80_out);
  not not_319 (not_319_out, not_318_out);
  and and_101 (and_101_out, and_96_out, not_317_out, or_34_out);
  or or_87 (or_87_out, and_101_out, or_66_out);
  or or_88 (or_88_out, not_138_out, INSTRUCTION[7]);
  or or_89 (or_89_out, nor_59_out, nor_67_out);
  nor nor_67 (nor_67_out, not_75_out, and_85_out);
  or or_90 (or_90_out, nor_60_out, nor_61_out);
  or or_91 (or_91_out, nor_62_out, and_97_out);
  or or_92 (or_92_out, nor_63_out, and_98_out);
  nand nand_28 (nand_28_out, not_96_out, not_101_out);
  or or_93 (or_93_out, nor_64_out, and_99_out);
  or or_94 (ARGC_2t, nor_65_out, and_88_out);
  _7404 u_7404_3 ();  // open: pin1, pin2, pin3, pin4, pin5, pin6, pin13, pin12, pin11, pin10, pin9, pin8
  _7400 u_7400_3 ();  // open: pin1, pin2, pin3, pin4, pin5, pin6, pin13, pin12, pin11, pin10, pin9, pin8
  _7402 u_7402_3 ();  // open: pin1, pin2, pin3, pin4, pin5, pin6, pin13, pin12, pin11, pin10, pin9, pin8
  _7408 u_7408_3 ();  // open: pin1, pin2, pin3, pin4, pin5, pin6, pin13, pin12, pin11, pin10, pin9, pin8
  _7432 u_7432_3 ();  // open: pin1, pin2, pin3, pin4, pin5, pin6, pin13, pin12, pin11, pin10, pin9, pin8
  _7432 u_7432_4 ();  // open: pin1, pin2, pin3, pin4, pin5, pin6, pin13, pin12, pin11, pin10, pin9, pin8
  _7427 u_7427_3 ();  // open: pin1, pin2, pin3, pin4, pin5, pin6, pin13, pin12, pin11, pin10, pin9, pin8
  _7402 u_7402_4 ();  // open: pin1, pin2, pin3, pin4, pin5, pin6, pin13, pin12, pin11, pin10, pin9, pin8
  _7432 u_7432_5 ();  // open: pin1, pin2, pin3, pin4, pin5, pin6, pin13, pin12, pin11, pin10, pin9, pin8
  _7408 u_7408_4 ();  // open: pin1, pin2, pin3, pin4, pin5, pin6, pin13, pin12, pin11, pin10, pin9, pin8
  _7427 u_7427_4 ();  // open: pin1, pin2, pin3, pin4, pin5, pin6, pin13, pin12, pin11, pin10, pin9, pin8
  _7402 u_7402_5 ();  // open: pin1, pin2, pin3, pin4, pin5, pin6, pin13, pin12, pin11, pin10, pin9, pin8
  _7432 u_7432_6 ();  // open: pin1, pin2, pin3, pin4, pin5, pin6, pin13, pin12, pin11, pin10, pin9, pin8
  _7408 u_7408_5 ();  // open: pin1, pin2, pin3, pin4, pin5, pin6, pin13, pin12, pin11, pin10, pin9, pin8
  assign MBUS_DOUT = and_8_out ? DAT : 8'bz;  // Controlled_Buffer controlled_buffer_1
  or or_95 (BUFF_FULL, and_102_out, or_85_out);
  and and_102 (and_102_out, decoder_32_out0, or_96_out);
  or or_96 (or_96_out, latch_3_dout, latch_1_dout, latch_2_dout);
  and and_103 (and_103_out, and_100_out, not_318_out);
  or or_97 (or_97_out, and_103_out, or_86_out);
  or or_98 (or_98_out, or_61_out, and_104_out);
  and and_104 (and_104_out, and_100_out, not_319_out);
  and and_105 (and_105_out, and_100_out, or_34_out);
  not not_320 (not_320_out, INSTRUCTION[7]);
  or or_99 (or_99_out, not_138_out, not_320_out);
  // NOR_Gate nor_68 has open pins: in0=or_88_out, in1=not_173_out, out=open
  nand nand_29 (nand_29_out, not_141_out, not_139_out, not_140_out, and_71_out);
  and and_106 (and_106_out, not_70_out, not_141_out);
  or or_100 (or_100_out, and_106_out, not_176_out);
  and and_107 (and_107_out, not_143_out, not_148_out);
  and and_108 (and_108_out, not_79_out, not_151_out);
  or or_101 (or_101_out, and_108_out, not_184_out);
  and and_109 (and_109_out, not_85_out, not_154_out);
  or or_102 (or_102_out, and_109_out, not_188_out);
  nand nand_30 (nand_30_out, not_155_out, not_158_out);
  nand nand_31 (nand_31_out, nand_30_out, not_222_out);
  nand nand_32 (nand_32_out, nand_28_out, not_223_out);
  not not_321 (not_321_out, or_29_out);
  nand nand_33 (nand_33_out, not_105_out, not_161_out);
  nand nand_34 (nand_34_out, nand_33_out, not_224_out);
  or or_103 (ILLEGALt, nor_47_out, nor_13_out);
  or or_104 (ILLEGALt, nor_48_out, nor_14_out);
  or or_105 (ILLEGALt, nor_49_out, nor_24_out);
  _7404 u_7404_4 ();  // open: pin1, pin2, pin3, pin4, pin5, pin6, pin13, pin12, pin11, pin10, pin9, pin8
  or or_106 (or_106_out, nor_50_out, nor_15_out);
  _7404 u_7404_5 ();  // open: pin1, pin2, pin3, pin4, pin5, pin6, pin13, pin12, pin11, pin10, pin9, pin8
  or or_107 (or_107_out, nor_51_out, nor_28_out);
  or or_108 (or_108_out, nor_52_out, nor_31_out);
  and and_110 (RDY, decoder_32_out0, not_322_out);
  not not_322 (not_322_out, BUFF_FULL);
  and and_111 (and_111_out, latch_2_dout, not_323_out);
  not not_323 (not_323_out, latch_3_dout);
  and and_112 (and_112_out, latch_3_dout, not_324_out);
  not not_324 (not_324_out, latch_1_dout);
  or or_109 (ERR, and_105_out, or_87_out);
  nand nand_35 (nand_35_out, or_100_out, or_69_out, or_52_out, or_40_out);
  or or_110 (or_110_out, and_107_out, not_180_out);
  and and_113 (and_113_out, or_101_out, or_71_out, or_54_out);
  nand nand_36 (nand_36_out, or_102_out, or_72_out, or_55_out, not_290_out);
  nand nand_37 (nand_37_out, nand_31_out, or_73_out, or_56_out, not_302_out);
  nand nand_38 (nand_38_out, nand_32_out, or_63_out, or_45_out, not_321_out);
  nand nand_39 (nand_39_out, nand_34_out, or_74_out, or_57_out, or_31_out);
  nand nand_40 (ILLEGALt, or_75_out, nand_19_out);
  nor nor_69 (ARGC_1t, ARGC_2t, ARGC_3t);
  _7410 u_7410_1 ();  // open: pin1, pin2, pin3, pin4, pin5, pin6, pin13, pin12, pin11, pin10, pin9, pin8
  _7404 u_7404_6 ();  // open: pin1, pin2, pin3, pin4, pin5, pin6, pin13, pin12, pin11, pin10, pin9, pin8
  nor nor_70 (ARGC_1t, ARGC_2t, ARGC_3t);
  _7427 u_7427_5 ();  // open: pin1, pin2, pin3, pin4, pin5, pin6, pin13, pin12, pin11, pin10, pin9, pin8
  _7400 u_7400_4 ();  // open: pin1, pin2, pin3, pin4, pin5, pin6, pin13, pin12, pin11, pin10, pin9, pin8
  _7402 u_7402_6 ();  // open: pin1, pin2, pin3, pin4, pin5, pin6, pin13, pin12, pin11, pin10, pin9, pin8
  _7404 u_7404_7 ();  // open: pin1, pin2, pin3, pin4, pin5, pin6, pin13, pin12, pin11, pin10, pin9, pin8
  nor nor_71 (ARGC_1t, ARGC_2t, ARGC_3t);
  or or_111 (or_111_out, ~nor_66_out, ~or_47_out);  // OR_Gate
  assign ARG_8BIT = and_80_out ? register_2_q : 8'bz;  // Controlled_Buffer controlled_buffer_2
  assign ARG_16BIT = ARG2_E ? {register_3_q, register_2_q} : 16'bz;  // Controlled_Buffer controlled_buffer_3
  and and_114 (RST_T, and_102_out, and_111_out);
  and and_115 (IRQ_T, and_102_out, and_112_out);
  and and_116 (NMI_T, and_102_out, latch_1_dout);
  and and_117 (ARGC_1, or_97_out, not_325_out);
  nor nor_72 (nor_72_out, or_97_out, or_98_out);
  and and_118 (ARGC_2, nor_72_out, not_325_out);
  and and_119 (ARGC_3, or_98_out, not_325_out);
  not not_325 (not_325_out, ERR);
  nor nor_73 (nor_73_out, undriven, undriven_2);
  nor nor_74 (nor_74_out, nand_29_out, nor_36_out);
  nand nand_41 (nand_41_out, or_110_out, or_70_out, or_53_out, not_301_out);
  nor nor_75 (nor_75_out, or_90_out, nor_37_out);
  nand nand_42 (nand_42_out, and_113_out, not_289_out);
  nor nor_76 (nor_76_out, or_91_out, nor_38_out);
  nor nor_77 (nor_77_out, or_92_out, nor_39_out);
  nor nor_78 (nor_78_out, or_81_out, and_64_out);
  nor nor_79 (nor_79_out, or_93_out, nor_40_out);
  nor nor_80 (ARGC_1t, ARGC_2t, ARGC_3t);
  _7400 u_7400_5 ();  // open: pin1, pin2, pin3, pin4, pin5, pin6, pin13, pin12, pin11, pin10, pin9, pin8
  _7402 u_7402_7 ();  // open: pin1, pin2, pin3, pin4, pin5, pin6, pin13, pin12, pin11, pin10, pin9, pin8
  _7408 u_7408_6 ();  // open: pin1, pin2, pin3, pin4, pin5, pin6, pin13, pin12, pin11, pin10, pin9, pin8
  _7432 u_7432_7 ();  // open: pin1, pin2, pin3, pin4, pin5, pin6, pin13, pin12, pin11, pin10, pin9, pin8
  _7427 u_7427_6 ();  // open: pin1, pin2, pin3, pin4, pin5, pin6, pin13, pin12, pin11, pin10, pin9, pin8
  _7400 u_7400_6 ();  // open: pin1, pin2, pin3, pin4, pin5, pin6, pin13, pin12, pin11, pin10, pin9, pin8
  _7402 u_7402_8 ();  // open: pin1, pin2, pin3, pin4, pin5, pin6, pin13, pin12, pin11, pin10, pin9, pin8
  _7404 u_7404_8 ();  // open: pin1, pin2, pin3, pin4, pin5, pin6, pin13, pin12, pin11, pin10, pin9, pin8
  _7432 u_7432_8 ();  // open: pin1, pin2, pin3, pin4, pin5, pin6, pin13, pin12, pin11, pin10, pin9, pin8
  nor nor_81 (ARGC_1t, ARGC_2t, ARGC_3t);
  _7432 u_7432_9 ();  // open: pin1, pin2, pin3, pin4, pin5, pin6, pin13, pin12, pin11, pin10, pin9, pin8
  nor nor_82 (ARGC_1t, ARGC_2t, ARGC_3t);
  nor nor_83 (nor_83_out, or_89_out, nor_44_out);
  _7427 u_7427_7 ();  // open: pin1, pin2, pin3, pin4, pin5, pin6, pin13, pin12, pin11, pin10, pin9, pin8
  _7402 u_7402_9 ();  // open: pin1, pin2, pin3, pin4, pin5, pin6, pin13, pin12, pin11, pin10, pin9, pin8
  _7404 u_7404_9 ();  // open: pin1, pin2, pin3, pin4, pin5, pin6, pin13, pin12, pin11, pin10, pin9, pin8
  _7432 u_7432_10 ();  // open: pin1, pin2, pin3, pin4, pin5, pin6, pin13, pin12, pin11, pin10, pin9, pin8
  _7408 u_7408_7 ();  // open: pin1, pin2, pin3, pin4, pin5, pin6, pin13, pin12, pin11, pin10, pin9, pin8
  _7420 u_7420_1 ();  // open: pin1, pin2, pin3, pin4, pin5, pin6, pin13, pin12, pin11, pin10, pin9, pin8
  _7421 u_7421_1 ();  // open: pin1, pin2, pin3, pin4, pin5, pin6, pin13, pin12, pin11, pin10, pin9, pin8
  _7432 u_7432_11 ();  // open: pin1, pin2, pin3, pin4, pin5, pin6, pin13, pin12, pin11, pin10, pin9, pin8
  _7432 u_7432_12 ();  // open: pin1, pin2, pin3, pin4, pin5, pin6, pin13, pin12, pin11, pin10, pin9, pin8
  _7402 u_7402_10 ();  // open: pin1, pin2, pin3, pin4, pin5, pin6, pin13, pin12, pin11, pin10, pin9, pin8
  _7408 u_7408_8 ();  // open: pin1, pin2, pin3, pin4, pin5, pin6, pin13, pin12, pin11, pin10, pin9, pin8
  _7408 u_7408_9 ();  // open: pin1, pin2, pin3, pin4, pin5, pin6, pin13, pin12, pin11, pin10, pin9, pin8
  _7400 u_7400_7 ();  // open: pin1, pin2, pin3, pin4, pin5, pin6, pin13, pin12, pin11, pin10, pin9, pin8
  _7404 u_7404_10 ();  // open: pin1, pin2, pin3, pin4, pin5, pin6, pin13, pin12, pin11, pin10, pin9, pin8
  _7402 u_7402_11 ();  // open: pin1, pin2, pin3, pin4, pin5, pin6, pin13, pin12, pin11, pin10, pin9, pin8
  _7408 u_7408_10 ();  // open: pin1, pin2, pin3, pin4, pin5, pin6, pin13, pin12, pin11, pin10, pin9, pin8
  _7432 u_7432_13 ();  // open: pin1, pin2, pin3, pin4, pin5, pin6, pin13, pin12, pin11, pin10, pin9, pin8
  _7404 u_7404_11 ();  // open: pin1, pin2, pin3, pin4, pin5, pin6, pin13, pin12, pin11, pin10, pin9, pin8
  _7411 u_7411_1 ();  // open: pin1, pin2, pin3, pin4, pin5, pin6, pin13, pin12, pin11, pin10, pin9, pin8
  _7402 u_7402_12 ();  // open: pin1, pin2, pin3, pin4, pin5, pin6, pin13, pin12, pin11, pin10, pin9, pin8
  _7408 u_7408_11 ();  // open: pin1, pin2, pin3, pin4, pin5, pin6, pin13, pin12, pin11, pin10, pin9, pin8
  _7432 u_7432_14 ();  // open: pin1, pin2, pin3, pin4, pin5, pin6, pin13, pin12, pin11, pin10, pin9, pin8
  _7420 u_7420_2 ();  // open: pin1, pin2, pin3, pin4, pin5, pin6, pin13, pin12, pin11, pin10, pin9, pin8
  _7404 u_7404_12 ();  // open: pin1, pin2, pin3, pin4, pin5, pin6, pin13, pin12, pin11, pin10, pin9, pin8
  _7411 u_7411_2 ();  // open: pin1, pin2, pin3, pin4, pin5, pin6, pin13, pin12, pin11, pin10, pin9, pin8
  _7402 u_7402_13 ();  // open: pin1, pin2, pin3, pin4, pin5, pin6, pin13, pin12, pin11, pin10, pin9, pin8
  _7408 u_7408_12 ();  // open: pin1, pin2, pin3, pin4, pin5, pin6, pin13, pin12, pin11, pin10, pin9, pin8
  _7432 u_7432_15 ();  // open: pin1, pin2, pin3, pin4, pin5, pin6, pin13, pin12, pin11, pin10, pin9, pin8
  _7420 u_7420_3 ();  // open: pin1, pin2, pin3, pin4, pin5, pin6, pin13, pin12, pin11, pin10, pin9, pin8
  _7404 u_7404_13 ();  // open: pin1, pin2, pin3, pin4, pin5, pin6, pin13, pin12, pin11, pin10, pin9, pin8
  _7402 u_7402_14 ();  // open: pin1, pin2, pin3, pin4, pin5, pin6, pin13, pin12, pin11, pin10, pin9, pin8
  _7408 u_7408_13 ();  // open: pin1, pin2, pin3, pin4, pin5, pin6, pin13, pin12, pin11, pin10, pin9, pin8
  _7432 u_7432_16 ();  // open: pin1, pin2, pin3, pin4, pin5, pin6, pin13, pin12, pin11, pin10, pin9, pin8
  _7420 u_7420_4 ();  // open: pin1, pin2, pin3, pin4, pin5, pin6, pin13, pin12, pin11, pin10, pin9, pin8
  _7404 u_7404_14 ();  // open: pin1, pin2, pin3, pin4, pin5, pin6, pin13, pin12, pin11, pin10, pin9, pin8
  _7402 u_7402_15 ();  // open: pin1, pin2, pin3, pin4, pin5, pin6, pin13, pin12, pin11, pin10, pin9, pin8
  _7408 u_7408_14 ();  // open: pin1, pin2, pin3, pin4, pin5, pin6, pin13, pin12, pin11, pin10, pin9, pin8
  _7432 u_7432_17 ();  // open: pin1, pin2, pin3, pin4, pin5, pin6, pin13, pin12, pin11, pin10, pin9, pin8
  _7400 u_7400_8 ();  // open: pin1, pin2, pin3, pin4, pin5, pin6, pin13, pin12, pin11, pin10, pin9, pin8
  _7432 u_7432_18 ();  // open: pin1, pin2, pin3, pin4, pin5, pin6, pin13, pin12, pin11, pin10, pin9, pin8
  _7400 u_7400_9 ();  // open: pin1, pin2, pin3, pin4, pin5, pin6, pin13, pin12, pin11, pin10, pin9, pin8
  _7420 u_7420_5 ();  // open: pin1, pin2, pin3, pin4, pin5, pin6, pin13, pin12, pin11, pin10, pin9, pin8
  _7404 u_7404_15 ();  // open: pin1, pin2, pin3, pin4, pin5, pin6, pin13, pin12, pin11, pin10, pin9, pin8
  _7402 u_7402_16 ();  // open: pin1, pin2, pin3, pin4, pin5, pin6, pin13, pin12, pin11, pin10, pin9, pin8
  _7408 u_7408_15 ();  // open: pin1, pin2, pin3, pin4, pin5, pin6, pin13, pin12, pin11, pin10, pin9, pin8
  _7432 u_7432_19 ();  // open: pin1, pin2, pin3, pin4, pin5, pin6, pin13, pin12, pin11, pin10, pin9, pin8
  _7400 u_7400_10 ();  // open: pin1, pin2, pin3, pin4, pin5, pin6, pin13, pin12, pin11, pin10, pin9, pin8
  _7432 u_7432_20 ();  // open: pin1, pin2, pin3, pin4, pin5, pin6, pin13, pin12, pin11, pin10, pin9, pin8
  _7411 u_7411_3 ();  // open: pin1, pin2, pin3, pin4, pin5, pin6, pin13, pin12, pin11, pin10, pin9, pin8
  _7413 u_7413_1 ();  // open: pin1, pin2, pin3, pin4, pin5, pin6, pin13, pin12, pin11, pin10, pin9, pin8
  _7432 u_7432_21 ();  // open: pin1, pin2, pin3, pin4, pin5, pin6, pin13, pin12, pin11, pin10, pin9, pin8
  _7400 u_7400_11 ();  // open: pin1, pin2, pin3, pin4, pin5, pin6, pin13, pin12, pin11, pin10, pin9, pin8
  _7432 u_7432_22 ();  // open: pin1, pin2, pin3, pin4, pin5, pin6, pin13, pin12, pin11, pin10, pin9, pin8
  _7400 u_7400_12 ();  // open: pin1, pin2, pin3, pin4, pin5, pin6, pin13, pin12, pin11, pin10, pin9, pin8
  _7408 u_7408_16 ();  // open: pin1, pin2, pin3, pin4, pin5, pin6, pin13, pin12, pin11, pin10, pin9, pin8
  _7432 u_7432_23 ();  // open: pin1, pin2, pin3, pin4, pin5, pin6, pin13, pin12, pin11, pin10, pin9, pin8
  _7411 u_7411_4 ();  // open: pin1, pin2, pin3, pin4, pin5, pin6, pin13, pin12, pin11, pin10, pin9, pin8
  _7400 u_7400_13 ();  // open: pin1, pin2, pin3, pin4, pin5, pin6, pin13, pin12, pin11, pin10, pin9, pin8
  _7404 u_7404_16 (
    .pin11(n7404_16_pin11), .pin10(n7404_16_pin11), .pin9(n7404_16_pin9), .pin8(n7404_16_pin9));  // open: pin1, pin2, pin3, pin4, pin5, pin6, pin13, pin12
  _7400 u_7400_14 ();  // open: pin1, pin2, pin3, pin4, pin5, pin6, pin13, pin12, pin11, pin10, pin9, pin8
  _7402 u_7402_17 ();  // open: pin1, pin2, pin3, pin4, pin5, pin6, pin13, pin12, pin11, pin10, pin9, pin8
  _7408 u_7408_17 ();  // open: pin1, pin2, pin3, pin4, pin5, pin6, pin13, pin12, pin11, pin10, pin9, pin8
  _7432 u_7432_24 ();  // open: pin1, pin2, pin3, pin4, pin5, pin6, pin13, pin12, pin11, pin10, pin9, pin8
  _7432 u_7432_25 ();  // open: pin1, pin2, pin3, pin4, pin5, pin6, pin13, pin12, pin11, pin10, pin9, pin8
  _7404 u_7404_17 ();  // open: pin1, pin2, pin3, pin4, pin5, pin6, pin13, pin12, pin11, pin10, pin9, pin8

  assign INSTRUCTION[6:4] = ALU_OPC;
  assign INT_VAL = INSTRUCTION[0];

  // Other names for the same wires on the sheet: OP_COUNT_DECODE[7:0] = {INSTRUCTION[7], ALU_OPC, INSTRUCTION[3:0]};
  //   ILLEGAL = ERR; STORE_BUFF = STB_BUFF

  // Notes on the sheet:
  //   bit y should not be dependent on regad
endmodule

module Addressing_Module (
  input  CLOCK,
  input  [15:0] BIT16_D,
  input  [15:0] SP_16bit,
  input  MASpec,
  input  READ,
  input  WRITE,
  input  [7:0] DATA_IN,
  output [15:0] ADDRESS_OUT,
  output [7:0] DATA_OUT,
  output READ_OUT,
  output WRITE_OUT
);

  wire latch_1_dout, latch_3_dout, not_1_out, or_1_out;
  wire [15:0] controlled_buffer_1_out;

  Latch latch_1 (.DOUT(latch_1_dout), .LOCK_E(CLOCK), .DIN(MASpec));
  Latch latch_2 (.DOUT(READ_OUT), .LOCK_E(CLOCK), .DIN(READ));
  Latch latch_3 (.DOUT(latch_3_dout), .LOCK_E(CLOCK), .DIN(WRITE));
  not not_1 (not_1_out, latch_1_dout);
  assign controlled_buffer_1_out = latch_1_dout ? BIT16_D : 16'bz;  // Controlled_Buffer controlled_buffer_1
  assign controlled_buffer_1_out = not_1_out ? SP_16bit : 16'bz;  // Controlled_Buffer controlled_buffer_2
  Pull_Resistor pull_resistor_1 (.node(controlled_buffer_1_out));
  assign DATA_OUT = latch_3_dout ? DATA_IN : 8'bz;  // Controlled_Buffer controlled_buffer_3
  Pull_Resistor pull_resistor_2 (.node(ADDRESS_OUT));
  assign ADDRESS_OUT = or_1_out ? controlled_buffer_1_out : 16'bz;  // Controlled_Buffer controlled_buffer_4
  Pull_Resistor pull_resistor_3 (.node(DATA_OUT));
  and and_1 (WRITE_OUT, latch_3_dout, CLOCK);
  or or_1 (or_1_out, READ_OUT, latch_3_dout);
endmodule

module AUX_Registers (
  input  CLOCK,
  input  RESET,
  input  EChangePC,
  input  IN_DEC_PC,
  input  LOAD_COUNT,
  input  [15:0] IMM16_DATA,
  input  PC_EH,
  input  PC_EL,
  input  IN_DEC_SP,
  input  EChangeSP,
  output [15:0] PC_OUT,
  output [15:0] SP_OUT,
  output [7:0] PC_HOUT,
  output [7:0] PC_LOUT
);

  wire and_1_out, and_2_out, and_3_out, latch_1_dout, latch_2_dout, latch_3_dout, latch_4_dout, latch_5_dout,
       latch_6_dout, latch_7_dout, latch_8_dout, not_1_out, not_2_out;
  wire [15:0] PC_q, register_1_q;

  Latch latch_1 (.DOUT(latch_1_dout), .LOCK_E(CLOCK), .DIN(RESET));
  Latch latch_2 (.DOUT(latch_2_dout), .LOCK_E(CLOCK), .DIN(EChangePC));
  Latch latch_3 (.DOUT(latch_3_dout), .LOCK_E(CLOCK), .DIN(IN_DEC_PC));
  Latch latch_4 (.DOUT(latch_4_dout), .LOCK_E(CLOCK), .DIN(LOAD_COUNT));
  Latch latch_5 (.DOUT(latch_5_dout), .LOCK_E(CLOCK), .DIN(PC_EH));
  Latch latch_6 (.DOUT(latch_6_dout), .LOCK_E(CLOCK), .DIN(PC_EL));
  Latch latch_7 (.DOUT(latch_7_dout), .LOCK_E(CLOCK), .DIN(IN_DEC_SP));
  Latch latch_8 (.DOUT(latch_8_dout), .LOCK_E(CLOCK), .DIN(EChangeSP));
  and and_1 (and_1_out, latch_5_dout, latch_6_dout);
  not not_1 (not_1_out, and_1_out);
  and and_2 (and_2_out, not_1_out, latch_5_dout);
  and and_3 (and_3_out, not_1_out, latch_6_dout);
  Counter #(.max('hffff), .width(16)) PC (
    .load(latch_4_dout), .up(latch_3_dout), .count(latch_2_dout), .clk(CLOCK), .D(IMM16_DATA), .Q(PC_q));  // open: clr, carry
  Counter SP (
    .clr(latch_1_dout), .load(1'b0), .up(latch_7_dout), .count(latch_8_dout), .clk(CLOCK), .Q(SP_OUT[7:0]));  // open: D, carry
  not not_2 (not_2_out, CLOCK);
  Register #(.trigger("high"), .width(16)) register_1 (
    .D(PC_q), .en(not_2_out), .clk(not_2_out), .Q(register_1_q));  // open: clr
  assign PC_HOUT = and_2_out ? register_1_q[15:8] : 8'bz;  // Controlled_Buffer controlled_buffer_1
  assign PC_LOUT = and_3_out ? register_1_q[7:0] : 8'bz;  // Controlled_Buffer controlled_buffer_2
  assign PC_OUT = and_1_out ? register_1_q : 16'bz;  // Controlled_Buffer controlled_buffer_3

  assign SP_OUT[15:8] = 8'hfe;
endmodule

module PSR_Register (
  input  INTP_D,
  input  IRQE_D,
  input  ERR_D,
  input  UN_D,
  input  INTP_E,
  input  IRQE_E,
  input  ERR_E,
  input  UN_E,
  input  CLOCK,
  input  HALT,
  input  VCC,
  input  RESET,
  output HALT_OUT,
  output VCC_OUT,
  output RESET_OUT,
  output INTP,
  output IRQE,
  output ERR,
  output UUSD,
  output PCS
);

  Register #(.trigger("high"), .width(1)) register_1 (.D(INTP_D), .en(INTP_E), .Q(INTP), .clk(CLOCK));  // open: clr
  Register #(.trigger("high"), .width(1)) register_2 (.D(IRQE_D), .en(IRQE_E), .Q(IRQE), .clk(CLOCK));  // open: clr
  Register #(.trigger("high"), .width(1)) register_3 (.D(ERR_D), .en(ERR_E), .Q(ERR), .clk(CLOCK));  // open: clr
  Register #(.trigger("high"), .width(1)) register_4 (.D(UN_D), .en(UN_E), .Q(UUSD), .clk(CLOCK));  // open: clr

  assign HALT_OUT = HALT;
  assign PCS = CLOCK;
  assign RESET_OUT = RESET;
  assign VCC_OUT = VCC;
endmodule

module CPU_CLOCK (
  input  INTERNAL_CLOCK,
  input  VCC,
  input  EXTERNAL_CLOCK,
  input  HALT_IN,
  output CLOCK_OUT
);

  wire and_1_out, and_2_out, and_3_out, not_1_out, not_2_out;

  not not_1 (not_1_out, and_2_out);
  and and_1 (and_1_out, not_1_out, HALT_IN);
  and and_2 (and_2_out, INTERNAL_CLOCK, VCC, not_2_out);
  not not_2 (not_2_out, and_1_out);
  and and_3 (and_3_out, EXTERNAL_CLOCK, VCC, and_1_out);
  or or_1 (CLOCK_OUT, and_2_out, and_3_out);
endmodule

module IO_INTERFACE (
  input  [7:0] INPUT_DATA_IN,
  input  INPUT_DECLARE_IN,
  input  [7:0] OUTPUT_DATA_IN,
  input  OUTPUT_DECLARE_IN,
  output [7:0] INPUT_DATA_OUT,
  output INPUT_DECLARE_OUT,
  output OUTPUT_DECLARE_OUT,
  output [7:0] OUTPUT_DATA_OUT
);

  wire [7:0] register_1_q, register_2_q;

  Register #(.trigger("high")) register_1 (
    .D(INPUT_DATA_IN), .en(1'b1), .clk(INPUT_DECLARE_IN), .Q(register_1_q));  // open: clr
  D_Flip_Flop d_ff_1 (
    .Q(INPUT_DECLARE_OUT), .Qn(OUTPUT_DECLARE_OUT), .preset(INPUT_DECLARE_IN), .reset(OUTPUT_DECLARE_IN));  // open: D, clk
  Register #(.trigger("high")) register_2 (
    .D(OUTPUT_DATA_IN), .en(1'b1), .clk(OUTPUT_DECLARE_IN), .Q(register_2_q));  // open: clr
  assign INPUT_DATA_OUT = INPUT_DECLARE_OUT ? register_1_q : 8'bz;  // Controlled_Buffer controlled_buffer_1
  assign OUTPUT_DATA_OUT = OUTPUT_DECLARE_OUT ? register_2_q : 8'bz;  // Controlled_Buffer controlled_buffer_2
endmodule

module CPU_BUFFER (
  input  EXTERNAL_CLOCK,
  input  [7:0] DEVICE_DATA_IN,
  input  DEVICE_INPUT,
  input  [7:0] DATA_IN,
  input  IRQ,
  input  NMI,
  input  EDAT1,
  input  EDAT2,
  input  CBUFF,
  input  RREAD,
  input  RWRITE,
  input  RHLE,
  input  LC_PC,
  input  ID_PC,
  input  PCM_E,
  input  ID_SP,
  input  SPM_E,
  input  CLCLT,
  input  FLAGS_E,
  input  LDF,
  input  LDX,
  input  LDY,
  input  MREAD,
  input  MWRITE,
  input  MDSpec,
  input  DBUS_R,
  input  DBUS_W,
  input  CLOCK,
  input  READ_INDAT,
  input  STORE_BUF_DBUS,
  input  [7:0] Data_Bus,
  input  EDAT_1,
  input  EDAT_2,
  input  Erase_Buffer,
  input  INTERRUPT,
  input  RESET,
  output [7:0] DEVICE_DATA_OUT,
  output DEVICE_OUTPUT,
  output READ_WRITE_OUT,
  output [7:0] DATA_OUT,
  output [15:0] ADDRESS_OUT,
  output [7:0] DATA_BUS_OUT,
  output [7:0] OP_0,
  output [7:0] OP_1,
  output [7:0] OP_2,
  output BUFFER_FULL,
  output READY,
  output INTERRUPT_OUT,
  output RESET_OUT
);

  wire and_1_out, and_2_out, and_3_out, and_4_out, and_5_out, and_6_out, and_7_out, and_8_out, and_9_out,
       and_10_out, and_11_out, and_12_out, and_13_out, and_14_out, and_15_out, and_16_out, and_17_out,
       and_18_out, and_19_out, and_20_out, CLOCK_t, decoder_1_out0, decoder_1_out1, decoder_1_out2,
       decoder_1_out3, HALT, Illegal, instruction_buffer_1_p6, instruction_buffer_1_p7,
       instruction_buffer_1_p8, instruction_buffer_1_p14, instruction_buffer_1_p15, instruction_buffer_1_p16,
       instruction_buffer_1_p17, instruction_buffer_1_p18, instruction_buffer_1_p19,
       io_interface_1_input_declare_out, io_interface_2_output_declare_out, Load_1, Load_2, Load_3,
       not_1_out, not_2_out, not_3_out, not_4_out, not_5_out, not_6_out, not_7_out, not_8_out, not_9_out,
       not_10_out, not_11_out, not_12_out, not_13_out, or_1_out, or_2_out, or_3_out, or_5_out, or_6_out,
       or_7_out, or_9_out, registers_1_p1, registers_1_p2, registers_1_p6, undriven, undriven_4, undriven_5,
       VCC;
  wire [1:0] counter_1_q;
  wire [2:0] ADD3_BUS;
  wire [7:0] controlled_buffer_2_out, controlled_buffer_3_out, DATA_BUS_t, instruction_buffer_1_p5,
       instruction_buffer_1_p13, io_interface_1_input_data_out, register_4_q, undriven_2, undriven_3;
  wire [15:0] ADD16_BUS, aux_registers_1_sp_out;

  not not_1 (not_1_out, instruction_buffer_1_p16);
  and and_1 (and_1_out, or_7_out, Illegal);
  // Registers registers_1: pin names not known; wires that end beside it: registers_1_p1, registers_1_p2, CLOCK_t, ADD3_BUS, DATA_BUS_t, registers_1_p6, DATA_BUS_t, ADD16_BUS
  AUX_Registers aux_registers_1 (
    .SP_OUT(aux_registers_1_sp_out), .PC_LOUT(ADD16_BUS[15:8]), .RESET(CLOCK_t), .IMM16_DATA(ADD16_BUS));  // open: PC_OUT, PC_HOUT, EChangePC, IN_DEC_PC, LOAD_COUNT, PC_EH, PC_EL, CLOCK, IN_DEC_SP, EChangeSP
  // ALU alu_1: pin names not known; wires that end beside it: CLOCK_t, registers_1_p6, DATA_BUS_t, DATA_BUS_t
  or or_1 (or_1_out, Erase_Buffer, and_2_out);
  and and_2 (and_2_out, and_1_out, not_7_out);
  not not_2 (not_2_out, OP_0[7]);
  not not_3 (not_3_out, OP_0[6]);
  not not_4 (not_4_out, OP_0[5]);
  not not_5 (not_5_out, OP_0[4]);
  and and_3 (and_3_out, OP_0[4], not_4_out, not_3_out, not_2_out);
  // Instruction_Buffer instruction_buffer_1: pin names not known; wires that end beside it: registers_1_p2, not_1_out, 1'b1, CLOCK_t, instruction_buffer_1_p5, instruction_buffer_1_p6, instruction_buffer_1_p7, instruction_buffer_1_p8, instruction_buffer_1_p6, instruction_buffer_1_p8, DATA_BUS_t, DATA_BUS_t, instruction_buffer_1_p13, instruction_buffer_1_p14, instruction_buffer_1_p15, instruction_buffer_1_p16, instruction_buffer_1_p17, instruction_buffer_1_p18, instruction_buffer_1_p19, instruction_buffer_1_p6, instruction_buffer_1_p8
  not not_6 (not_6_out, STORE_BUF_DBUS);
  and and_4 (and_4_out, READ_INDAT, STORE_BUF_DBUS);
  and and_5 (and_5_out, OP_0[4], OP_0[5], not_3_out, not_2_out);
  or or_2 (or_2_out, and_5_out, and_3_out);
  CPU_CLOCK cpu_clock_1 (
    .INTERNAL_CLOCK(VCC), .VCC(EXTERNAL_CLOCK), .EXTERNAL_CLOCK(HALT), .CLOCK_OUT(CLOCK_t));  // open: HALT_IN
  and and_6 (and_6_out, READ_INDAT, not_6_out);
  assign DATA_BUS_OUT = and_6_out ? Data_Bus : 8'bz;  // Controlled_Buffer controlled_buffer_1
  assign controlled_buffer_2_out = and_4_out ? Data_Bus : 8'bz;  // Controlled_Buffer controlled_buffer_2
  Register #(.trigger("high")) register_1 (
    .D(controlled_buffer_2_out), .en(and_7_out), .clk(CLOCK), .Q(OP_0), .clr(or_1_out));
  Pull_Resistor pull_resistor_1 (.node(controlled_buffer_2_out));
  and and_7 (and_7_out, not_8_out, decoder_1_out0);
  Register #(.trigger("high")) register_2 (
    .D(controlled_buffer_2_out), .en(and_8_out), .clk(CLOCK), .Q(OP_1), .clr(or_1_out));
  and and_8 (and_8_out, not_8_out, decoder_1_out1);
  Register #(.trigger("high")) register_3 (
    .D(controlled_buffer_2_out), .en(and_9_out), .clk(CLOCK), .Q(OP_2), .clr(or_1_out));
  and and_9 (and_9_out, not_8_out, decoder_1_out2);
  not not_7 (not_7_out, CLOCK);
  and and_10 (and_10_out, not_5_out, not_4_out, not_3_out, not_2_out);
  and and_11 (and_11_out, OP_0[4], OP_0[5], not_3_out, OP_0[7]);
  or or_3 (or_3_out, and_11_out, or_2_out);
  Controlled_Buffer #(.width(8)) controlled_buffer_3 (.in(register_4_q), .out(controlled_buffer_3_out));  // open: en
  Register register_4 (.D(DATA_BUS_t), .clk(CLOCK_t), .Q(register_4_q));  // open: en, clr
  Decoder #(.select(2)) decoder_1 (
    .out0(decoder_1_out0), .out1(decoder_1_out1), .out2(decoder_1_out2), .out3(decoder_1_out3),
    .sel(counter_1_q), .en(1'b1));
  Counter #(.max('h3), .width(2)) counter_1 (
    .load(1'b0), .count(not_8_out), .Q(counter_1_q), .up(1'b1), .clk(not_7_out), .clr(or_1_out));  // open: D, carry
  and and_12 (and_12_out, OP_0[4], not_4_out, OP_0[6], not_2_out);
  and and_13 (and_13_out, and_10_out, OP_0[3]);
  not not_8 (not_8_out, BUFFER_FULL);
  or or_4 (BUFFER_FULL, and_14_out, and_15_out, and_18_out, or_9_out);
  and and_14 (and_14_out, decoder_1_out1, Load_1);
  and and_15 (and_15_out, decoder_1_out2, Load_2);
  and and_16 (and_16_out, not_5_out, not_4_out, OP_0[6], not_2_out);
  and and_17 (and_17_out, not_5_out, OP_0[5], OP_0[6], OP_0[7]);
  or or_5 (or_5_out, and_12_out, and_13_out);
  or or_6 (or_6_out, and_17_out, or_5_out);
  assign DATA_BUS_OUT = EDAT_1 ? OP_1 : 8'bz;  // Controlled_Buffer controlled_buffer_4
  assign DATA_BUS_OUT = EDAT_2 ? OP_2 : 8'bz;  // Controlled_Buffer controlled_buffer_5
  or or_7 (or_7_out, counter_1_q[0], counter_1_q[1]);
  not not_9 (not_9_out, or_7_out);
  and and_18 (and_18_out, decoder_1_out3, Load_3);
  and and_19 (and_19_out, and_16_out, not_10_out);
  not not_10 (not_10_out, OP_0[3]);
  and and_20 (and_20_out, or_3_out, not_11_out);
  not not_11 (not_11_out, OP_0[3]);
  and and_21 (Load_3, or_3_out, OP_0[3]);
  Register #(.trigger("high"), .width(1)) register_5 (
    .D(INTERRUPT), .en(1'b1), .clk(not_9_out), .Q(INTERRUPT_OUT));  // open: clr
  Register #(.trigger("high"), .width(1)) register_6 (
    .D(RESET), .en(1'b1), .clk(not_9_out), .Q(RESET_OUT));  // open: clr
  or or_8 (Load_1, or_6_out, and_19_out, and_20_out);
  not not_12 (not_12_out, OP_0[3]);
  IO_INTERFACE io_interface_1 (
    .INPUT_DATA_IN(DEVICE_DATA_IN), .INPUT_DECLARE_IN(DEVICE_INPUT), .OUTPUT_DATA_IN(undriven_2),
    .OUTPUT_DECLARE_IN(undriven_4), .INPUT_DATA_OUT(io_interface_1_input_data_out),
    .INPUT_DECLARE_OUT(io_interface_1_input_declare_out), .OUTPUT_DECLARE_OUT(DEVICE_OUTPUT),
    .OUTPUT_DATA_OUT(DEVICE_DATA_OUT));
  IO_INTERFACE io_interface_2 (
    .INPUT_DATA_IN(DATA_IN), .INPUT_DECLARE_IN(undriven), .OUTPUT_DATA_IN(undriven_3),
    .OUTPUT_DECLARE_IN(undriven_5), .INPUT_DATA_OUT(instruction_buffer_1_p5),
    .INPUT_DECLARE_OUT(READ_WRITE_OUT), .OUTPUT_DECLARE_OUT(io_interface_2_output_declare_out),
    .OUTPUT_DATA_OUT(DATA_OUT));
  not not_13 (not_13_out, or_9_out);
  or or_9 (or_9_out, INTERRUPT_OUT, RESET_OUT);
  nor nor_1 (Load_2, Load_1, Load_3);
  and and_22 (Illegal, and_10_out, not_12_out);
  Instruction_Decoder instruction_decoder_1 (
    .CBUFF(instruction_buffer_1_p6), .MDSpec(instruction_buffer_1_p7), .IR_QT(instruction_buffer_1_p8),
    .EXECUTE(instruction_buffer_1_p16), .RESET_DECODER(instruction_buffer_1_p17),
    .IRQ(instruction_buffer_1_p18), .NMI(instruction_buffer_1_p19), .CLOCK(CLOCK_t),
    .Instruction_IN(instruction_buffer_1_p13));  // open: ID_SP, SPM_E, LD_XF, LDY, CCLT, FLAGS_E, IOB_CPY, ID_PC, PCM_E, LC_PC, RPC_H, RPC_L, RHLE, MEMB_CPY, C_RST, DB_IRCTX, ADD_16, C_IRQ, C_NMI, RREAD, RWRITE, EDAT1, EDAT2, DBUS_CPY, RESET_CPU, ADD_8
  Addressing_Module addressing_module_1 (
    .CLOCK(CLOCK_t), .BIT16_D(ADD16_BUS), .SP_16bit(aux_registers_1_sp_out), .DATA_IN(DATA_BUS_t));  // open: MASpec, READ, WRITE, ADDRESS_OUT, DATA_OUT, READ_OUT, WRITE_OUT
  and and_23 (READY, not_9_out, not_13_out);

  // Other names for the same wires on the sheet: op_code[7:0] = OP_0

  // Notes on the sheet:
  //   Fixed state data ?
endmodule

module GCard (
  input  in_1,
  input  [1:0] DISPLAY_MODE,
  input  WRITE_ENABLE,
  input  [7:0] DATA
);

  wire and_1_out, clock_1_out, decoder_1_out0, decoder_1_out1, decoder_1_out2, decoder_1_out3,
       decoder_2_out0, decoder_2_out1, decoder_2_out2, gpu_hcounter_1_reset_out, gpu_hcounter_1_sync,
       gpu_hcounter_1_write_enable, gpu_vcounter_1_sync, gpu_vcounter_1_write_enable, rgb_video_1_p1,
       rgb_video_1_p2, rgb_video_1_p3, rgb_video_1_p4, rgb_video_1_p5, rgb_video_2_p2, rgb_video_3_p2,
       rgb_video_4_p2, rgb_video_5_p2, rgb_video_6_p2, rgb_video_7_p2, rgb_video_8_p2, rgb_video_9_p2,
       rgb_video_10_p2, rgb_video_11_p2, rgb_video_12_p2;
  wire [11:0] gpu_hcounter_1_data_xaddress, gpu_vcounter_1_data_yaddress;

  Clock clock_1 (.out(clock_1_out));
  and and_1 (and_1_out, gpu_vcounter_1_write_enable, gpu_hcounter_1_write_enable);
  Counter #(.max('h7), .width(3)) counter_1 ();  // open: load, D, count, Q, carry, up, clk, clr
  RAM #(.addrWidth(20), .dataWidth(4)) ram_1 ();  // open: addr, we, oe, clk, din, dout
  GPU_HCounter gpu_hcounter_1 (
    .DATA_XADDRESS(gpu_hcounter_1_data_xaddress), .SYNC(gpu_hcounter_1_sync),
    .WRITE_ENABLE(gpu_hcounter_1_write_enable), .RESET_OUT(gpu_hcounter_1_reset_out));  // open: CLOCK
  GPU_VCounter gpu_vcounter_1 (
    .CLOCK(gpu_hcounter_1_reset_out), .DATA_YADDRESS(gpu_vcounter_1_data_yaddress),
    .SYNC(gpu_vcounter_1_sync), .WRITE_ENABLE(gpu_vcounter_1_write_enable));  // open: RESET_OUT
  LED led_1 (.in(gpu_hcounter_1_sync));
  LED led_2 (.in(gpu_hcounter_1_write_enable));
  Hex_Digit_Display hex_digit_display_1 (.value(gpu_hcounter_1_data_xaddress[11:8]));  // open: dp
  LED led_3 (.in(gpu_vcounter_1_sync));
  LED led_4 (.in(gpu_vcounter_1_write_enable));
  Hex_Digit_Display hex_digit_display_2 (.value(gpu_vcounter_1_data_yaddress[11:8]));  // open: dp
  Hex_Digit_Display hex_digit_display_3 (.value(gpu_hcounter_1_data_xaddress[7:4]));  // open: dp
  Hex_Digit_Display hex_digit_display_4 (.value(gpu_vcounter_1_data_yaddress[7:4]));  // open: dp
  Hex_Digit_Display hex_digit_display_5 (.value(gpu_hcounter_1_data_xaddress[3:0]));  // open: dp
  Hex_Digit_Display hex_digit_display_6 (.value(gpu_vcounter_1_data_yaddress[3:0]));  // open: dp
  Decoder #(.select(2)) decoder_1 (
    .out0(decoder_1_out0), .out1(decoder_1_out1), .out2(decoder_1_out2), .out3(decoder_1_out3),
    .sel(gpu_hcounter_1_data_xaddress[11:10]), .en(and_1_out));
  Decoder #(.select(2)) decoder_2 (
    .out0(decoder_2_out0), .out1(decoder_2_out1), .out2(decoder_2_out2),
    .sel(gpu_vcounter_1_data_yaddress[11:10]), .en(and_1_out));  // open: out3
  // RGB_Video #(.cursor("No Cursor"), .height(256), .scale(1), .width(256)) rgb_video_1: pin names not known; wires that end beside it: rgb_video_1_p1, rgb_video_1_p2, rgb_video_1_p3, rgb_video_1_p4, rgb_video_1_p5
  and and_2 (rgb_video_1_p2, decoder_2_out0, decoder_1_out0);
  // RGB_Video #(.cursor("No Cursor"), .height(256), .scale(1), .width(256)) rgb_video_2: pin names not known; wires that end beside it: rgb_video_1_p1, rgb_video_2_p2, rgb_video_1_p3, rgb_video_1_p4, rgb_video_1_p5
  and and_3 (rgb_video_2_p2, decoder_2_out1, decoder_1_out0);
  // RGB_Video #(.cursor("No Cursor"), .height(256), .scale(1), .width(256)) rgb_video_3: pin names not known; wires that end beside it: rgb_video_1_p1, rgb_video_3_p2, rgb_video_1_p3, rgb_video_1_p4, rgb_video_1_p5
  and and_4 (rgb_video_3_p2, decoder_2_out2, decoder_1_out0);
  // RGB_Video #(.cursor("No Cursor"), .height(256), .scale(1), .width(256)) rgb_video_4: pin names not known; wires that end beside it: rgb_video_1_p1, rgb_video_4_p2, rgb_video_1_p3, rgb_video_1_p4, rgb_video_1_p5
  // RGB_Video #(.cursor("No Cursor"), .height(256), .scale(1), .width(256)) rgb_video_5: pin names not known; wires that end beside it: rgb_video_1_p1, rgb_video_5_p2, rgb_video_1_p3, rgb_video_1_p4, rgb_video_1_p5
  // RGB_Video #(.cursor("No Cursor"), .height(256), .scale(1), .width(256)) rgb_video_6: pin names not known; wires that end beside it: rgb_video_1_p1, rgb_video_6_p2, rgb_video_1_p3, rgb_video_1_p4, rgb_video_1_p5
  and and_5 (rgb_video_4_p2, decoder_2_out0, decoder_1_out1);
  and and_6 (rgb_video_5_p2, decoder_2_out1, decoder_1_out1);
  and and_7 (rgb_video_6_p2, decoder_2_out2, decoder_1_out1);
  // RGB_Video #(.cursor("No Cursor"), .height(256), .scale(1), .width(256)) rgb_video_7: pin names not known; wires that end beside it: rgb_video_1_p1, rgb_video_7_p2, rgb_video_1_p3, rgb_video_1_p4, rgb_video_1_p5
  and and_8 (rgb_video_7_p2, decoder_2_out0, decoder_1_out2);
  // RGB_Video #(.cursor("No Cursor"), .height(256), .scale(1), .width(256)) rgb_video_8: pin names not known; wires that end beside it: rgb_video_1_p1, rgb_video_8_p2, rgb_video_1_p3, rgb_video_1_p4, rgb_video_1_p5
  and and_9 (rgb_video_8_p2, decoder_2_out1, decoder_1_out2);
  // RGB_Video #(.cursor("No Cursor"), .height(256), .scale(1), .width(256)) rgb_video_9: pin names not known; wires that end beside it: rgb_video_1_p1, rgb_video_9_p2, rgb_video_1_p3, rgb_video_1_p4, rgb_video_1_p5
  and and_10 (rgb_video_9_p2, decoder_2_out2, decoder_1_out2);
  // RGB_Video #(.cursor("No Cursor"), .height(256), .scale(1), .width(256)) rgb_video_10: pin names not known; wires that end beside it: rgb_video_1_p1, rgb_video_10_p2, rgb_video_1_p3, rgb_video_1_p4, rgb_video_1_p5
  and and_11 (rgb_video_10_p2, decoder_2_out0, decoder_1_out3);
  // RGB_Video #(.cursor("No Cursor"), .height(256), .scale(1), .width(256)) rgb_video_11: pin names not known; wires that end beside it: rgb_video_1_p1, rgb_video_11_p2, rgb_video_1_p3, rgb_video_1_p4, rgb_video_1_p5
  and and_12 (rgb_video_11_p2, decoder_2_out1, decoder_1_out3);
  // RGB_Video #(.cursor("No Cursor"), .height(256), .scale(1), .width(256)) rgb_video_12: pin names not known; wires that end beside it: rgb_video_1_p1, rgb_video_12_p2, rgb_video_1_p3, rgb_video_1_p4, rgb_video_1_p5
  and and_13 (rgb_video_12_p2, decoder_2_out2, decoder_1_out3);
endmodule

module GPU_HCounter (
  input  CLOCK,
  output [11:0] DATA_XADDRESS,
  output SYNC,
  output WRITE_ENABLE,
  output RESET_OUT
);

  wire counter_1_carry, counter_2_carry, d_ff_1_qn, d_ff_2_q, I800_out, I840_out, I968_out, not_1_out,
       not_2_out, not_3_out, not_4_out, not_5_out, not_6_out, not_7_out, not_8_out, not_9_out, not_10_out,
       not_11_out, not_12_out, not_13_out, not_14_out, not_15_out, not_16_out, not_17_out, not_18_out,
       not_19_out, not_20_out, not_21_out, not_22_out, not_23_out, not_24_out, not_25_out, not_26_out,
       not_27_out, not_28_out, not_29_out;

  Counter #(.max('hf), .width(4)) counter_1 (
    .load(1'b0), .count(1'b1), .Q(DATA_XADDRESS[3:0]), .carry(counter_1_carry), .up(1'b1), .clk(CLOCK),
    .clr(RESET_OUT));  // open: D
  Counter #(.max('hf), .width(4)) counter_2 (
    .load(1'b0), .count(1'b1), .Q(DATA_XADDRESS[7:4]), .carry(counter_2_carry), .up(1'b1), .clk(not_1_out),
    .clr(RESET_OUT));  // open: D
  not not_1 (not_1_out, counter_1_carry);
  Counter #(.max('hf), .width(4)) counter_3 (
    .load(1'b0), .count(1'b1), .Q(DATA_XADDRESS[11:8]), .up(1'b1), .clk(not_2_out), .clr(RESET_OUT));  // open: D, carry
  not not_2 (not_2_out, counter_2_carry);
  not not_3 (not_3_out, DATA_XADDRESS[0]);
  not not_4 (not_4_out, DATA_XADDRESS[1]);
  not not_5 (not_5_out, DATA_XADDRESS[2]);
  not not_6 (not_6_out, DATA_XADDRESS[4]);
  not not_7 (not_7_out, DATA_XADDRESS[5]);
  not not_8 (not_8_out, DATA_XADDRESS[7]);
  not not_9 (not_9_out, DATA_XADDRESS[0]);
  not not_10 (not_10_out, DATA_XADDRESS[1]);
  not not_11 (not_11_out, DATA_XADDRESS[2]);
  not not_12 (not_12_out, DATA_XADDRESS[4]);
  not not_13 (not_13_out, DATA_XADDRESS[5]);
  not not_14 (not_14_out, DATA_XADDRESS[0]);
  not not_15 (not_15_out, DATA_XADDRESS[1]);
  not not_16 (not_16_out, DATA_XADDRESS[2]);
  not not_17 (not_17_out, DATA_XADDRESS[3]);
  not not_18 (not_18_out, DATA_XADDRESS[4]);
  not not_19 (not_19_out, DATA_XADDRESS[6]);
  not not_20 (not_20_out, DATA_XADDRESS[7]);
  not not_21 (not_21_out, DATA_XADDRESS[0]);
  not not_22 (not_22_out, DATA_XADDRESS[1]);
  not not_23 (not_23_out, DATA_XADDRESS[2]);
  not not_24 (not_24_out, DATA_XADDRESS[3]);
  not not_25 (not_25_out, DATA_XADDRESS[4]);
  not not_26 (not_26_out, DATA_XADDRESS[6]);
  not not_27 (not_27_out, DATA_XADDRESS[7]);
  not not_28 (not_28_out, DATA_XADDRESS[8]);
  not not_29 (not_29_out, DATA_XADDRESS[9]);
  and I840 (I840_out, not_3_out, not_4_out, not_5_out, DATA_XADDRESS[3], not_6_out, not_7_out, DATA_XADDRESS[6], not_8_out, DATA_XADDRESS[8], DATA_XADDRESS[9]);
  D_Flip_Flop d_ff_1 (.Q(SYNC), .Qn(d_ff_1_qn), .preset(I840_out), .reset(I968_out));  // open: D, clk
  and I968 (I968_out, not_9_out, not_10_out, not_11_out, DATA_XADDRESS[3], not_12_out, not_13_out, DATA_XADDRESS[6], DATA_XADDRESS[7], DATA_XADDRESS[8], DATA_XADDRESS[9]);
  and I800 (I800_out, not_14_out, not_15_out, not_16_out, not_17_out, not_18_out, DATA_XADDRESS[5], not_19_out, not_20_out, DATA_XADDRESS[8], DATA_XADDRESS[9]);
  D_Flip_Flop d_ff_2 (.Q(d_ff_2_q), .Qn(WRITE_ENABLE), .preset(I800_out), .reset(RESET_OUT));  // open: D, clk
  and I1056 (RESET_OUT, not_21_out, not_22_out, not_23_out, not_24_out, not_25_out, DATA_XADDRESS[5], not_26_out, not_27_out, not_28_out, not_29_out, DATA_XADDRESS[10]);
endmodule

module GPU_VCounter (
  input  CLOCK,
  output [11:0] DATA_YADDRESS,
  output SYNC,
  output WRITE_ENABLE,
  output RESET_OUT
);

  wire counter_1_carry, counter_2_carry, d_ff_1_qn, d_ff_2_q, I600_out, I601_out, I605_out, not_1_out,
       not_2_out, not_3_out, not_4_out, not_5_out, not_6_out, not_7_out, not_8_out, not_9_out, not_10_out,
       not_11_out, not_12_out, not_13_out, not_14_out, not_15_out, not_16_out, not_17_out, not_18_out,
       not_19_out, not_20_out, not_21_out, not_22_out;

  Counter #(.max('hf), .width(4)) counter_1 (
    .load(1'b0), .count(1'b1), .Q(DATA_YADDRESS[3:0]), .carry(counter_1_carry), .up(1'b1), .clk(CLOCK),
    .clr(RESET_OUT));  // open: D
  Counter #(.max('hf), .width(4)) counter_2 (
    .load(1'b0), .count(1'b1), .Q(DATA_YADDRESS[7:4]), .carry(counter_2_carry), .up(1'b1), .clk(not_1_out),
    .clr(RESET_OUT));  // open: D
  not not_1 (not_1_out, counter_1_carry);
  Counter #(.max('hf), .width(4)) counter_3 (
    .load(1'b0), .count(1'b1), .Q(DATA_YADDRESS[11:8]), .up(1'b1), .clk(not_2_out), .clr(RESET_OUT));  // open: D, carry
  not not_2 (not_2_out, counter_2_carry);
  not not_3 (not_3_out, DATA_YADDRESS[1]);
  not not_4 (not_4_out, DATA_YADDRESS[2]);
  not not_5 (not_5_out, DATA_YADDRESS[5]);
  not not_6 (not_6_out, DATA_YADDRESS[7]);
  not not_7 (not_7_out, DATA_YADDRESS[8]);
  not not_8 (not_8_out, DATA_YADDRESS[1]);
  not not_9 (not_9_out, DATA_YADDRESS[5]);
  not not_10 (not_10_out, DATA_YADDRESS[7]);
  not not_11 (not_11_out, DATA_YADDRESS[8]);
  not not_12 (not_12_out, DATA_YADDRESS[0]);
  not not_13 (not_13_out, DATA_YADDRESS[1]);
  not not_14 (not_14_out, DATA_YADDRESS[2]);
  not not_15 (not_15_out, DATA_YADDRESS[5]);
  not not_16 (not_16_out, DATA_YADDRESS[7]);
  not not_17 (not_17_out, DATA_YADDRESS[8]);
  not not_18 (not_18_out, DATA_YADDRESS[0]);
  not not_19 (not_19_out, DATA_YADDRESS[1]);
  not not_20 (not_20_out, DATA_YADDRESS[3]);
  not not_21 (not_21_out, DATA_YADDRESS[7]);
  not not_22 (not_22_out, DATA_YADDRESS[8]);
  and I601 (I601_out, DATA_YADDRESS[0], not_3_out, not_4_out, DATA_YADDRESS[3], DATA_YADDRESS[4], not_5_out, DATA_YADDRESS[6], not_6_out, not_7_out, DATA_YADDRESS[9]);
  D_Flip_Flop d_ff_1 (.Q(SYNC), .Qn(d_ff_1_qn), .preset(I601_out), .reset(I605_out));  // open: D, clk
  and I605 (I605_out, DATA_YADDRESS[0], not_8_out, DATA_YADDRESS[2], DATA_YADDRESS[3], DATA_YADDRESS[4], not_9_out, DATA_YADDRESS[6], not_10_out, not_11_out, DATA_YADDRESS[9]);
  and I600 (I600_out, not_12_out, not_13_out, not_14_out, DATA_YADDRESS[3], DATA_YADDRESS[4], not_15_out, DATA_YADDRESS[6], not_16_out, not_17_out, DATA_YADDRESS[9]);
  D_Flip_Flop d_ff_2 (.Q(d_ff_2_q), .Qn(WRITE_ENABLE), .preset(I600_out), .reset(RESET_OUT));  // open: D, clk
  and I628 (RESET_OUT, not_18_out, not_19_out, DATA_YADDRESS[2], not_20_out, DATA_YADDRESS[4], DATA_YADDRESS[5], DATA_YADDRESS[6], not_21_out, not_22_out, DATA_YADDRESS[9]);
endmodule
module GCard_Buffer (
  input  in_1,
  input  [1:0] DISPLAY_MODE,
  input  WRITE_ENABLE,
  input  [7:0] DATA
);

  wire and_1_out, clock_1_out, decoder_1_out0, decoder_1_out1, decoder_1_out2, decoder_1_out3,
       decoder_2_out0, decoder_2_out1, decoder_2_out2, gpu_hcounter_1_reset_out, gpu_hcounter_1_sync,
       gpu_hcounter_1_write_enable, gpu_vcounter_1_sync, gpu_vcounter_1_write_enable, rgb_video_1_p2,
       rgb_video_2_p2, rgb_video_3_p2, rgb_video_4_p2, rgb_video_5_p2, rgb_video_6_p2, rgb_video_7_p2,
       rgb_video_8_p2, rgb_video_9_p2, rgb_video_10_p2, rgb_video_11_p2, rgb_video_12_p2;
  wire [3:0] gpu_hcounter_1_data_xaddress, gpu_hcounter_1_data_xaddress_2, gpu_hcounter_1_data_xaddress_3,
       gpu_vcounter_1_data_yaddress, gpu_vcounter_1_data_yaddress_2, gpu_vcounter_1_data_yaddress_3,
       ram_1_dout;

  Clock clock_1 (.out(clock_1_out));
  and and_1 (and_1_out, gpu_vcounter_1_write_enable, gpu_hcounter_1_write_enable);
  GPU_HCounter gpu_hcounter_1 (
    .CLOCK(clock_1_out),
    .DATA_XADDRESS({gpu_hcounter_1_data_xaddress, gpu_hcounter_1_data_xaddress_3, gpu_hcounter_1_data_xaddress_2}),
    .SYNC(gpu_hcounter_1_sync), .WRITE_ENABLE(gpu_hcounter_1_write_enable),
    .RESET_OUT(gpu_hcounter_1_reset_out));
  GPU_VCounter gpu_vcounter_1 (
    .CLOCK(gpu_hcounter_1_reset_out),
    .DATA_YADDRESS({gpu_vcounter_1_data_yaddress, gpu_vcounter_1_data_yaddress_3, gpu_vcounter_1_data_yaddress_2}),
    .SYNC(gpu_vcounter_1_sync), .WRITE_ENABLE(gpu_vcounter_1_write_enable));  // open: RESET_OUT
  LED led_1 (.in(gpu_hcounter_1_sync));
  LED led_2 (.in(gpu_hcounter_1_write_enable));
  Hex_Digit_Display hex_digit_display_1 (.value(gpu_hcounter_1_data_xaddress));  // open: dp
  LED led_3 (.in(gpu_vcounter_1_sync));
  LED led_4 (.in(gpu_vcounter_1_write_enable));
  Hex_Digit_Display hex_digit_display_2 (.value(gpu_vcounter_1_data_yaddress));  // open: dp
  Hex_Digit_Display hex_digit_display_3 (.value(gpu_hcounter_1_data_xaddress_3));  // open: dp
  Hex_Digit_Display hex_digit_display_4 (.value(gpu_vcounter_1_data_yaddress_3));  // open: dp
  Hex_Digit_Display hex_digit_display_5 (.value(gpu_hcounter_1_data_xaddress_2));  // open: dp
  Hex_Digit_Display hex_digit_display_6 (.value(gpu_vcounter_1_data_yaddress_2));  // open: dp
  RAM #(.addrWidth(20), .dataWidth(4)) ram_1 (
    .addr({gpu_vcounter_1_data_yaddress[1:0], gpu_vcounter_1_data_yaddress_3, gpu_vcounter_1_data_yaddress_2, gpu_hcounter_1_data_xaddress[1:0], gpu_hcounter_1_data_xaddress_3, gpu_hcounter_1_data_xaddress_2}),
    .we(1'b0), .oe(1'b1), .clk(clock_1_out), .dout(ram_1_dout));  // open: din
  Decoder #(.select(2)) decoder_1 (
    .out0(decoder_1_out0), .out1(decoder_1_out1), .out2(decoder_1_out2), .out3(decoder_1_out3),
    .sel(gpu_hcounter_1_data_xaddress[1:0]), .en(and_1_out));
  Decoder #(.select(2)) decoder_2 (
    .out0(decoder_2_out0), .out1(decoder_2_out1), .out2(decoder_2_out2),
    .sel(gpu_vcounter_1_data_yaddress[1:0]), .en(and_1_out));  // open: out3
  // RGB_Video #(.cursor("No Cursor"), .height(256), .scale(1), .width(256)) rgb_video_1: pin names not known; wires that end beside it: clock_1_out, rgb_video_1_p2, {gpu_hcounter_1_data_xaddress_3, gpu_hcounter_1_data_xaddress_2}, {gpu_vcounter_1_data_yaddress_3, gpu_vcounter_1_data_yaddress_2}, ram_1_dout
  and and_2 (rgb_video_1_p2, decoder_2_out0, decoder_1_out0);
  // RGB_Video #(.cursor("No Cursor"), .height(256), .scale(1), .width(256)) rgb_video_2: pin names not known; wires that end beside it: clock_1_out, rgb_video_2_p2, {gpu_hcounter_1_data_xaddress_3, gpu_hcounter_1_data_xaddress_2}, {gpu_vcounter_1_data_yaddress_3, gpu_vcounter_1_data_yaddress_2}, ram_1_dout
  and and_3 (rgb_video_2_p2, decoder_2_out1, decoder_1_out0);
  // RGB_Video #(.cursor("No Cursor"), .height(256), .scale(1), .width(256)) rgb_video_3: pin names not known; wires that end beside it: clock_1_out, rgb_video_3_p2, {gpu_hcounter_1_data_xaddress_3, gpu_hcounter_1_data_xaddress_2}, {gpu_vcounter_1_data_yaddress_3, gpu_vcounter_1_data_yaddress_2}, ram_1_dout
  and and_4 (rgb_video_3_p2, decoder_2_out2, decoder_1_out0);
  // RGB_Video #(.cursor("No Cursor"), .height(256), .scale(1), .width(256)) rgb_video_4: pin names not known; wires that end beside it: clock_1_out, rgb_video_4_p2, {gpu_hcounter_1_data_xaddress_3, gpu_hcounter_1_data_xaddress_2}, {gpu_vcounter_1_data_yaddress_3, gpu_vcounter_1_data_yaddress_2}, ram_1_dout
  // RGB_Video #(.cursor("No Cursor"), .height(256), .scale(1), .width(256)) rgb_video_5: pin names not known; wires that end beside it: clock_1_out, rgb_video_5_p2, {gpu_hcounter_1_data_xaddress_3, gpu_hcounter_1_data_xaddress_2}, {gpu_vcounter_1_data_yaddress_3, gpu_vcounter_1_data_yaddress_2}, ram_1_dout
  // RGB_Video #(.cursor("No Cursor"), .height(256), .scale(1), .width(256)) rgb_video_6: pin names not known; wires that end beside it: clock_1_out, rgb_video_6_p2, {gpu_hcounter_1_data_xaddress_3, gpu_hcounter_1_data_xaddress_2}, {gpu_vcounter_1_data_yaddress_3, gpu_vcounter_1_data_yaddress_2}, ram_1_dout
  and and_5 (rgb_video_4_p2, decoder_2_out0, decoder_1_out1);
  and and_6 (rgb_video_5_p2, decoder_2_out1, decoder_1_out1);
  and and_7 (rgb_video_6_p2, decoder_2_out2, decoder_1_out1);
  // RGB_Video #(.cursor("No Cursor"), .height(256), .scale(1), .width(256)) rgb_video_7: pin names not known; wires that end beside it: clock_1_out, rgb_video_7_p2, {gpu_hcounter_1_data_xaddress_3, gpu_hcounter_1_data_xaddress_2}, {gpu_vcounter_1_data_yaddress_3, gpu_vcounter_1_data_yaddress_2}, ram_1_dout
  and and_8 (rgb_video_7_p2, decoder_2_out0, decoder_1_out2);
  // RGB_Video #(.cursor("No Cursor"), .height(256), .scale(1), .width(256)) rgb_video_8: pin names not known; wires that end beside it: clock_1_out, rgb_video_8_p2, {gpu_hcounter_1_data_xaddress_3, gpu_hcounter_1_data_xaddress_2}, {gpu_vcounter_1_data_yaddress_3, gpu_vcounter_1_data_yaddress_2}, ram_1_dout
  and and_9 (rgb_video_8_p2, decoder_2_out1, decoder_1_out2);
  // RGB_Video #(.cursor("No Cursor"), .height(256), .scale(1), .width(256)) rgb_video_9: pin names not known; wires that end beside it: clock_1_out, rgb_video_9_p2, {gpu_hcounter_1_data_xaddress_3, gpu_hcounter_1_data_xaddress_2}, {gpu_vcounter_1_data_yaddress_3, gpu_vcounter_1_data_yaddress_2}, ram_1_dout
  and and_10 (rgb_video_9_p2, decoder_2_out2, decoder_1_out2);
  // RGB_Video #(.cursor("No Cursor"), .height(256), .scale(1), .width(256)) rgb_video_10: pin names not known; wires that end beside it: clock_1_out, rgb_video_10_p2, {gpu_hcounter_1_data_xaddress_3, gpu_hcounter_1_data_xaddress_2}, {gpu_vcounter_1_data_yaddress_3, gpu_vcounter_1_data_yaddress_2}, ram_1_dout
  and and_11 (rgb_video_10_p2, decoder_2_out0, decoder_1_out3);
  // RGB_Video #(.cursor("No Cursor"), .height(256), .scale(1), .width(256)) rgb_video_11: pin names not known; wires that end beside it: clock_1_out, rgb_video_11_p2, {gpu_hcounter_1_data_xaddress_3, gpu_hcounter_1_data_xaddress_2}, {gpu_vcounter_1_data_yaddress_3, gpu_vcounter_1_data_yaddress_2}, ram_1_dout
  and and_12 (rgb_video_11_p2, decoder_2_out1, decoder_1_out3);
  // RGB_Video #(.cursor("No Cursor"), .height(256), .scale(1), .width(256)) rgb_video_12: pin names not known; wires that end beside it: clock_1_out, rgb_video_12_p2, {gpu_hcounter_1_data_xaddress_3, gpu_hcounter_1_data_xaddress_2}, {gpu_vcounter_1_data_yaddress_3, gpu_vcounter_1_data_yaddress_2}, ram_1_dout
  and and_13 (rgb_video_12_p2, decoder_2_out2, decoder_1_out3);
endmodule

module Latch (
  input  LOCK_E,
  input  DIN,
  output DOUT
);

  wire and_1_out, and_2_out, not_1_out, not_2_out, or_1_out, or_2_out, undriven, undriven_2;

  not not_1 (not_1_out, LOCK_E);
  or or_1 (or_1_out, and_1_out, and_2_out);
  not not_2 (not_2_out, undriven);
  Register #(.trigger("high"), .width(1)) register_1 (.D(DIN), .en(1'b1), .Q(DOUT), .clk(not_1_out));  // open: clr
  and and_1 (and_1_out, undriven, or_1_out);
  or or_2 (or_2_out, and_1_out, and_2_out);
  and and_2 (and_2_out, undriven_2, not_2_out);
endmodule

module temp_test (
  input  [7:0] in_1,
  output out_2
);

  wire and_1_out, and_2_out, and_3_out, and_4_out, and_5_out, and_6_out, and_7_out, and_8_out, and_9_out,
       and_10_out, and_11_out, and_12_out, and_13_out, and_14_out, and_15_out, and_16_out, and_17_out,
       and_18_out, and_19_out, and_20_out, and_21_out, and_22_out, and_23_out, and_24_out, or_1_out,
       or_2_out, or_3_out, or_4_out, or_5_out, or_6_out, or_7_out, or_8_out, or_9_out, or_10_out, or_11_out,
       or_12_out, or_13_out, or_14_out, or_15_out;

  and and_1 (and_1_out, in_1[0], in_1[1]);
  or or_1 (or_1_out, in_1[0], in_1[1]);
  and and_2 (and_2_out, in_1[2], in_1[3]);
  or or_2 (or_2_out, in_1[2], in_1[3]);
  and and_3 (and_3_out, in_1[4], in_1[5]);
  or or_3 (or_3_out, in_1[4], in_1[5]);
  and and_4 (and_4_out, in_1[6], in_1[7]);
  or or_4 (or_4_out, in_1[6], in_1[7]);
  and and_5 (and_5_out, or_1_out, ~and_1_out);  // AND_Gate
  and and_6 (and_6_out, and_1_out, or_1_out);
  and and_7 (and_7_out, or_2_out, ~and_2_out);  // AND_Gate
  and and_8 (and_8_out, and_2_out, or_2_out);
  and and_9 (and_9_out, or_3_out, ~and_3_out);  // AND_Gate
  and and_10 (and_10_out, and_3_out, or_3_out);
  and and_11 (and_11_out, or_4_out, ~and_4_out);  // AND_Gate
  and and_12 (and_12_out, and_4_out, or_4_out);
  or or_5 (or_5_out, and_5_out, and_6_out);
  or or_6 (or_6_out, and_7_out, and_8_out);
  or or_7 (or_7_out, and_9_out, and_10_out);
  or or_8 (or_8_out, and_11_out, and_12_out);
  and and_13 (and_13_out, or_7_out, or_8_out);
  or or_9 (or_9_out, or_7_out, or_8_out);
  and and_14 (and_14_out, or_5_out, or_6_out);
  or or_10 (or_10_out, or_5_out, or_6_out);
  and and_15 (and_15_out, or_10_out, ~and_14_out);  // AND_Gate
  and and_16 (and_16_out, and_14_out, or_10_out);
  and and_17 (and_17_out, or_9_out, ~and_13_out);  // AND_Gate
  and and_18 (and_18_out, and_13_out, or_9_out);
  or or_11 (or_11_out, and_15_out, and_16_out);
  or or_12 (or_12_out, and_17_out, and_18_out);
  and and_19 (and_19_out, or_11_out, or_12_out);
  or or_13 (or_13_out, or_11_out, or_12_out);
  and and_20 (and_20_out, or_13_out, ~and_19_out);  // AND_Gate
  and and_21 (and_21_out, and_19_out, or_13_out);
  or or_14 (or_14_out, and_20_out, and_21_out);
  and and_22 (and_22_out, or_14_out, 1'b1);
  or or_15 (or_15_out, or_14_out, 1'b1);
  and and_23 (and_23_out, or_15_out, ~and_22_out);  // AND_Gate
  and and_24 (and_24_out, and_22_out, or_15_out);
  or or_16 (out_2, and_23_out, and_24_out);
endmodule

module tmep (
  input  I1,
  input  I2
);
endmodule

module temp (
  input  I1,
  input  regE,
  input  Y,
  output ill,
  output UUSD
);

  wire and_1_out, and_2_out, not_1_out, not_2_out, not_3_out;

  not not_1 (not_1_out, I1);
  not not_2 (not_2_out, regE);
  not not_3 (not_3_out, Y);
  and and_1 (and_1_out, not_1_out, not_3_out);
  and and_2 (and_2_out, not_1_out, regE);
  and and_3 (UUSD, not_1_out, not_2_out);
  or or_1 (ill, and_1_out, and_2_out);
endmodule

module temp2 (
  input  I2,
  input  Il2,
  input  M2,
  output e
);

  wire and_1_out, and_2_out, not_1_out, not_2_out, not_3_out;

  not not_1 (not_1_out, I2);
  not not_2 (not_2_out, Il2);
  not not_3 (not_3_out, M2);
  and and_1 (and_1_out, not_1_out, not_2_out);
  and and_2 (and_2_out, not_1_out, not_3_out);
  or or_1 (e, and_1_out, and_2_out);
endmodule

module newGPU (
  input  CLK,
  input  [13:0] AD_IN,
  input  [7:0] DAT_IN,
  input  READ,
  input  WRITE,
  output HSYNC,
  output VSYNC
);

  wire and_1_out, and_2_out, and_3_out, and_4_out, and_5_out, and_6_out, and_7_out, and_8_out, buffer_1_out,
       buffer_2_out, buffer_3_out, buffer_4_out, buffer_5_out, buffer_6_out, buffer_7_out, buffer_8_out,
       clock_1_out, comparator_1_eq, comparator_2_eq, comparator_3_eq, comparator_4_eq, comparator_5_eq,
       comparator_6_eq, comparator_7_eq, comparator_8_eq, d_ff_1_q, d_ff_3_q, not_1_out, not_2_out;
  wire [3:0] multiplexer_2_out, multiplexer_3_out, multiplexer_4_out, ram_1_dout, ram_1_dout_2;
  wire [7:0] register_1_q, register_2_q;
  wire [8:0] counter_1_q;
  wire [9:0] counter_2_q;
  wire [14:0] multiplexer_1_out;

  Clock clock_1 (.out(clock_1_out));
  Counter #(.max('h1ff), .width(9)) counter_1 (
    .count(1'b1), .Q(counter_1_q), .up(1'b1), .clk(clock_1_out), .clr(and_1_out));  // open: load, D, carry
  and and_1 (and_1_out, 1'b1, comparator_4_eq);
  Counter #(.max('h3ff), .width(10)) counter_2 (
    .count(comparator_4_eq), .Q(counter_2_q), .up(1'b1), .clk(clock_1_out), .clr(and_2_out));  // open: load, D, carry
  and and_2 (and_2_out, clock_1_out, comparator_8_eq);
  and and_3 (and_3_out, READ, not_2_out);
  and and_4 (and_4_out, not_2_out, WRITE);
  and and_5 (and_5_out, DAT_IN[4], and_4_out);
  not not_1 (not_1_out, DAT_IN[4]);
  and and_6 (and_6_out, not_1_out, and_4_out);
  Comparator #(.width(9)) comparator_1 (.a(counter_1_q), .b(9'hc8), .eq(comparator_1_eq));  // open: gt, lt
  Comparator #(.width(9)) comparator_2 (.a(counter_1_q), .b(9'hd2), .eq(comparator_2_eq));  // open: gt, lt
  Comparator #(.width(9)) comparator_3 (.a(counter_1_q), .b(9'hf2), .eq(comparator_3_eq));  // open: gt, lt
  Comparator #(.width(9)) comparator_4 (.a(counter_1_q), .b(9'h108), .eq(comparator_4_eq));  // open: gt, lt
  Comparator #(.width(10)) comparator_5 (.a(counter_2_q), .b(10'h258), .eq(comparator_5_eq));  // open: gt, lt
  Comparator #(.width(10)) comparator_6 (.a(counter_2_q), .b(10'h259), .eq(comparator_6_eq));  // open: gt, lt
  Comparator #(.width(10)) comparator_7 (.a(counter_2_q), .b(10'h25d), .eq(comparator_7_eq));  // open: gt, lt
  Comparator #(.width(10)) comparator_8 (.a(counter_2_q), .b(10'h274), .eq(comparator_8_eq));  // open: gt, lt
  buf buffer_1 (buffer_1_out, and_4_out);
  buf buffer_2 (buffer_2_out, buffer_1_out);
  buf buffer_3 (buffer_3_out, buffer_2_out);
  D_Flip_Flop d_ff_1 (
    .clk(comparator_1_eq), .D(comparator_1_eq), .Q(d_ff_1_q), .reset(comparator_4_eq));  // open: Qn, preset
  D_Flip_Flop d_ff_2 (.Q(HSYNC), .preset(comparator_2_eq), .reset(comparator_3_eq));  // open: clk, D, Qn
  D_Flip_Flop d_ff_3 (
    .clk(comparator_5_eq), .D(comparator_5_eq), .Q(d_ff_3_q), .reset(comparator_8_eq));  // open: Qn, preset
  D_Flip_Flop d_ff_4 (.Q(VSYNC), .preset(comparator_6_eq), .reset(comparator_7_eq));  // open: clk, D, Qn
  buf buffer_4 (buffer_4_out, buffer_3_out);
  buf buffer_5 (buffer_5_out, buffer_4_out);
  buf buffer_6 (buffer_6_out, buffer_5_out);
  Multiplexer #(.width(15)) multiplexer_1 (
    .in0({counter_2_q[9:3], counter_1_q[8:1]}), .in1({DAT_IN[6], AD_IN}), .out(multiplexer_1_out),
    .sel(not_2_out));
  Multiplexer #(.width(4)) multiplexer_2 (
    .in0(ram_1_dout), .in1(DAT_IN[3:0]), .out(multiplexer_2_out), .sel(and_6_out));
  Multiplexer #(.width(4)) multiplexer_3 (
    .in0(ram_1_dout_2), .in1(DAT_IN[3:0]), .out(multiplexer_3_out), .sel(and_5_out));
  buf buffer_7 (buffer_7_out, buffer_6_out);
  buf buffer_8 (buffer_8_out, buffer_7_out);
  and and_7 (and_7_out, d_ff_1_q, d_ff_3_q);
  RAM #(.addrWidth(15), .trigger("high")) ram_1 (
    .addr(multiplexer_1_out), .we(buffer_8_out), .oe(1'b1), .din({multiplexer_3_out, multiplexer_2_out}),
    .dout({ram_1_dout_2, ram_1_dout}));
  not not_2 (not_2_out, clock_1_out);
  Register #(.trigger("high")) register_1 (
    .D({ram_1_dout_2, ram_1_dout}), .en(and_7_out), .Q(register_1_q), .clk(and_8_out));  // open: clr
  and and_8 (and_8_out, counter_1_q[0], clock_1_out);
  Register #(.trigger("high")) register_2 (
    .D({ram_1_dout_2, ram_1_dout}), .en(1'b1), .Q(register_2_q), .clk(and_3_out));  // open: clr
  Multiplexer #(.width(4)) multiplexer_4 (
    .in0(register_1_q[3:0]), .in1(register_1_q[7:4]), .out(multiplexer_4_out), .sel(counter_1_q[0]));
endmodule
