// Logisim project TI74CDO01CMOS.circ as structural Verilog
module main (
  input  in_1,
  input  in_2,
  input  in_3,
  input  in_4,
  input  in_5,
  input  in_6,
  input  in_7,
  input  in_8,
  input  in_9,
  input  in_10,
  input  in_11,
  input  in_12,
  input  in_13,
  input  in_14,
  input  in_15,
  input  in_16
);

  wire and_1_out, and_2_out, and_3_out, and_4_out, and_5_out, and_6_out, and_7_out, and_8_out, and_9_out,
       and_10_out, and_11_out, and_12_out, and_13_out, and_14_out, not_1_out, not_2_out, not_3_out,
       not_4_out, not_5_out, not_6_out, not_7_out, not_8_out, not_9_out, not_10_out, not_11_out, not_12_out,
       not_13_out, not_14_out, not_15_out, not_16_out, not_17_out, not_18_out, not_19_out, not_20_out,
       not_21_out, not_22_out, not_23_out, not_24_out, not_25_out, not_26_out, not_27_out, not_28_out,
       not_29_out, not_30_out, or_1_out, or_2_out, or_3_out, or_4_out, or_5_out, or_6_out, or_7_out,
       or_8_out, or_9_out, or_10_out, or_11_out, or_12_out, or_13_out, or_14_out;

  not not_1 (not_1_out, in_1);
  and and_1 (and_1_out, not_1_out, not_2_out);
  not not_2 (not_2_out, in_2);
  or or_1 (or_1_out, in_1, in_2);
  not not_3 (not_3_out, or_1_out);
  not not_4 (not_4_out, in_3);
  and and_2 (and_2_out, not_4_out, not_5_out);
  not not_5 (not_5_out, in_4);
  or or_2 (or_2_out, in_3, in_4);
  not not_6 (not_6_out, or_2_out);
  not not_7 (not_7_out, in_5);
  and and_3 (and_3_out, not_7_out, not_8_out);
  not not_8 (not_8_out, in_6);
  or or_3 (or_3_out, in_5, in_6);
  not not_9 (not_9_out, or_3_out);
  not not_10 (not_10_out, in_7);
  and and_4 (and_4_out, not_10_out, not_11_out);
  not not_11 (not_11_out, in_8);
  or or_4 (or_4_out, in_7, in_8);
  not not_12 (not_12_out, or_4_out);
  not not_13 (not_13_out, in_9);
  and and_5 (and_5_out, not_13_out, not_14_out);
  not not_14 (not_14_out, in_10);
  or or_5 (or_5_out, in_9, in_10);
  not not_15 (not_15_out, in_11);
  and and_6 (and_6_out, not_15_out, not_16_out);
  not not_16 (not_16_out, in_12);
  or or_6 (or_6_out, in_11, in_12);
  not not_17 (not_17_out, in_13);
  and and_7 (and_7_out, not_17_out, not_18_out);
  not not_18 (not_18_out, in_14);
  or or_7 (or_7_out, in_13, in_14);
  not not_19 (not_19_out, in_15);
  and and_8 (and_8_out, not_19_out, not_20_out);
  not not_20 (not_20_out, in_16);
  or or_8 (or_8_out, in_15, in_16);
  and and_9 (and_9_out, and_1_out, and_2_out);
  not not_21 (not_21_out, not_3_out);
  or or_9 (or_9_out, not_21_out, not_22_out);
  not not_22 (not_22_out, not_6_out);
  and and_10 (and_10_out, and_3_out, and_4_out);
  not not_23 (not_23_out, not_9_out);
  or or_10 (or_10_out, not_23_out, not_24_out);
  not not_24 (not_24_out, not_12_out);
  and and_11 (and_11_out, and_5_out, and_6_out);
  and and_12 (and_12_out, and_7_out, and_8_out);
  not not_25 (not_25_out, or_9_out);
  not not_26 (not_26_out, or_10_out);
  or or_11 (or_11_out, or_5_out, or_6_out);
  or or_12 (or_12_out, or_7_out, or_8_out);
  and and_13 (and_13_out, and_9_out, and_10_out);
  not not_27 (not_27_out, not_25_out);
  or or_13 (or_13_out, not_27_out, not_28_out);
  not not_28 (not_28_out, not_26_out);
  not not_29 (not_29_out, or_13_out);
  and and_14 (and_14_out, and_11_out, and_12_out);
  or or_14 (or_14_out, or_11_out, or_12_out);
  not not_30 (not_30_out, or_14_out);

  // Notes on the sheet:
  //   Real ratio BB
  //   3x real BB
endmodule

module STD_CPU (
  input  VCC,
  input  E_CLOCK,
  input  [7:0] MDATIN,
  input  [7:0] IO_DATIN,
  input  HIRQ,
  input  NMI,
  input  RST,
  input  HALT,
  input  TEMP_STOP_OSCILLATION,
  output GND,
  output MREAD,
  output MWRITE,
  output [15:0] ADD_OUT,
  output [7:0] DAT_OUT,
  output INTP,
  output IRQE,
  output ERR,
  output UUSD,
  output [7:0] IODAT,
  output IOWRITE,
  output IOREAD,
  output PCS
);

  wire AFULL, ARREAD, B_FULL, CIRQ, CLBB, clock_1_out, CNMI, CRST, CST_AD1, CST_AD2, CST_AD3, CST_AD4,
       CST_READ, DB_PSH, DBOT, eARG1, eARG2, eCPC, eERR, eIRQ, ePCH, ePCL, eRHL, eSP, eUUSD, eWFLG, I_LD,
       IB_RDY, INT, IRT, IRTV_BUS, LD_XF, LDY, MREAD_t, MWRITE_t, nB_FULL, nDB_PLL, not_1_out, ntEQUAL,
       ntINTP, ntJNE, or_1_out, RREAD, RRES, RWRITE, tHIRQ, tHLT, tIRQ, tMBOE, tNMI, tPCH, tPCL, tRST;
  wire [2:0] AOPC_BUS, RAD_BUS;
  wire [7:0] controlled_buffer_1_out, controlled_buffer_3_out, controlled_buffer_4_out, D_BUS, F_BUS,
       INST_BUS;
  wire [15:0] AD16_BUS;

  Clock clock_1 (.out(clock_1_out));
  assign controlled_buffer_1_out = not_1_out ? MDATIN : 8'bz;  // Controlled_Buffer controlled_buffer_1
  not not_1 (not_1_out, MWRITE);
  SN74AC32N_OR sn74ac32n_or_1 (
    .Y1(eCPC), .A1(ntEQUAL), .B1(ntJNE));  // open: Y2, GND, Y4, Y3, A2, B2, VCC, B4, A4, B3, A3
  SN74AC08N_AND sn74ac08n_and_1 (
    .Y1(ePCH), .Y2(ePCL), .A1(tPCH), .B1(eCPC), .A2(tPCL), .B2(eCPC));  // open: GND, Y4, Y3, VCC, B4, A4, B3, A3
  SN74AC08N_AND sn74ac08n_and_2 (
    .Y1(tMBOE), .Y4(eIRQ), .Y3(tHIRQ), .A1(B_FULL), .B1(MREAD_t), .B4(ntINTP), .A4(IRQE), .B3(eIRQ), .A3(HIRQ));  // open: Y2, GND, A2, B2, VCC
  SN74AC04N_NOT sn74ac04n_not_1 (
    .Y1(ntEQUAL), .Y3(nB_FULL), .Y6(ntINTP), .A1(F_BUS[2]), .A3(B_FULL), .A6(INTP));  // open: Y2, GND, Y4, Y5, A2, VCC, A4, A5
  assign DAT_OUT = MWRITE ? controlled_buffer_3_out : 8'bz;  // Controlled_Buffer controlled_buffer_2
  assign controlled_buffer_3_out = not_1_out ? controlled_buffer_1_out : 8'bz;  // Controlled_Buffer controlled_buffer_3
  Scheduler scheduler_1 (
    .Vcc(VCC), .CLOCK(PCS), .MBUS_OE(tMBOE), .STB_BUFF(nB_FULL), .DATIN(controlled_buffer_3_out),
    .CLR_BUFF(CLBB), .ARG1_E(eARG1), .ARG2_E(eARG2), .S_IRQ(INT), .H_IRQ(tHIRQ), .C_IRQ(CIRQ), .NMI(NMI),
    .C_NMI(CNMI), .RST(tRST), .C_RST(CRST), .DBU_TRUE(DBOT), .CLR(TEMP_STOP_OSCILLATION), .MBUS_DOUT(D_BUS),
    .INSTRUCTION(INST_BUS), .ARG_8(D_BUS), .ARG_16(AD16_BUS), .REG_ADD(RAD_BUS), .ALU_OPC(AOPC_BUS),
    .IRT_VAL(IRTV_BUS), .RDY(IB_RDY), .BUFF_FULL(B_FULL), .ERR(eERR), .RST_T(tRST), .IRQ_T(tIRQ),
    .NMI_T(tNMI), .AFULL(AFULL), .UUSD(eUUSD), .GND(GND));
  ALU alu_1 (
    .CLOCK(PCS), .VCC(VCC), .RRES(RRES), .R_FLGS(eWFLG), .LD_XF(LD_XF), .LDY(LDY), .AOPC(AOPC_BUS),
    .FDIN(F_BUS), .DIN(D_BUS), .FOUT(F_BUS), .DOUT(D_BUS), .GND(GND));
  REGISTERS registers_1 (
    .CLOCK(PCS), .VCC(VCC), .WRITE(RWRITE), .READ(RREAD), .ADDRESS(RAD_BUS), .DAT_IN(D_BUS), .RHL(eRHL),
    .FLG_IN(F_BUS), .EFIN(eWFLG), .DAT_OUT(D_BUS), .HL_OUT(AD16_BUS), .F_OUT(F_BUS), .GND(GND));
  AUX_Registers aux_registers_1 (
    .VCC(VCC), .CLOCK(PCS), .RESET(CRST), .PC_DATIN(AD16_BUS), .DAT_IN(D_BUS), .ePCH(ePCH), .ePCL(ePCL),
    .eSP(eSP), .I_LD(I_LD), .READ(ARREAD), .READ_CST(CST_READ),
    .CSTAD_DAT({CST_AD4, CST_AD3, CST_AD2, CST_AD1}), .ADDRESS_16BIT(AD16_BUS), .PC8_OUT(D_BUS), .GND(GND));
  or or_1 (or_1_out, TEMP_STOP_OSCILLATION, IRT);
  SN74AC573N_Latch sn74ac573n_latch_1 (
    .GND(GND), .O1(D_BUS[0]), .O2(D_BUS[1]), .O3(D_BUS[2]), .O4(D_BUS[3]), .O8(D_BUS[4]), .O7(D_BUS[5]),
    .O6(D_BUS[6]), .O5(D_BUS[7]), .NOE(nDB_PLL), .I1(D_BUS[0]), .I2(D_BUS[1]), .I3(D_BUS[2]), .I4(D_BUS[3]),
    .I5(D_BUS[4]), .I6(D_BUS[5]), .I7(D_BUS[6]), .I8(D_BUS[7]), .VCC_5V(VCC), .LE(DB_PSH));
  CPU_CLOCK cpu_clock_1 (.Vcc(VCC), .I_CLOCK(clock_1_out), .O_CLOCK(E_CLOCK), .H_IN(tHLT), .CLOCK_OUT(PCS), .GND(GND));
  Status_Transceiver status_transceiver_1 (
    .VCC(VCC), .CLOCK(PCS), .RESET(CRST), .INTP_D(AFULL), .IRQE_D(IRTV_BUS), .ERR(eERR), .UN_D(eUUSD),
    .INTP_E(AFULL), .IRQE_E(or_1_out), .RESET_CPU(RST), .HALT(HALT), .GND(GND), .INTP(INTP), .IRQE(IRQE),
    .ERROR(ERR), .UUSD(UUSD), .RSTCPU(tRST), .HALT_OUT(tHLT));  // open: VCC_OUT
  assign controlled_buffer_4_out = IOREAD ? IO_DATIN : 8'bz;  // Controlled_Buffer controlled_buffer_4
  assign IODAT = IOWRITE ? D_BUS : 8'bz;  // Controlled_Buffer controlled_buffer_5
  assign D_BUS = IOREAD ? controlled_buffer_4_out : 8'bz;  // Controlled_Buffer controlled_buffer_6
  Addresser addresser_1 (
    .Vcc(VCC), .CLOCK(PCS), .BIT16_D(AD16_BUS), .READ(MREAD_t), .WRITE(MWRITE_t), .DATIN(D_BUS),
    .WOUT(MWRITE), .ROUT(MREAD), .ADOUT(ADD_OUT), .DOUT(controlled_buffer_3_out), .GND(GND));
  Instruction_Decoder instruction_decoder_1 (
    .VCC(VCC), .CLOCK(PCS), .INST_IN(INST_BUS), .EXEC(B_FULL), .RST_DCR(IB_RDY), .IRQ(tIRQ), .NMI(tNMI),
    .RST_CPU(tRST), .AFULL_IN(AFULL), .CLR_BF(CLBB), .CIRQ(CIRQ), .CNMI(CNMI), .CRST(CRST), .eARG1(eARG1),
    .eARG2(eARG2), .RRES(RRES), .LD_XF(LD_XF), .LDY(LDY), .RREAD(RREAD), .RWRITE(RWRITE), .eRHL(eRHL),
    .eWFLG(eWFLG), .ARREAD(ARREAD), .PCH(tPCH), .PCL(tPCL), .ESP(eSP), .I_LD(I_LD), .DB_PSH(DB_PSH),
    .nDB_PLL(nDB_PLL), .MREAD(MREAD_t), .MWRITE(MWRITE_t), .INT(INT), .IRT(IRT), .IOB_IN(IOREAD),
    .IOB_OUT(IOWRITE), .DBOT(DBOT), .ntJNE(ntJNE), .CST_READ(CST_READ), .CST_AD1(CST_AD1), .CST_AD2(CST_AD2),
    .CST_AD3(CST_AD3), .CST_AD4(CST_AD4), .GND(GND));

  // Other names for the same wires on the sheet: ECLK = E_CLOCK; tEQUAL = F_BUS[2]; HIRQ_IN = HIRQ; HLT_IN = HALT;
  //   iCLK = PCS; IOBIN = IOREAD; IOBOUT = IOWRITE; IODATIN[7:0] = IO_DATIN; MWRITE_OUT = MWRITE; RST_IN = RST;
  //   tERR = ERR; tINTP = INTP; tIRQE = IRQE; tUUSD = UUSD

  // Notes on the sheet:
  //   Tranceiver =>
  //   STS_TRSCVR =>
  //   STS_TRSCVR =>
  //   ADDDRESSER =>
  //   ALU =>
  //   ID =>
  //   <= ADDDRESSER
  //   Tranceiver =>
endmodule

module REGISTERS (
  input  CLOCK,
  input  VCC,
  input  WRITE,
  input  READ,
  input  [2:0] ADDRESS,
  input  [7:0] DAT_IN,
  input  RHL,
  input  [7:0] FLG_IN,
  input  EFIN,
  output [7:0] DAT_OUT,
  output [15:0] HL_OUT,
  output [7:0] F_OUT,
  output GND
);

  wire ADDA, ADDB, ADDC, ADDD, ADDE, ADDF, ADDH, ADDL, aEFIN, aLEF, aWRITE, eWRITE, FDIN1, FDIN2, FDIN3,
       FDIN4, FDIN5, FDIN6, FDIN7, FDIN8, LEA, LEB, LEC, LED, LEE, LEF, LEH, LEL, nREAD, nRHL, nWRITE, REA,
       REB, REC, RED, REE, REF, REH, REL, sn74ac04n_not_1_y5, sn74ac04n_not_1_y6, sn74ac04n_not_2_y5,
       sn74ac04n_not_4_y3, sn74ac04n_not_4_y4, sn74ac04n_not_4_y5, sn74ac08n_and_1_y3, sn74ac08n_and_1_y4,
       sn74ac08n_and_2_y3, sn74ac08n_and_2_y4, undriven, undriven_2, undriven_3, undriven_4, undriven_5;

  SN74AC08N_AND sn74ac08n_and_1 (
    .Y4(sn74ac08n_and_1_y4), .Y3(sn74ac08n_and_1_y3), .B4(WRITE), .A4(sn74ac04n_not_1_y5),
    .B3(sn74ac08n_and_1_y4), .A3(CLOCK));  // open: Y1, Y2, GND, A1, B1, A2, B2, VCC
  SN74AC04N_NOT sn74ac04n_not_1 (
    .Y4(nWRITE), .Y5(sn74ac04n_not_1_y5), .Y6(sn74ac04n_not_1_y6), .A4(sn74ac08n_and_1_y3), .A5(READ));  // open: Y1, Y2, Y3, GND, A1, A2, A3, VCC, A6
  SN74AC04N_NOT sn74ac04n_not_2 (
    .GND(GND), .Y4(nWRITE), .Y5(sn74ac04n_not_2_y5), .Y6(nRHL), .VCC(VCC), .A4(sn74ac08n_and_2_y4),
    .A5(READ), .A6(RHL));  // open: Y1, Y2, Y3, A1, A2, A3
  SN74AC08N_AND sn74ac08n_and_2 (
    .Y2(aEFIN), .GND(GND), .Y4(sn74ac08n_and_2_y4), .Y3(sn74ac08n_and_2_y3), .A2(EFIN), .B2(CLOCK),
    .VCC(VCC), .B4(sn74ac08n_and_2_y3), .A4(CLOCK), .B3(sn74ac04n_not_2_y5), .A3(WRITE));  // open: Y1, A1, B1
  // SN74AC08N_AND sn74ac08n_and_3: pin names not known
  // SN74AC04N_NOT sn74ac04n_not_3: pin names not known
  CD74AC138E_DEMUX3 cd74ac138e_demux3_1 (
    .GND(GND), .Y1(ADDA), .Y2(ADDB), .Y3(ADDC), .Y4(ADDD), .Y5(ADDE), .Y6(ADDH), .Y7(ADDL), .Y8(ADDF),
    .VCC(VCC), .A(ADDRESS[0]), .B(ADDRESS[1]), .C(ADDRESS[2]), .NE3(GND), .NE2(GND), .E1(VCC));
  SN74AC04N_NOT sn74ac04n_not_4 (
    .Y1(nREAD), .Y2(nWRITE), .Y3(sn74ac04n_not_4_y3), .GND(GND), .Y4(sn74ac04n_not_4_y4),
    .Y5(sn74ac04n_not_4_y5), .Y6(nRHL), .A1(READ), .A2(eWRITE), .A3(undriven), .VCC(VCC), .A4(undriven_4),
    .A5(undriven_3), .A6(RHL));
  SN74AC08N_AND sn74ac08n_and_4 (
    .Y1(aWRITE), .Y2(aEFIN), .GND(GND), .Y4(eWRITE), .A1(WRITE), .B1(nREAD), .A2(EFIN), .B2(CLOCK),
    .VCC(VCC), .B4(aWRITE), .A4(CLOCK));  // open: Y3, B3, A3
  SN74AC32N_OR sn74ac32n_or_1 (
    .Y1(LEF), .GND(GND), .A1(aLEF), .B1(aEFIN), .A2(undriven_2), .B2(undriven_2), .VCC(VCC), .B4(undriven_5),
    .A4(undriven_5), .B3(undriven_5), .A3(undriven_5));  // open: Y2, Y4, Y3
  SN74AC32N_OR sn74ac32n_or_2 (
    .Y1(REA), .Y2(REB), .GND(GND), .Y4(RED), .Y3(REC), .A1(ADDA), .B1(nREAD), .A2(ADDB), .B2(nREAD),
    .VCC(VCC), .B4(nREAD), .A4(ADDD), .B3(nREAD), .A3(ADDC));
  SN74AC573N_Latch AX (
    .GND(GND), .O1(DAT_OUT[0]), .O2(DAT_OUT[1]), .O3(DAT_OUT[2]), .O4(DAT_OUT[3]), .O8(DAT_OUT[6]),
    .O7(DAT_OUT[7]), .O6(DAT_OUT[4]), .O5(DAT_OUT[5]), .NOE(REA), .I1(DAT_IN[0]), .I2(DAT_IN[1]),
    .I3(DAT_IN[2]), .I4(DAT_IN[3]), .I5(DAT_IN[4]), .I6(DAT_IN[5]), .I7(DAT_IN[6]), .I8(DAT_IN[7]),
    .VCC_5V(VCC), .LE(LEA));
  SN74AC573N_Latch BX (
    .GND(GND), .O1(DAT_OUT[0]), .O2(DAT_OUT[1]), .O3(DAT_OUT[2]), .O4(DAT_OUT[3]), .O8(DAT_OUT[6]),
    .O7(DAT_OUT[7]), .O6(DAT_OUT[4]), .O5(DAT_OUT[5]), .NOE(REB), .I1(DAT_IN[0]), .I2(DAT_IN[1]),
    .I3(DAT_IN[2]), .I4(DAT_IN[3]), .I5(DAT_IN[4]), .I6(DAT_IN[5]), .I7(DAT_IN[6]), .I8(DAT_IN[7]),
    .VCC_5V(VCC), .LE(LEB));
  SN74AC573N_Latch CX (
    .GND(GND), .O1(DAT_OUT[0]), .O2(DAT_OUT[1]), .O3(DAT_OUT[2]), .O4(DAT_OUT[3]), .O8(DAT_OUT[6]),
    .O7(DAT_OUT[7]), .O6(DAT_OUT[4]), .O5(DAT_OUT[5]), .NOE(REC), .I1(DAT_IN[0]), .I2(DAT_IN[1]),
    .I3(DAT_IN[2]), .I4(DAT_IN[3]), .I5(DAT_IN[4]), .I6(DAT_IN[5]), .I7(DAT_IN[6]), .I8(DAT_IN[7]),
    .VCC_5V(VCC), .LE(LEC));
  SN74AC573N_Latch DX (
    .GND(GND), .O1(DAT_OUT[0]), .O2(DAT_OUT[1]), .O3(DAT_OUT[2]), .O4(DAT_OUT[3]), .O8(DAT_OUT[6]),
    .O7(DAT_OUT[7]), .O6(DAT_OUT[4]), .O5(DAT_OUT[5]), .NOE(RED), .I1(DAT_IN[0]), .I2(DAT_IN[1]),
    .I3(DAT_IN[2]), .I4(DAT_IN[3]), .I5(DAT_IN[4]), .I6(DAT_IN[5]), .I7(DAT_IN[6]), .I8(DAT_IN[7]),
    .VCC_5V(VCC), .LE(LED));
  CD74AC02EE4_NOR cd74ac02ee4_nor_1 (
    .Y1(LEA), .Y2(LEB), .GND(GND), .Y4(LED), .Y3(LEC), .A1(nWRITE), .B1(ADDA), .A2(nWRITE), .B2(ADDB),
    .VCC(VCC), .B4(ADDD), .A4(nWRITE), .B3(ADDC), .A3(nWRITE));
  SN74AC32N_OR sn74ac32n_or_3 (
    .Y1(REE), .Y2(REH), .GND(GND), .Y4(REF), .Y3(REL), .A1(ADDE), .B1(nREAD), .A2(ADDH), .B2(nREAD),
    .VCC(VCC), .B4(nREAD), .A4(ADDF), .B3(nREAD), .A3(ADDL));
  SN74AC573N_Latch EX (
    .GND(GND), .O1(DAT_OUT[0]), .O2(DAT_OUT[1]), .O3(DAT_OUT[2]), .O4(DAT_OUT[3]), .O8(DAT_OUT[6]),
    .O7(DAT_OUT[7]), .O6(DAT_OUT[4]), .O5(DAT_OUT[5]), .NOE(REE), .I1(DAT_IN[0]), .I2(DAT_IN[1]),
    .I3(DAT_IN[2]), .I4(DAT_IN[3]), .I5(DAT_IN[4]), .I6(DAT_IN[5]), .I7(DAT_IN[6]), .I8(DAT_IN[7]),
    .VCC_5V(VCC), .LE(LEE));
  SN74AC573N_Latch H (
    .GND(GND), .O1(DAT_OUT[0]), .O2(DAT_OUT[1]), .O3(DAT_OUT[2]), .O4(DAT_OUT[3]), .O8(DAT_OUT[6]),
    .O7(DAT_OUT[7]), .O6(DAT_OUT[4]), .O5(DAT_OUT[5]), .NOE(REH), .I1(DAT_IN[0]), .I2(DAT_IN[1]),
    .I3(DAT_IN[2]), .I4(DAT_IN[3]), .I5(DAT_IN[4]), .I6(DAT_IN[5]), .I7(DAT_IN[6]), .I8(DAT_IN[7]),
    .VCC_5V(VCC), .LE(LEH));
  SN74AC573N_Latch L (
    .GND(GND), .O1(DAT_OUT[0]), .O2(DAT_OUT[1]), .O3(DAT_OUT[2]), .O4(DAT_OUT[3]), .O8(DAT_OUT[6]),
    .O7(DAT_OUT[7]), .O6(DAT_OUT[4]), .O5(DAT_OUT[5]), .NOE(REL), .I1(DAT_IN[0]), .I2(DAT_IN[1]),
    .I3(DAT_IN[2]), .I4(DAT_IN[3]), .I5(DAT_IN[4]), .I6(DAT_IN[5]), .I7(DAT_IN[6]), .I8(DAT_IN[7]),
    .VCC_5V(VCC), .LE(LEL));
  SN74AC573N_Latch F (
    .GND(GND), .O1(DAT_OUT[0]), .O2(DAT_OUT[1]), .O3(DAT_OUT[2]), .O4(DAT_OUT[3]), .O8(DAT_OUT[6]),
    .O7(DAT_OUT[7]), .O6(DAT_OUT[4]), .O5(DAT_OUT[5]), .NOE(REF), .I1(FDIN1), .I2(FDIN2), .I3(FDIN3),
    .I4(FDIN4), .I5(FDIN5), .I6(FDIN6), .I7(FDIN7), .I8(FDIN8), .VCC_5V(VCC), .LE(LEF));
  CD74AC02EE4_NOR cd74ac02ee4_nor_2 (
    .Y1(LEE), .Y2(LEH), .GND(GND), .Y4(aLEF), .Y3(LEL), .A1(nWRITE), .B1(ADDE), .A2(nWRITE), .B2(ADDH),
    .VCC(VCC), .B4(ADDF), .A4(nWRITE), .B3(ADDL), .A3(nWRITE));
  SN74AC573N_Latch HL_H (
    .GND(GND), .O1(HL_OUT[0]), .O2(HL_OUT[1]), .O3(HL_OUT[2]), .O4(HL_OUT[3]), .O8(HL_OUT[4]),
    .O7(HL_OUT[5]), .O6(HL_OUT[6]), .O5(HL_OUT[7]), .NOE(nRHL), .I1(DAT_IN[0]), .I2(DAT_IN[1]),
    .I3(DAT_IN[2]), .I4(DAT_IN[3]), .I5(DAT_IN[4]), .I6(DAT_IN[5]), .I7(DAT_IN[6]), .I8(DAT_IN[7]),
    .VCC_5V(VCC), .LE(LEH));
  SN74AC573N_Latch HL_L (
    .GND(GND), .O1(HL_OUT[8]), .O2(HL_OUT[9]), .O3(HL_OUT[10]), .O4(HL_OUT[11]), .O8(HL_OUT[12]),
    .O7(HL_OUT[13]), .O6(HL_OUT[14]), .O5(HL_OUT[15]), .NOE(nRHL), .I1(DAT_IN[0]), .I2(DAT_IN[1]),
    .I3(DAT_IN[2]), .I4(DAT_IN[3]), .I5(DAT_IN[4]), .I6(DAT_IN[5]), .I7(DAT_IN[6]), .I8(DAT_IN[7]),
    .VCC_5V(VCC), .LE(LEL));
  SN74AC573N_Latch FB_F (
    .GND(GND), .O1(F_OUT[0]), .O2(F_OUT[1]), .O3(F_OUT[2]), .O4(F_OUT[3]), .O8(F_OUT[4]), .O7(F_OUT[5]),
    .O6(F_OUT[6]), .O5(F_OUT[7]), .NOE(EFIN), .I1(FDIN1), .I2(FDIN2), .I3(FDIN3), .I4(FDIN4), .I5(FDIN5),
    .I6(FDIN6), .I7(FDIN7), .I8(FDIN8), .VCC_5V(VCC), .LE(LEF));
  MUX_74AC11257 mux_74ac11257_1 (
    .Y1(FDIN1), .Y2(FDIN2), .GND1(GND), .GND2(GND), .GND3(GND), .GND4(GND), .Y3(FDIN3), .Y4(FDIN4),
    .nOE(GND), .nA_B(ADDF), .A1(DAT_IN[0]), .B1(FLG_IN[0]), .A2(DAT_IN[1]), .B2(FLG_IN[1]), .VCC1_5V(VCC),
    .VCC2_5V(VCC), .A3(DAT_IN[2]), .B3(FLG_IN[2]), .A4(DAT_IN[3]), .B4(FLG_IN[3]));
  MUX_74AC11257 mux_74ac11257_2 (
    .Y1(FDIN5), .Y2(FDIN6), .GND1(GND), .GND2(GND), .GND3(GND), .GND4(GND), .Y3(FDIN7), .Y4(FDIN8),
    .nOE(GND), .nA_B(ADDF), .A1(DAT_IN[4]), .B1(FLG_IN[4]), .A2(DAT_IN[5]), .B2(FLG_IN[5]), .VCC1_5V(VCC),
    .VCC2_5V(VCC), .A3(DAT_IN[6]), .B3(FLG_IN[6]), .A4(DAT_IN[7]), .B4(FLG_IN[7]));

  // Other names for the same wires on the sheet: ADD1 = ADDRESS[0]; ADD2 = ADDRESS[1]; ADD3 = ADDRESS[2]; CLK = CLOCK;
  //   IN1 = DAT_IN[0]; IN2 = DAT_IN[1]; IN3 = DAT_IN[2]; IN4 = DAT_IN[3]; IN5 = DAT_IN[4]; IN6 = DAT_IN[5];
  //   IN7 = DAT_IN[6]; IN8 = DAT_IN[7]; OUT1 = DAT_OUT[0]; OUT2 = DAT_OUT[1]; OUT3 = DAT_OUT[2]; OUT4 = DAT_OUT[3];
  //   OUT7 = DAT_OUT[4]; OUT8 = DAT_OUT[5]; OUT5 = DAT_OUT[6]; OUT6 = DAT_OUT[7]; FOUT1 = F_OUT[0]; FOUT2 = F_OUT[1];
  //   FOUT3 = F_OUT[2]; FOUT4 = F_OUT[3]; FOUT5 = F_OUT[4]; FOUT6 = F_OUT[5]; FOUT7 = F_OUT[6]; FOUT8 = F_OUT[7];
  //   FIN1 = FLG_IN[0]; FIN2 = FLG_IN[1]; FIN3 = FLG_IN[2]; FIN4 = FLG_IN[3]; FIN5 = FLG_IN[4]; FIN6 = FLG_IN[5];
  //   FIN7 = FLG_IN[6]; FIN8 = FLG_IN[7]; HL1 = HL_OUT[0]; HL2 = HL_OUT[1]; HL3 = HL_OUT[2]; HL4 = HL_OUT[3];
  //   HL5 = HL_OUT[4]; HL6 = HL_OUT[5]; HL7 = HL_OUT[6]; HL8 = HL_OUT[7]; HL9 = HL_OUT[8]; HL10 = HL_OUT[9];
  //   HL11 = HL_OUT[10]; HL12 = HL_OUT[11]; HL13 = HL_OUT[12]; HL14 = HL_OUT[13]; HL15 = HL_OUT[14];
  //   HL16 = HL_OUT[15]

  // Notes on the sheet:
  //   SN74AC573N D-LATCH: 11
  //   CD74AC138E DEMUX: 1
  //   SN74AC04N NOT: 1
  //   SN74AC08N AND: 1
  //   SN74AC32N OR: 3
  //   CD74AC02EE4 NOR: 2
  //   AREG
  //   GPU
  //   AREG
  //   AREG
  //   AREG
endmodule

module ALU (
  input  CLOCK,
  input  VCC,
  input  RRES,
  input  R_FLGS,
  input  LD_XF,
  input  LDY,
  input  [2:0] AOPC,
  input  [7:0] FDIN,
  input  [7:0] DIN,
  output [7:0] FOUT,
  output [7:0] DOUT,
  output GND
);

  wire addR1, addR2, addR3, addR4, addR5, addR6, addR7, addR8, andR1, andR2, andR3, andR4, andR5, andR6,
       andR7, andR8, BRW, BRWout, cd74ac238e_adder_1_cout, cd74ac238e_adder_2_cout,
       cd74hc85e_magcmp_1_aebout, cd74hc85e_magcmp_1_ahbout, cd74hc85e_magcmp_1_albout, CRY, CRYout, DF6,
       DF7, DF8, DX1, DX2, DX3, DX4, DX5, DX6, DX7, DX8, DXsd1, DXsd2, DXsd3, DXsd4, DXsd5, DXsd6, DXsd7,
       DXsd8, DY1, DY2, DY3, DY4, DY5, DY6, DY7, DY8, eBRWout, eCRY, eCRYout, eLD_XF, eLDY, eMUX1, eMUX2, EQ,
       EQout, eRRES, GRT, GRTout, LSS, LSSout, muxR1, muxR2, muxR3, muxR4, muxR5, muxR6, muxR7, muxR8,
       nBRWout, nCRY, nCRYout, neADC, neADD, neAND, neNOT, neOR, neSUB, nRFLG, nsdR1, nsdR2, nsdR3, nsdR4,
       nsdR5, nsdR6, nsdR7, nsdR8, orR1, orR2, orR3, orR4, orR5, orR6, orR7, orR8, sn74ac04n_not_1_y3,
       sn74ac04n_not_1_y5, sn74ac04n_not_1_y6, sn74ac08n_and_1_y4, sn74ac08n_and_4_y3, subR1, subR2, subR3,
       subR4, subR5, subR6, subR7, subR8, undriven, undriven_2, undriven_3, undriven_4, undriven_5;

  SN74AC573N_Latch F (
    .GND(GND), .O1(BRW), .O2(CRY), .O3(EQ), .O4(LSS), .O8(GRT), .O7(DF6), .O6(DF7), .O5(DF8), .NOE(GND),
    .I1(FDIN[0]), .I2(FDIN[1]), .I3(FDIN[2]), .I4(FDIN[3]), .I5(FDIN[4]), .I6(FDIN[5]), .I7(FDIN[6]),
    .I8(FDIN[7]), .VCC_5V(VCC), .LE(eLD_XF));
  SN74AC573N_Latch X (
    .GND(GND), .O1(DX1), .O2(DX2), .O3(DX3), .O4(DX4), .O8(DX5), .O7(DX6), .O6(DX7), .O5(DX8), .NOE(GND),
    .I1(DIN[0]), .I2(DIN[1]), .I3(DIN[2]), .I4(DIN[3]), .I5(DIN[4]), .I6(DIN[5]), .I7(DIN[6]), .I8(DIN[7]),
    .VCC_5V(VCC), .LE(eLD_XF));
  SN74AC573N_Latch Y (
    .GND(GND), .O1(DY1), .O2(DY2), .O3(DY3), .O4(DY4), .O8(DY5), .O7(DY6), .O6(DY7), .O5(DY8), .NOE(GND),
    .I1(DIN[0]), .I2(DIN[1]), .I3(DIN[2]), .I4(DIN[3]), .I5(DIN[4]), .I6(DIN[5]), .I7(DIN[6]), .I8(DIN[7]),
    .VCC_5V(VCC), .LE(eLDY));
  SN74AC08N_AND sn74ac08n_and_1 (
    .Y1(eLD_XF), .Y2(eLDY), .GND(GND), .Y4(sn74ac08n_and_1_y4), .A1(LD_XF), .B1(CLOCK), .A2(LDY), .B2(CLOCK),
    .VCC(VCC), .B4(neADC), .A4(neADD), .B3(undriven_2), .A3(undriven_2));  // open: Y3
  CD74AC138E_DEMUX3 cd74ac138e_demux3_1 (
    .GND(GND), .Y1(neNOT), .Y2(neAND), .Y3(neOR), .Y4(neADC), .Y5(neADD), .Y6(neSUB), .VCC(VCC), .A(AOPC[0]),
    .B(AOPC[1]), .C(AOPC[2]), .NE3(GND), .NE2(GND), .E1(VCC));  // open: Y7, Y8
  CD74AC02EE4_NOR cd74ac02ee4_nor_1 (
    .Y1(eCRY), .GND(GND), .Y4(eBRWout), .Y3(eCRYout), .A1(nCRY), .B1(neADC), .A2(undriven), .B2(undriven),
    .VCC(VCC), .B4(nBRWout), .A4(neSUB), .B3(nCRYout), .A3(sn74ac08n_and_1_y4));  // open: Y2
  SN74AC08N_AND sn74ac08n_and_2 (
    .Y1(andR1), .Y2(andR2), .GND(GND), .Y4(andR5), .Y3(andR6), .A1(DX1), .B1(DY1), .A2(DX2), .B2(DY2),
    .VCC(VCC), .B4(DY5), .A4(DX5), .B3(DY6), .A3(DX6));
  SN74AC08N_AND sn74ac08n_and_3 (
    .Y1(andR3), .Y2(andR4), .GND(GND), .Y4(andR7), .Y3(andR8), .A1(DX3), .B1(DY3), .A2(DX4), .B2(DY4),
    .VCC(VCC), .B4(DY7), .A4(DX7), .B3(DY8), .A3(DX8));
  CD74AC238E_adder cd74ac238e_adder_1 (
    .GND(GND), .S0(addR1), .S3(addR4), .Cout(cd74ac238e_adder_1_cout), .S1(addR2), .S2(addR3), .Cin(eCRY),
    .A1(DX1), .B1(DY1), .B2(DY2), .A2(DX2), .B3(DY3), .A3(DX3), .A4(DX4), .B4(DY4), .Vcc_5V(VCC));
  CD74AC238E_adder cd74ac238e_adder_2 (
    .GND(GND), .S0(nsdR1), .S3(nsdR4), .Cout(cd74ac238e_adder_2_cout), .S1(nsdR2), .S2(nsdR3), .Cin(BRW),
    .A1(DXsd1), .B1(DY1), .B2(DY2), .A2(DXsd2), .B3(DY3), .A3(DXsd3), .A4(DXsd4), .B4(DY4), .Vcc_5V(VCC));
  SN74AC08N_AND sn74ac08n_and_4 (
    .Y1(eMUX1), .Y2(eMUX2), .GND(GND), .Y3(sn74ac08n_and_4_y3), .A1(neAND), .B1(neOR), .A2(neNOT),
    .B2(sn74ac08n_and_1_y4), .VCC(VCC), .B4(sn74ac08n_and_4_y3));  // open: Y4, A4, B3, A3
  MUX_74AC11257 mux_74ac11257_1 (
    .Y1(muxR1), .Y2(muxR2), .GND1(GND), .GND2(GND), .GND3(GND), .GND4(GND), .Y3(muxR3), .Y4(muxR4),
    .nOE(eMUX1), .nA_B(neAND), .A1(andR1), .B1(orR1), .A2(andR2), .B2(orR2), .VCC1_5V(VCC), .VCC2_5V(VCC),
    .A3(andR3), .B3(orR3), .A4(andR4), .B4(orR4));
  MUX_74AC11257 mux_74ac11257_2 (
    .Y1(muxR5), .Y2(muxR6), .GND1(GND), .GND2(GND), .GND3(GND), .GND4(GND), .Y3(muxR7), .Y4(muxR8),
    .nOE(eMUX1), .nA_B(neAND), .A1(andR5), .B1(orR5), .A2(andR6), .B2(orR6), .VCC1_5V(VCC), .VCC2_5V(VCC),
    .A3(andR7), .B3(orR7), .A4(andR8), .B4(orR8));
  SN74AC32N_OR sn74ac32n_or_1 (
    .Y1(orR1), .Y2(orR2), .GND(GND), .Y4(orR5), .Y3(orR6), .A1(DX1), .B1(DY1), .A2(DX2), .B2(DY2), .VCC(VCC),
    .B4(DY5), .A4(DX5), .B3(DY6), .A3(DX6));
  SN74AC32N_OR sn74ac32n_or_2 (
    .Y1(orR3), .Y2(orR4), .GND(GND), .Y4(orR7), .Y3(orR8), .A1(DX3), .B1(DY3), .A2(DX4), .B2(DY4), .VCC(VCC),
    .B4(DY7), .A4(DX7), .B3(DY8), .A3(DX8));
  CD74AC238E_adder cd74ac238e_adder_3 (
    .GND(GND), .S0(addR5), .S3(addR8), .Cout(CRYout), .S1(addR6), .S2(addR7), .Cin(cd74ac238e_adder_1_cout),
    .A1(DX5), .B1(DY5), .B2(DY6), .A2(DX6), .B3(DY7), .A3(DX7), .A4(DX8), .B4(DY8), .Vcc_5V(VCC));
  CD74AC238E_adder cd74ac238e_adder_4 (
    .GND(GND), .S0(nsdR5), .S3(nsdR8), .Cout(BRWout), .S1(nsdR6), .S2(nsdR7), .Cin(cd74ac238e_adder_2_cout),
    .A1(DXsd5), .B1(DY5), .B2(DY6), .A2(DXsd6), .B3(DY7), .A3(DXsd7), .A4(DXsd8), .B4(DY8), .Vcc_5V(VCC));
  SN74AC04N_NOT sn74ac04n_not_1 (
    .Y1(nCRY), .Y2(eRRES), .Y3(sn74ac04n_not_1_y3), .GND(GND), .Y4(nRFLG), .Y5(sn74ac04n_not_1_y5),
    .Y6(sn74ac04n_not_1_y6), .A1(CRY), .A2(RRES), .A3(undriven_3), .VCC(VCC), .A4(R_FLGS), .A5(undriven_5),
    .A6(undriven_4));
  MUX_74AC11257 mux_74ac11257_3 (
    .Y1(muxR1), .Y2(muxR2), .GND1(GND), .GND2(GND), .GND3(GND), .GND4(GND), .Y3(muxR3), .Y4(muxR4),
    .nOE(eMUX2), .nA_B(neNOT), .A1(DXsd1), .B1(addR1), .A2(DXsd2), .B2(addR2), .VCC1_5V(VCC), .VCC2_5V(VCC),
    .A3(DXsd3), .B3(addR3), .A4(DXsd4), .B4(addR4));
  MUX_74AC11257 mux_74ac11257_4 (
    .Y1(muxR5), .Y2(muxR6), .GND1(GND), .GND2(GND), .GND3(GND), .GND4(GND), .Y3(muxR7), .Y4(muxR8),
    .nOE(eMUX2), .nA_B(neNOT), .A1(DXsd5), .B1(addR5), .A2(DXsd6), .B2(addR6), .VCC1_5V(VCC), .VCC2_5V(VCC),
    .A3(DXsd7), .B3(addR7), .A4(DXsd8), .B4(addR8));
  SN74AC04N_NOT sn74ac04n_not_2 (
    .Y1(DXsd1), .Y2(DXsd2), .Y3(DXsd3), .GND(GND), .Y4(DXsd7), .Y5(DXsd6), .Y6(DXsd5), .A1(DX1), .A2(DX2),
    .A3(DX3), .VCC(VCC), .A4(DX7), .A5(DX6), .A6(DX5));
  SN74AC04N_NOT sn74ac04n_not_3 (
    .Y1(DXsd4), .Y2(subR1), .Y3(subR2), .GND(GND), .Y4(subR6), .Y5(subR5), .Y6(DXsd8), .A1(DX4), .A2(nsdR1),
    .A3(nsdR2), .VCC(VCC), .A4(nsdR6), .A5(nsdR5), .A6(DX8));
  SN74AC04N_NOT sn74ac04n_not_4 (
    .Y1(subR3), .Y2(subR4), .Y3(nBRWout), .GND(GND), .Y4(nCRYout), .Y5(subR8), .Y6(subR7), .A1(nsdR3),
    .A2(nsdR4), .A3(BRWout), .VCC(VCC), .A4(CRYout), .A5(nsdR8), .A6(nsdR7));
  CD74HC85E_MagCMP cd74hc85e_magcmp_1 (
    .GND(GND), .AHBout(cd74hc85e_magcmp_1_ahbout), .AEBout(cd74hc85e_magcmp_1_aebout),
    .ALBout(cd74hc85e_magcmp_1_albout), .B4(DY4), .ALBin(GND), .AEBin(VCC), .AHBin(GND), .A4(DX4), .B3(DY3),
    .A3(DX3), .A2(DX2), .B2(DY2), .A1(DX1), .B1(DY1), .VCC(VCC));
  CD74HC85E_MagCMP cd74hc85e_magcmp_2 (
    .GND(GND), .AHBout(GRTout), .AEBout(EQout), .ALBout(LSSout), .B4(DY8), .ALBin(cd74hc85e_magcmp_1_albout),
    .AEBin(cd74hc85e_magcmp_1_aebout), .AHBin(cd74hc85e_magcmp_1_ahbout), .A4(DX8), .B3(DY7), .A3(DX7),
    .A2(DX6), .B2(DY6), .A1(DX5), .B1(DY5), .VCC(VCC));
  MUX_74AC11257 mux_74ac11257_5 (
    .Y1(DOUT[0]), .Y2(DOUT[1]), .GND1(GND), .GND2(GND), .GND3(GND), .GND4(GND), .Y3(DOUT[2]), .Y4(DOUT[3]),
    .nOE(eRRES), .nA_B(neSUB), .A1(subR1), .B1(muxR1), .A2(subR2), .B2(muxR2), .VCC1_5V(VCC), .VCC2_5V(VCC),
    .A3(subR3), .B3(muxR3), .A4(subR4), .B4(muxR4));
  MUX_74AC11257 mux_74ac11257_6 (
    .Y1(DOUT[4]), .Y2(DOUT[5]), .GND1(GND), .GND2(GND), .GND3(GND), .GND4(GND), .Y3(DOUT[6]), .Y4(DOUT[7]),
    .nOE(eRRES), .nA_B(neSUB), .A1(subR5), .B1(muxR5), .A2(subR6), .B2(muxR6), .VCC1_5V(VCC), .VCC2_5V(VCC),
    .A3(subR7), .B3(muxR7), .A4(subR8), .B4(muxR8));
  SN74AC573N_Latch sn74ac573n_latch_1 (
    .GND(GND), .O1(FOUT[0]), .O2(FOUT[1]), .O3(FOUT[2]), .O4(FOUT[3]), .O8(FOUT[4]), .O7(FOUT[5]),
    .O6(FOUT[6]), .O5(FOUT[7]), .NOE(nRFLG), .I1(eBRWout), .I2(eCRYout), .I3(EQout), .I4(LSSout),
    .I5(GRTout), .I6(DF6), .I7(DF7), .I8(DF8), .VCC_5V(VCC), .LE(VCC));

  // Other names for the same wires on the sheet: OP1 = AOPC[0]; OP2 = AOPC[1]; OP3 = AOPC[2]; CLK = CLOCK;
  //   R1 = DOUT[0]; R2 = DOUT[1]; R3 = DOUT[2]; R4 = DOUT[3]; R5 = DOUT[4]; R6 = DOUT[5]; R7 = DOUT[6]; R8 = DOUT[7];
  //   notR1 = DXsd1; notR2 = DXsd2; notR3 = DXsd3; notR4 = DXsd4; notR5 = DXsd5; notR6 = DXsd6; notR7 = DXsd7;
  //   notR8 = DXsd8; RFLG = R_FLGS

  // Notes on the sheet:
  //   SN74AC573N D-LATCH: 4
  //   CD74AC138E DEMUX: 1
  //   SN74AC04N NOT: 4
  //   SN74AC08N AND: 4
  //   SN74AC32N OR: 2
  //   CD74AC02EE4 NOR: 1
  //   CD74HC85E MAGCOMP: 2
  //   74AC11257 MUX: 6
  //   CD74AC238E ADDR: 4
  //   AREG
  //   STD_CPU
  //   in IB
  //   STD_CPU
  //   in IB
endmodule

module Scheduler (
  input  Vcc,
  input  CLOCK,
  input  MBUS_OE,
  input  STB_BUFF,
  input  [7:0] DATIN,
  input  CLR_BUFF,
  input  ARG1_E,
  input  ARG2_E,
  input  S_IRQ,
  input  H_IRQ,
  input  C_IRQ,
  input  NMI,
  input  C_NMI,
  input  RST,
  input  C_RST,
  input  DBU_TRUE,
  input  CLR,
  output [7:0] MBUS_DOUT,
  output [7:0] INSTRUCTION,
  output [7:0] ARG_8,
  output [15:0] ARG_16,
  output [2:0] REG_ADD,
  output [2:0] ALU_OPC,
  output IRT_VAL,
  output RDY,
  output BUFF_FULL,
  output ERR,
  output RST_T,
  output IRQ_T,
  output NMI_T,
  output AFULL,
  output UUSD,
  output GND
);

  wire aARG1_E, AC3E, AG11, AG12, AG13, AG14, AG15, AG16, AG17, AG18, and_1_out, and_2_out, and_3_out,
       and_4_out, and_5_out, and_6_out, BFULL1, BFULL2, BFULL3, cCBUFF, cd74ac02ee4_nor_3_y1,
       cd74ac02ee4_nor_3_y3, cd74ac02ee4_nor_3_y4, cd74ac138e_demux3_1_y2, cd74ac138e_demux3_1_y3,
       cd74ac138e_demux3_1_y4, cd74ac163e_counter_1_qa, cd74ac163e_counter_1_qb, cHIRQ, cSIRQ, DX22, DX24,
       eARG1_E, eCBUFF, eCIRQ, eCNMI, eCOUNT, eCRST, eMBOE, eWREG1, eWREG2, eWREG3, HHdis, I0x0, I0x4, I0x5,
       mux_74ac11257_1_y4, nAC1T, nAC2T, nAC3T, nAFULL, nARG1_E, nARG2_E, ncCBUFF, nCLK, nCLR, nDBUT, nDX24,
       neCSIRQ, neHIRQ, neMBOE, neNMI, neRST, neSIRQ, neWRITE, nI8, nIFULL, nRAT, nREG1, nREG2, nREG3, nREG4,
       nSTBB, ntCBUFF, ntCSIRQ, ntHIRQ, ntSIRQ, nUUSD, nYbit, RRAD2, sn74ac00n_nand_3_y1,
       sn74ac00n_nand_4_y2, sn74ac00n_nand_4_y3, sn74ac00n_nand_5_y4, sn74ac04n_not_3_y1, sn74ac04n_not_3_y4,
       sn74ac04n_not_3_y5, sn74ac08n_and_2_y4, sn74ac32n_or_1_y4, sn74ac32n_or_2_y1, sn74hc27n_tnor_1_y2,
       sn74hc27n_tnor_2_y1, tCBUFF, tHIRQ, tIRQ, tNMI, tRST;

  not not_1 (nCLR, CLR);
  SN74AC04N_NOT sn74ac04n_not_1 (
    .Y1(nAFULL), .Y2(ncCBUFF), .Y6(nI8), .A1(AFULL), .A2(cCBUFF), .A6(INSTRUCTION[7]));  // open: Y3, GND, Y4, Y5, A3, VCC, A4, A5
  SN74AC573N_Latch DBUS (
    .GND(GND), .O1(MBUS_DOUT[0]), .O2(MBUS_DOUT[1]), .O3(MBUS_DOUT[2]), .O4(MBUS_DOUT[3]), .O8(MBUS_DOUT[4]),
    .O7(MBUS_DOUT[5]), .O6(MBUS_DOUT[6]), .O5(MBUS_DOUT[7]), .NOE(neMBOE), .I1(DATIN[0]), .I2(DATIN[1]),
    .I3(DATIN[2]), .I4(DATIN[3]), .I5(DATIN[4]), .I6(DATIN[5]), .I7(DATIN[6]), .I8(DATIN[7]), .VCC_5V(Vcc),
    .LE(neMBOE));
  SN74AC573N_Latch INST (
    .GND(GND), .O1(INSTRUCTION[0]), .O2(INSTRUCTION[1]), .O3(INSTRUCTION[2]), .O4(INSTRUCTION[3]),
    .O8(ALU_OPC[0]), .O7(ALU_OPC[1]), .O6(ALU_OPC[2]), .O5(INSTRUCTION[7]), .NOE(GND), .I1(DATIN[0]),
    .I2(DATIN[1]), .I3(DATIN[2]), .I4(DATIN[3]), .I5(DATIN[4]), .I6(DATIN[5]), .I7(DATIN[6]), .I8(DATIN[7]),
    .VCC_5V(Vcc), .LE(eWREG1));
  SN74AC573N_Latch ARG1 (
    .GND(GND), .O1(AG11), .O2(AG12), .O3(AG13), .O4(AG14), .O8(AG15), .O7(AG16), .O6(AG17), .O5(AG18),
    .NOE(GND), .I1(DATIN[0]), .I2(DATIN[1]), .I3(DATIN[2]), .I4(DATIN[3]), .I5(DATIN[4]), .I6(DATIN[5]),
    .I7(DATIN[6]), .I8(DATIN[7]), .VCC_5V(Vcc), .LE(eWREG2));
  SN74AC573N_Latch ARG2 (
    .GND(GND), .O1(ARG_16[8]), .O2(ARG_16[9]), .O3(ARG_16[10]), .O4(ARG_16[11]), .O8(ARG_16[12]),
    .O7(ARG_16[13]), .O6(ARG_16[14]), .O5(ARG_16[15]), .NOE(nARG2_E), .I1(DATIN[0]), .I2(DATIN[1]),
    .I3(DATIN[2]), .I4(DATIN[3]), .I5(DATIN[4]), .I6(DATIN[5]), .I7(DATIN[6]), .I8(DATIN[7]), .VCC_5V(Vcc),
    .LE(eWREG3));
  SN74AC04N_NOT sn74ac04n_not_2 (
    .Y1(nARG1_E), .Y2(nARG2_E), .Y3(nDBUT), .GND(GND), .Y4(nCLK), .Y5(neMBOE), .Y6(nSTBB), .A1(aARG1_E),
    .A2(ARG2_E), .A3(DBU_TRUE), .VCC(Vcc), .A4(CLOCK), .A5(eMBOE), .A6(STB_BUFF));
  MUX_74AC11257 mux_74ac11257_1 (
    .Y1(REG_ADD[0]), .Y2(REG_ADD[1]), .GND1(GND), .GND2(GND), .GND3(GND), .GND4(GND), .Y3(REG_ADD[2]),
    .Y4(mux_74ac11257_1_y4), .nOE(GND), .nA_B(RRAD2), .A1(INSTRUCTION[0]), .B1(AG16), .A2(INSTRUCTION[1]),
    .B2(AG17), .VCC1_5V(Vcc), .VCC2_5V(Vcc), .A3(INSTRUCTION[2]), .B3(AG18), .A4(GND), .B4(GND));
  // NoConnect on mux_74ac11257_1_y4
  SN74AC32N_OR sn74ac32n_or_1 (
    .Y1(cSIRQ), .Y2(cHIRQ), .GND(GND), .Y4(sn74ac32n_or_1_y4), .Y3(neWRITE), .A1(ntCSIRQ), .B1(eCIRQ),
    .A2(eCIRQ), .B2(ntHIRQ), .VCC(Vcc), .B4(nSTBB), .A4(BUFF_FULL), .B3(sn74ac32n_or_1_y4), .A3(nCLK));
  CD74AC02EE4_NOR cd74ac02ee4_nor_1 (
    .Y1(eWREG1), .Y2(eWREG2), .GND(GND), .Y4(eWREG3), .Y3(BFULL1), .A1(neWRITE), .B1(nREG1), .A2(neWRITE),
    .B2(nREG2), .VCC(Vcc), .B4(neWRITE), .A4(nREG3), .B3(nREG2), .A3(nAC1T));
  CD74AC02EE4_NOR cd74ac02ee4_nor_2 (
    .Y1(eCOUNT), .Y2(RDY), .GND(GND), .Y4(BFULL2), .Y3(BFULL3), .A1(ERR), .B1(BUFF_FULL), .A2(nREG1),
    .B2(BUFF_FULL), .VCC(Vcc), .B4(nREG3), .A4(nAC2T), .B3(nREG4), .A3(nAC3T));
  SN74AC573N_Latch ARG1_8bit (
    .GND(GND), .O1(ARG_8[0]), .O2(ARG_8[1]), .O3(ARG_8[2]), .O4(ARG_8[3]), .O8(ARG_8[4]), .O7(ARG_8[5]),
    .O6(ARG_8[6]), .O5(ARG_8[7]), .NOE(nARG1_E), .I1(AG11), .I2(AG12), .I3(AG13), .I4(AG14), .I5(AG15),
    .I6(AG16), .I7(AG17), .I8(AG18), .VCC_5V(Vcc), .LE(Vcc));
  SN74AC573N_Latch ARG1_16bit (
    .GND(GND), .O1(ARG_16[0]), .O2(ARG_16[1]), .O3(ARG_16[2]), .O4(ARG_16[3]), .O8(ARG_16[4]),
    .O7(ARG_16[5]), .O6(ARG_16[6]), .O5(ARG_16[7]), .NOE(nARG2_E), .I1(AG11), .I2(AG12), .I3(AG13),
    .I4(AG14), .I5(AG15), .I6(AG16), .I7(AG17), .I8(AG18), .VCC_5V(Vcc), .LE(Vcc));
  SN74AC08N_AND sn74ac08n_and_1 (
    .Y1(aARG1_E), .Y2(RRAD2), .GND(GND), .Y4(eARG1_E), .Y3(eMBOE), .A1(eARG1_E), .B1(nDBUT), .A2(eARG1_E),
    .B2(DBU_TRUE), .VCC(Vcc), .B4(nARG2_E), .A4(ARG1_E), .B3(MBUS_OE), .A3(nSTBB));
  CD74AC163E_Counter cd74ac163e_counter_1 (
    .GND(GND), .QA(cd74ac163e_counter_1_qa), .QB(cd74ac163e_counter_1_qb), .nCLR(ntCBUFF), .CLK(nCLK),
    .A(GND), .B(GND), .C(GND), .D(GND), .ENP(eCOUNT), .VCC(Vcc), .ENT(Vcc), .nLD(Vcc));  // open: RCO, QC, QD
  CD74AC02EE4_NOR cd74ac02ee4_nor_3 (
    .Y1(cd74ac02ee4_nor_3_y1), .Y2(nAC2T), .GND(GND), .Y4(cd74ac02ee4_nor_3_y4), .Y3(cd74ac02ee4_nor_3_y3),
    .A1(nI8), .B1(HHdis), .A2(cd74ac02ee4_nor_3_y1), .B2(sn74ac04n_not_3_y1), .VCC(Vcc), .B4(nDX24),
    .A4(I0x0), .B3(I0x5), .A3(nYbit));
  SN74AC32N_OR sn74ac32n_or_2 (
    .Y1(sn74ac32n_or_2_y1), .Y2(nAC3T), .GND(GND), .Y4(ERR), .Y3(nAC1T), .A1(nYbit), .B1(I0x4), .A2(AC3E),
    .B2(nYbit), .VCC(Vcc), .B4(cd74ac02ee4_nor_3_y4), .A4(cd74ac02ee4_nor_3_y3), .B3(sn74ac04n_not_3_y5),
    .A3(sn74ac04n_not_3_y4));
  SN74AC04N_NOT sn74ac04n_not_3 (
    .Y1(sn74ac04n_not_3_y1), .Y2(nYbit), .Y3(nDX24), .GND(GND), .Y4(sn74ac04n_not_3_y4),
    .Y5(sn74ac04n_not_3_y5), .Y6(UUSD), .A1(sn74ac32n_or_2_y1), .A2(INSTRUCTION[3]), .A3(DX24), .VCC(Vcc),
    .A4(nAC3T), .A5(nAC2T), .A6(nUUSD));
  SN74HC27N_TNOR sn74hc27n_tnor_1 (
    .GND(GND), .Y1(nRAT), .Y2(sn74hc27n_tnor_1_y2), .Y3(nIFULL), .A1(INSTRUCTION[0]), .B1(INSTRUCTION[1]),
    .C1(INSTRUCTION[2]), .A2(ALU_OPC[0]), .B2(ALU_OPC[1]), .C2(ALU_OPC[2]), .A3(BFULL3), .B3(BFULL2),
    .C3(BFULL1), .VCC(Vcc));
  SN74AC08N_AND sn74ac08n_and_2 (
    .Y1(HHdis), .Y2(nUUSD), .GND(GND), .Y4(sn74ac08n_and_2_y4), .Y3(AC3E), .A1(sn74hc27n_tnor_1_y2),
    .B1(nYbit), .A2(DX22), .B2(DX24), .VCC(Vcc), .B4(cd74ac138e_demux3_1_y4), .A4(cd74ac138e_demux3_1_y3),
    .B3(sn74ac08n_and_2_y4), .A3(cd74ac138e_demux3_1_y2));
  CD74AC138E_DEMUX3 cd74ac138e_demux3_1 (
    .GND(GND), .Y1(I0x0), .Y2(cd74ac138e_demux3_1_y2), .Y3(cd74ac138e_demux3_1_y3),
    .Y4(cd74ac138e_demux3_1_y4), .Y5(I0x4), .Y6(I0x5), .VCC(Vcc), .A(ALU_OPC[0]), .B(ALU_OPC[1]),
    .C(ALU_OPC[2]), .NE3(GND), .NE2(INSTRUCTION[7]), .E1(Vcc));  // open: Y7, Y8
  CD74AC139E_DEMUX2 cd74ac139e_demux2_1 (
    .out_15(nREG4), .out_9(DX22), .out_11(DX24), .out_12(nREG1), .out_13(nREG2), .out_14(nREG3), .GND(GND),
    .VCC(Vcc), .nG1(I0x0), .A1(nRAT), .B1(INSTRUCTION[3]), .nG2(GND), .A2(cd74ac163e_counter_1_qa),
    .B2(cd74ac163e_counter_1_qb));  // open: out_8, out_10
  SN74AC00N_NAND sn74ac00n_nand_1 (
    .Y1(BUFF_FULL), .Y2(eCNMI), .GND(GND), .Y4(eCIRQ), .Y3(eCRST), .A1(nAFULL), .B1(nIFULL), .A2(CLOCK),
    .B2(C_NMI), .VCC(Vcc), .B4(CLOCK), .A4(C_IRQ), .B3(CLOCK), .A3(C_RST));
  SN74AC00N_NAND sn74ac00n_nand_2 (
    .Y1(neSIRQ), .Y2(neNMI), .GND(GND), .Y4(neHIRQ), .Y3(neRST), .A1(S_IRQ), .B1(CLOCK), .A2(NMI),
    .B2(CLOCK), .VCC(Vcc), .B4(H_IRQ), .A4(CLOCK), .B3(RST), .A3(CLOCK));
  SN74AC00N_NAND sn74ac00n_nand_3 (
    .Y1(sn74ac00n_nand_3_y1), .Y2(ntSIRQ), .GND(GND), .Y4(tHIRQ), .Y3(ntHIRQ), .A1(ntSIRQ), .B1(neSIRQ),
    .A2(sn74ac00n_nand_3_y1), .B2(and_1_out), .VCC(Vcc), .B4(ntHIRQ), .A4(neHIRQ), .B3(tHIRQ), .A3(and_4_out));
  and and_1 (and_1_out, cSIRQ, nCLR);
  SN74AC00N_NAND sn74ac00n_nand_4 (
    .Y1(tNMI), .Y2(sn74ac00n_nand_4_y2), .GND(GND), .Y4(tRST), .Y3(sn74ac00n_nand_4_y3),
    .A1(sn74ac00n_nand_4_y2), .B1(neNMI), .A2(tNMI), .B2(and_2_out), .VCC(Vcc), .B4(sn74ac00n_nand_4_y3),
    .A4(neRST), .B3(tRST), .A3(and_5_out));
  and and_2 (and_2_out, eCNMI, nCLR);
  SN74AC00N_NAND sn74ac00n_nand_5 (
    .Y1(tCBUFF), .Y2(ntCBUFF), .GND(GND), .Y4(sn74ac00n_nand_5_y4), .Y3(ntCSIRQ), .A1(ntCBUFF), .B1(eCBUFF),
    .A2(tCBUFF), .B2(and_3_out), .VCC(Vcc), .B4(ntCSIRQ), .A4(neCSIRQ), .B3(sn74ac00n_nand_5_y4),
    .A3(and_6_out));
  and and_3 (and_3_out, ncCBUFF, nCLR);
  SN74AC00N_NAND sn74ac00n_nand_6 (
    .Y1(eCBUFF), .GND(GND), .Y4(neCSIRQ), .Y3(tIRQ), .A1(CLR_BUFF), .B1(CLOCK), .VCC(Vcc), .B4(ntHIRQ),
    .A4(nCLK), .B3(ntHIRQ), .A3(ntSIRQ));  // open: Y2, A2, B2
  SN74HC27N_TNOR sn74hc27n_tnor_2 (
    .GND(GND), .Y1(sn74hc27n_tnor_2_y1), .Y2(cCBUFF), .Y3(AFULL), .A1(tIRQ), .B1(tNMI), .C1(tRST), .A2(nCLK),
    .B2(CLR_BUFF), .C2(ntCBUFF), .A3(GND), .B3(nREG1), .C3(sn74hc27n_tnor_2_y1), .VCC(Vcc));
  SN74AC08N_AND sn74ac08n_and_3 (
    .Y1(IRQ_T), .Y2(NMI_T), .GND(GND), .Y4(RST_T), .A1(AFULL), .B1(tIRQ), .A2(AFULL), .B2(tNMI), .VCC(Vcc),
    .B4(AFULL), .A4(tRST));  // open: Y3, B3, A3
  and and_4 (and_4_out, cHIRQ, nCLR);
  and and_5 (and_5_out, eCRST, nCLR);
  and and_6 (and_6_out, ntHIRQ, nCLR);

  assign INSTRUCTION[6:4] = ALU_OPC;
  assign IRT_VAL = INSTRUCTION[0];

  // Other names for the same wires on the sheet: I5 = ALU_OPC[0]; I6 = ALU_OPC[1]; I7 = ALU_OPC[2]; AG118 = ARG_8[0];
  //   AG128 = ARG_8[1]; AG138 = ARG_8[2]; AG148 = ARG_8[3]; AG158 = ARG_8[4]; AG168 = ARG_8[5]; AG178 = ARG_8[6];
  //   AG188 = ARG_8[7]; AG1116 = ARG_16[0]; AG1216 = ARG_16[1]; AG1316 = ARG_16[2]; AG1416 = ARG_16[3];
  //   AG1516 = ARG_16[4]; AG1616 = ARG_16[5]; AG1716 = ARG_16[6]; AG1816 = ARG_16[7]; AG21 = ARG_16[8];
  //   AG22 = ARG_16[9]; AG23 = ARG_16[10]; AG24 = ARG_16[11]; AG25 = ARG_16[12]; AG26 = ARG_16[13]; AG27 = ARG_16[14];
  //   AG28 = ARG_16[15]; BFULL = BUFF_FULL; CBUFF = CLR_BUFF; CIRQ = C_IRQ; CLK = CLOCK; CNMI = C_NMI; CRST = C_RST;
  //   DIN1 = DATIN[0]; DIN2 = DATIN[1]; DIN3 = DATIN[2]; DIN4 = DATIN[3]; DIN5 = DATIN[4]; DIN6 = DATIN[5];
  //   DIN7 = DATIN[6]; DIN8 = DATIN[7]; DBUT = DBU_TRUE; HIRQ = H_IRQ; Illegal = ERR; I1 = INSTRUCTION[0];
  //   RADI1 = INSTRUCTION[0]; I2 = INSTRUCTION[1]; RADI2 = INSTRUCTION[1]; I3 = INSTRUCTION[2];
  //   RADI3 = INSTRUCTION[2]; I4 = INSTRUCTION[3]; I8 = INSTRUCTION[7]; IRQo = IRQ_T; MBOE = MBUS_OE;
  //   DB1 = MBUS_DOUT[0]; DB2 = MBUS_DOUT[1]; DB3 = MBUS_DOUT[2]; DB4 = MBUS_DOUT[3]; DB5 = MBUS_DOUT[4];
  //   DB6 = MBUS_DOUT[5]; DB7 = MBUS_DOUT[6]; DB8 = MBUS_DOUT[7]; NMIo = NMI_T; RADA1 = AG16; RADA2 = AG17;
  //   RADA3 = AG18; RAD1 = REG_ADD[0]; RAD2 = REG_ADD[1]; RAD3 = REG_ADD[2]; RSTo = RST_T; SIRQ = S_IRQ;
  //   STBB = STB_BUFF

  // Notes on the sheet:
  //   SN74AC573N D-LATCH: 6
  //   CD74AC138E DEMUX: 1
  //   SN74AC04N NOT: 2
  //   SN74AC08N AND: 3
  //   SN74AC32N OR: 2
  //   CD74AC02EE4 NOR: 3
  //   Comes from the ALU =>
  //   CD74HC85E MAGCOMP: 0
  //   74AC11257 MUX: 1
  //   CD74AC238E ADDR: 0
  //   CD74HC27N TNOR: 2
  //   CD74AC139E DEMUX2: 1
  //   CD74AC163E COUNTER: 1
  //   SN74AC00N NAND: 6
endmodule

module Instruction_Decoder (
  input  VCC,
  input  CLOCK,
  input  [7:0] INST_IN,
  input  EXEC,
  input  RST_DCR,
  input  IRQ,
  input  NMI,
  input  RST_CPU,
  input  AFULL_IN,
  output CLR_BF,
  output CIRQ,
  output CNMI,
  output CRST,
  output eARG1,
  output eARG2,
  output RRES,
  output LD_XF,
  output LDY,
  output RREAD,
  output RWRITE,
  output eRHL,
  output eWFLG,
  output ARREAD,
  output PCH,
  output PCL,
  output ESP,
  output I_LD,
  output DB_PSH,
  output nDB_PLL,
  output MREAD,
  output MWRITE,
  output INT,
  output IRT,
  output IOB_IN,
  output IOB_OUT,
  output DBOT,
  output ntJNE,
  output CST_READ,
  output CST_AD1,
  output CST_AD2,
  output CST_AD3,
  output CST_AD4,
  output GND
);

  wire cd74ac163e_counter_1_qc, cd74ac163e_counter_1_qd, cd74ac163e_counter_1_rco, CT1, CT2, eCBUFF, nAFIN,
       nCLK, nRST_DCR, sn74ac04n_not_1_y3, sn74ac04n_not_1_y5, undriven, undriven_2;

  CD74AC163E_Counter cd74ac163e_counter_1 (
    .GND(GND), .RCO(cd74ac163e_counter_1_rco), .QA(CT1), .QB(CT2), .QC(cd74ac163e_counter_1_qc),
    .QD(cd74ac163e_counter_1_qd), .nCLR(nRST_DCR), .CLK(nCLK), .A(GND), .B(GND), .C(GND), .D(GND),
    .ENP(EXEC), .VCC(VCC), .ENT(VCC), .nLD(VCC));
  SN74AC04N_NOT sn74ac04n_not_1 (
    .Y1(nCLK), .Y2(nRST_DCR), .Y3(sn74ac04n_not_1_y3), .GND(GND), .Y5(sn74ac04n_not_1_y5), .Y6(nAFIN),
    .A1(CLOCK), .A2(RST_DCR), .A3(undriven), .VCC(VCC), .A5(undriven_2), .A6(AFULL_IN));  // open: Y4, A4
  SN74AC08N_AND sn74ac08n_and_1 (
    .Y1(CIRQ), .Y2(CNMI), .GND(GND), .Y4(CLR_BF), .Y3(CRST), .A1(eCBUFF), .B1(IRQ), .A2(eCBUFF), .B2(NMI),
    .VCC(VCC), .B4(nAFIN), .A4(eCBUFF), .B3(RST_CPU), .A3(eCBUFF));
  // NoConnect on cd74ac163e_counter_1_rco
  // NoConnect on cd74ac163e_counter_1_qc
  // NoConnect on cd74ac163e_counter_1_qd
  PLA #(.in_width(11), .out_width(30), .\table ("10000000100 000001000000010000000000000001 # NOP\n10000001000 000001000000110000000110000001 # LDB HL\n10000001100 000001000000110000000010000101 # LDB 16\n10000010000 000000000000010101100100000001 # JNE HL\n10000010100 000000000000010101100000000101 # JNE 16\n10000011000 000001000001010000000101000001 # STB HL\n10000011100 000001000001010000000001000101 # STB 16\n10000100000 000001000001010010010001000001 # PUSH reg\n10000100100 000001000001010010010000000011 # PUSH 8\n10000101000 000001000000110110010010000001 # POP reg\n10000110000 000001001000010000000010000001 # INB reg\n10000110100 000001010000010000000001000001 # OUB reg\n10000111000 000001000010010000000000000001 # INT\n10000111100 000001000100010000000000000001 # IRT\n10001000000 000001000000010000000001010000 # NOT reg 0\n10001000001 000001000000010000001010001001 # NOT reg 1\n10001000100 000001000000010000000001010000 # NOT reg reg 0\n10001000101 000001100000010000001010001011 # NOT reg reg 1\n10001xxxx00 000001000000010000000001010000 # ART 0\n10001xxx001 000001100000010000000001100010 # ART reg 1\n10001xxxx10 000001100000010000001010001011 # ART 2\n10001xxx101 000001000000010000000000100010 # ART 8 1\n10001110x10 000001000000010000001000000001 # CMP 2\n10001001000 000001000000011000000001000000 # MVB reg 0\n10001111001 000001100000000000000010000011 # MVB reg 1\n10001111100 000001000000010000000010000011 # MVB 8\n1001xxxxx00 000001000001010011010000000000 # IRQ 0\n1001xxxxx01 000001000001010010110000000000 # IRQ 1\n1001xxxxx10 101011000000110101000000000000 # IRQ 2\n1001xxxxx11 101111000000110100100000000001 # IRQ 3\n1010xxxxx00 000001000001010011010000000000 # NMI 0\n1010xxxxx01 000001000001010010110000000000 # NMI 1\n1010xxxxx10 110011000000110101000000000000 # NMI 2\n1010xxxxx11 110111000000110100100000000001 # NMI 3\n11xxxxxxx00 111011000000110101000000000000 # RST0\n11xxxxxxx01 111111000000110100100000000001 # RST1\n0xxxxxxxxxx 000001000000110001110000000000 # FNINST")) num3 (
    .in({EXEC, RST_CPU, NMI, IRQ, INST_IN[7:3], CT2, CT1}),
    .out({CST_AD4, CST_AD3, CST_AD2, CST_AD1, CST_READ, ntJNE, DBOT, IOB_OUT, IOB_IN, IRT, INT, MWRITE, MREAD, nDB_PLL, DB_PSH, I_LD, ESP, PCL, PCH, ARREAD, eWFLG, eRHL, RWRITE, RREAD, LDY, LD_XF, RRES, eARG2, eARG1, eCBUFF}));

  // Other names for the same wires on the sheet: IRQ_IN = IRQ; NMI_IN = NMI; RST_IN = RST_CPU; AFIN = AFULL_IN;
  //   CB_IRQ = CIRQ; CB_NMI = CNMI; CB_RST = CRST; CLK = CLOCK; sCBUFF = CLR_BF

  // Notes on the sheet:
  //   CD74AC138E DEMUX: 0
  //   SN74AC04N NOT: 1
  //   SN74AC08N AND: 1
  //   SN74AC32N OR: 0
  //   CD74AC02EE4 NOR: 0
  //   SN74AC573N D-LATCH: 0
  //   CD74AC238E ADDR: 0
  //   ATF22V10C CPLD: 3
  //   CD74HC85E MAGCOMP: 0
  //   74AC11257 MUX: 0
  //   AREG
  //   CD74HC27N TNOR: 0
  //   CD74AC139E DEMUX2: 0
  //   CD74AC163E COUNTER: 1
  //   SN74AC00N NAND: 0
  //   Cannot find suitable EEPROMs => to be resolved
  //   STD_CPU
  //   Unfortunately, it is too complicated (and big) to make a decoder without an (E)EPROM. However, the silicon based one will not use an EEPROM but an integrated Logic Array.
endmodule

module AUX_Registers (
  input  VCC,
  input  CLOCK,
  input  RESET,
  input  [15:0] PC_DATIN,
  input  [7:0] DAT_IN,
  input  ePCH,
  input  ePCL,
  input  eSP,
  input  I_LD,
  input  READ,
  input  READ_CST,
  input  [3:0] CSTAD_DAT,
  output [15:0] ADDRESS_16BIT,
  output [7:0] PC8_OUT,
  output GND
);

  wire cd74ac163e_counter_1_rco, cd74ac163e_counter_5_rco, cd74ac238e_adder_1_cout, cd74ac238e_adder_2_cout,
       DIN1, DIN2, DIN3, DIN4, DIN5, DIN6, DIN7, DIN8, dpRCOi1, dpRCOi2, dpRCOi3, dpRCOo1, dpRCOo2, dpRCOo3,
       dsp1, dsp2, dsp3, dsp4, dsp5, dsp6, dsp7, dsp8, ePC_t, ePCH_t, ePCL_t, LD16, nCLK, nDSP, ndsp1, ndsp2,
       ndsp3, ndsp4, ndsp5, ndsp6, ndsp7, ndsp8, nePC, nePCRHL, neSPR, nILD, nLD16, nLDPCh, nLDPCl, nPCRH,
       nPCRHL, nPCRL, nRCST, nRST, nsp1, nsp2, nsp3, nsp4, nsp5, nsp6, nsp7, nsp8, nSPR, ntPCRHL, PC1, PC2,
       PC3, PC4, PC5, PC6, PC7, PC8, PC9, PC10, PC11, PC12, PC13, PC14, PC15, PC16, PCI,
       sn74ac573n_latch_1_o1, sn74ac573n_latch_1_o2, sn74ac573n_latch_1_o3, sn74ac573n_latch_1_o4,
       sn74ac573n_latch_1_o5, sn74ac573n_latch_1_o6, sn74ac573n_latch_1_o7, sn74ac573n_latch_1_o8,
       sn74ac573n_latch_2_o1, sn74ac573n_latch_2_o2, sn74ac573n_latch_2_o3, sn74ac573n_latch_2_o4,
       sn74ac573n_latch_2_o5, sn74ac573n_latch_2_o6, sn74ac573n_latch_2_o7, sn74ac573n_latch_2_o8, sp1, sp2,
       sp3, sp4, sp5, sp6, sp7, sp8, spRCOi, spRCOo;

  SN74AC573N_Latch sn74ac573n_latch_1 (
    .GND(GND), .O1(sn74ac573n_latch_1_o1), .O2(sn74ac573n_latch_1_o2), .O3(sn74ac573n_latch_1_o3),
    .O4(sn74ac573n_latch_1_o4), .O8(sn74ac573n_latch_1_o8), .O7(sn74ac573n_latch_1_o7),
    .O6(sn74ac573n_latch_1_o6), .O5(sn74ac573n_latch_1_o5), .NOE(nLD16), .I1(PC_DATIN[12]),
    .I2(PC_DATIN[13]), .I3(PC_DATIN[14]), .I4(PC_DATIN[15]), .I5(PC_DATIN[8]), .I6(PC_DATIN[9]),
    .I7(PC_DATIN[10]), .I8(PC_DATIN[11]), .VCC_5V(VCC), .LE(VCC));
  SN74AC573N_Latch sn74ac573n_latch_2 (
    .GND(GND), .O1(sn74ac573n_latch_2_o1), .O2(sn74ac573n_latch_2_o2), .O3(sn74ac573n_latch_2_o3),
    .O4(sn74ac573n_latch_2_o4), .O8(sn74ac573n_latch_2_o8), .O7(sn74ac573n_latch_2_o7),
    .O6(sn74ac573n_latch_2_o6), .O5(sn74ac573n_latch_2_o5), .NOE(nLD16), .I1(PC_DATIN[4]), .I2(PC_DATIN[5]),
    .I3(PC_DATIN[6]), .I4(PC_DATIN[7]), .I5(PC_DATIN[0]), .I6(PC_DATIN[1]), .I7(PC_DATIN[2]),
    .I8(PC_DATIN[3]), .VCC_5V(VCC), .LE(VCC));
  SN74AC573N_Latch sn74ac573n_latch_3 (
    .GND(GND), .O1(sn74ac573n_latch_2_o1), .O2(sn74ac573n_latch_2_o2), .O3(sn74ac573n_latch_2_o3),
    .O4(sn74ac573n_latch_2_o4), .O8(sn74ac573n_latch_2_o8), .O7(sn74ac573n_latch_2_o7),
    .O6(sn74ac573n_latch_2_o6), .O5(sn74ac573n_latch_2_o5), .NOE(LD16), .I1(DIN5), .I2(DIN6), .I3(DIN7),
    .I4(DIN8), .I5(DIN1), .I6(DIN2), .I7(DIN3), .I8(DIN4), .VCC_5V(VCC), .LE(VCC));
  SN74AC04N_NOT sn74ac04n_not_1 (
    .Y1(nRCST), .Y4(nILD), .Y5(LD16), .Y6(ePC_t), .A1(READ_CST), .A4(I_LD), .A5(nLD16), .A6(nePC));  // open: Y2, Y3, GND, A2, A3, VCC
  CD74AC02EE4_NOR cd74ac02ee4_nor_1 (
    .Y1(PCI), .A1(nePC), .B1(I_LD));  // open: Y2, GND, Y4, Y3, A2, B2, VCC, B4, A4, B3, A3
  SN74AC32N_OR sn74ac32n_or_1 (
    .Y2(nPCRHL), .Y4(nSPR), .Y3(nePCRHL), .A2(nePCRHL), .B2(READ_CST), .B4(neSPR), .A4(READ_CST),
    .B3(ntPCRHL), .A3(eSP));  // open: Y1, GND, A1, B1, VCC
  SN74AC08N_AND sn74ac08n_and_1 (
    .Y1(ePCL_t), .Y3(ePCH_t), .A1(ePCL), .B1(nePC), .B3(nePC), .A3(ePCH));  // open: Y2, GND, Y4, A2, B2, VCC, B4, A4
  CD74AC163E_Counter cd74ac163e_counter_1 (
    .GND(GND), .RCO(cd74ac163e_counter_1_rco), .QA(PC13), .QB(PC14), .QC(PC15), .QD(PC16), .nCLR(VCC),
    .CLK(CLOCK), .A(sn74ac573n_latch_1_o1), .B(sn74ac573n_latch_1_o2), .C(sn74ac573n_latch_1_o3),
    .D(sn74ac573n_latch_1_o4), .ENP(dpRCOo3), .VCC(VCC), .ENT(VCC), .nLD(nLDPCh));
  CD74AC163E_Counter cd74ac163e_counter_2 (
    .GND(GND), .RCO(dpRCOi3), .QA(PC9), .QB(PC10), .QC(PC11), .QD(PC12), .nCLR(VCC), .CLK(CLOCK),
    .A(sn74ac573n_latch_1_o8), .B(sn74ac573n_latch_1_o7), .C(sn74ac573n_latch_1_o6),
    .D(sn74ac573n_latch_1_o5), .ENP(dpRCOo2), .VCC(VCC), .ENT(VCC), .nLD(nLDPCh));
  CD74AC163E_Counter cd74ac163e_counter_3 (
    .GND(GND), .RCO(dpRCOi2), .QA(PC5), .QB(PC6), .QC(PC7), .QD(PC8), .nCLR(VCC), .CLK(CLOCK),
    .A(sn74ac573n_latch_2_o1), .B(sn74ac573n_latch_2_o2), .C(sn74ac573n_latch_2_o3),
    .D(sn74ac573n_latch_2_o4), .ENP(dpRCOo1), .VCC(VCC), .ENT(VCC), .nLD(nLDPCl));
  CD74AC163E_Counter cd74ac163e_counter_4 (
    .GND(GND), .RCO(dpRCOi1), .QA(PC1), .QB(PC2), .QC(PC3), .QD(PC4), .nCLR(VCC), .CLK(CLOCK),
    .A(sn74ac573n_latch_2_o8), .B(sn74ac573n_latch_2_o7), .C(sn74ac573n_latch_2_o6),
    .D(sn74ac573n_latch_2_o5), .ENP(PCI), .VCC(VCC), .ENT(VCC), .nLD(nLDPCl));
  CD74AC163E_Counter cd74ac163e_counter_5 (
    .GND(GND), .RCO(cd74ac163e_counter_5_rco), .QA(sp5), .QB(sp6), .QC(sp7), .QD(sp8), .nCLR(nRST),
    .CLK(CLOCK), .A(dsp5), .B(dsp6), .C(dsp7), .D(dsp8), .ENP(spRCOo), .VCC(VCC), .ENT(VCC), .nLD(nDSP));
  CD74AC163E_Counter cd74ac163e_counter_6 (
    .GND(GND), .RCO(spRCOi), .QA(sp1), .QB(sp2), .QC(sp3), .QD(sp4), .nCLR(nRST), .CLK(CLOCK), .A(dsp1),
    .B(dsp2), .C(dsp3), .D(dsp4), .ENP(eSP), .VCC(VCC), .ENT(VCC), .nLD(nDSP));
  // NoConnect on cd74ac163e_counter_1_rco
  // NoConnect on cd74ac163e_counter_5_rco
  SN74AC00N_NAND sn74ac00n_nand_1 (
    .Y1(nPCRH), .Y2(nPCRL), .GND(GND), .Y4(neSPR), .A1(READ), .B1(ePCH_t), .A2(READ), .B2(ePCL_t), .VCC(VCC),
    .B4(eSP), .A4(READ));  // open: Y3, B3, A3
  SN74AC00N_NAND sn74ac00n_nand_2 (
    .Y2(nDSP), .GND(GND), .Y4(nePC), .A2(I_LD), .B2(eSP), .VCC(VCC), .B4(ePCH), .A4(ePCL));  // open: Y1, Y3, A1, B1, B3, A3
  SN74AC08N_AND sn74ac08n_and_2 (
    .Y1(spRCOo), .Y2(dpRCOo1), .GND(GND), .Y4(dpRCOo2), .Y3(dpRCOo3), .A1(eSP), .B1(spRCOi), .A2(PCI),
    .B2(dpRCOi1), .VCC(VCC), .B4(dpRCOi2), .A4(PCI), .B3(dpRCOi3), .A3(PCI));
  CD74AC238E_adder cd74ac238e_adder_1 (
    .GND(GND), .S0(ndsp5), .S3(ndsp8), .Cout(cd74ac238e_adder_1_cout), .S1(ndsp6), .S2(ndsp7),
    .Cin(cd74ac238e_adder_2_cout), .A1(nsp5), .B1(GND), .B2(GND), .A2(nsp6), .B3(GND), .A3(nsp7), .A4(nsp8),
    .B4(GND), .Vcc_5V(VCC));
  CD74AC238E_adder cd74ac238e_adder_2 (
    .GND(GND), .S0(ndsp1), .S3(ndsp4), .Cout(cd74ac238e_adder_2_cout), .S1(ndsp2), .S2(ndsp3), .Cin(VCC),
    .A1(nsp1), .B1(GND), .B2(GND), .A2(nsp2), .B3(GND), .A3(nsp3), .A4(nsp4), .B4(GND), .Vcc_5V(VCC));
  SN74AC04N_NOT sn74ac04n_not_2 (
    .Y1(nsp1), .Y2(nsp2), .Y3(nsp3), .GND(GND), .Y4(nsp7), .Y5(nsp6), .Y6(nsp5), .A1(sp1), .A2(sp2),
    .A3(sp3), .VCC(VCC), .A4(sp7), .A5(sp6), .A6(sp5));
  SN74AC04N_NOT sn74ac04n_not_3 (
    .Y1(nsp4), .Y2(dsp1), .Y3(dsp2), .GND(GND), .Y4(dsp4), .Y5(dsp3), .Y6(nsp8), .A1(sp4), .A2(ndsp1),
    .A3(ndsp2), .VCC(VCC), .A4(ndsp4), .A5(ndsp3), .A6(sp8));
  SN74AC04N_NOT sn74ac04n_not_4 (
    .Y1(dsp5), .Y2(dsp6), .Y3(nRST), .GND(GND), .Y4(nCLK), .Y5(dsp8), .Y6(dsp7), .A1(ndsp5), .A2(ndsp6),
    .A3(RESET), .VCC(VCC), .A4(CLOCK), .A5(ndsp8), .A6(ndsp7));
  // NoConnect on cd74ac238e_adder_1_cout
  SN74AC00N_NAND sn74ac00n_nand_3 (
    .Y1(nLDPCh), .Y2(nLDPCl), .GND(GND), .Y4(nLD16), .Y3(ntPCRHL), .A1(ePCH), .B1(I_LD), .A2(ePCL),
    .B2(I_LD), .VCC(VCC), .B4(ePC_t), .A4(I_LD), .B3(ePC_t), .A3(READ));
  SN74AC573N_Latch sn74ac573n_latch_4 (
    .GND(GND), .O1(ADDRESS_16BIT[0]), .O2(ADDRESS_16BIT[1]), .O3(ADDRESS_16BIT[2]), .O4(ADDRESS_16BIT[3]),
    .O8(ADDRESS_16BIT[4]), .O7(ADDRESS_16BIT[5]), .O6(ADDRESS_16BIT[6]), .O5(ADDRESS_16BIT[7]), .NOE(nPCRHL),
    .I1(PC1), .I2(PC2), .I3(PC3), .I4(PC4), .I5(PC5), .I6(PC6), .I7(PC7), .I8(PC8), .VCC_5V(VCC), .LE(nCLK));
  SN74AC573N_Latch sn74ac573n_latch_5 (
    .GND(GND), .O1(ADDRESS_16BIT[8]), .O2(ADDRESS_16BIT[9]), .O3(ADDRESS_16BIT[10]), .O4(ADDRESS_16BIT[11]),
    .O8(ADDRESS_16BIT[12]), .O7(ADDRESS_16BIT[13]), .O6(ADDRESS_16BIT[14]), .O5(ADDRESS_16BIT[15]),
    .NOE(nPCRHL), .I1(PC9), .I2(PC10), .I3(PC11), .I4(PC12), .I5(PC13), .I6(PC14), .I7(PC15), .I8(PC16),
    .VCC_5V(VCC), .LE(nCLK));
  SN74AC573N_Latch sn74ac573n_latch_6 (
    .GND(GND), .O1(PC8_OUT[0]), .O2(PC8_OUT[1]), .O3(PC8_OUT[2]), .O4(PC8_OUT[3]), .O8(PC8_OUT[4]),
    .O7(PC8_OUT[5]), .O6(PC8_OUT[6]), .O5(PC8_OUT[7]), .NOE(nPCRL), .I1(PC1), .I2(PC2), .I3(PC3), .I4(PC4),
    .I5(PC5), .I6(PC6), .I7(PC7), .I8(PC8), .VCC_5V(VCC), .LE(nCLK));
  SN74AC573N_Latch sn74ac573n_latch_7 (
    .GND(GND), .O1(PC8_OUT[0]), .O2(PC8_OUT[1]), .O3(PC8_OUT[2]), .O4(PC8_OUT[3]), .O8(PC8_OUT[4]),
    .O7(PC8_OUT[5]), .O6(PC8_OUT[6]), .O5(PC8_OUT[7]), .NOE(nPCRH), .I1(PC9), .I2(PC10), .I3(PC11),
    .I4(PC12), .I5(PC13), .I6(PC14), .I7(PC15), .I8(PC16), .VCC_5V(VCC), .LE(nCLK));
  SN74AC573N_Latch sn74ac573n_latch_8 (
    .GND(GND), .O1(ADDRESS_16BIT[0]), .O2(ADDRESS_16BIT[1]), .O3(ADDRESS_16BIT[2]), .O4(ADDRESS_16BIT[3]),
    .O8(ADDRESS_16BIT[4]), .O7(ADDRESS_16BIT[5]), .O6(ADDRESS_16BIT[6]), .O5(ADDRESS_16BIT[7]), .NOE(nSPR),
    .I1(sp1), .I2(sp2), .I3(sp3), .I4(sp4), .I5(sp5), .I6(sp6), .I7(sp7), .I8(sp8), .VCC_5V(VCC), .LE(nCLK));
  SN74AC573N_Latch sn74ac573n_latch_9 (
    .GND(GND), .O1(ADDRESS_16BIT[8]), .O2(ADDRESS_16BIT[9]), .O3(ADDRESS_16BIT[10]), .O4(ADDRESS_16BIT[11]),
    .O8(ADDRESS_16BIT[12]), .O7(ADDRESS_16BIT[13]), .O6(ADDRESS_16BIT[14]), .O5(ADDRESS_16BIT[15]),
    .NOE(nSPR), .I1(GND), .I2(VCC), .I3(VCC), .I4(VCC), .I5(VCC), .I6(VCC), .I7(VCC), .I8(VCC), .VCC_5V(VCC),
    .LE(nCLK));
  SN74AC573N_Latch sn74ac573n_latch_10 (
    .GND(GND), .O1(ADDRESS_16BIT[0]), .O2(ADDRESS_16BIT[1]), .O3(ADDRESS_16BIT[2]), .O4(ADDRESS_16BIT[3]),
    .O8(ADDRESS_16BIT[4]), .O7(ADDRESS_16BIT[5]), .O6(ADDRESS_16BIT[6]), .O5(ADDRESS_16BIT[7]), .NOE(nRCST),
    .I1(CSTAD_DAT[0]), .I2(CSTAD_DAT[1]), .I3(CSTAD_DAT[2]), .I4(CSTAD_DAT[3]), .I5(VCC), .I6(VCC), .I7(VCC),
    .I8(VCC), .VCC_5V(VCC), .LE(nCLK));
  SN74AC573N_Latch sn74ac573n_latch_11 (
    .GND(GND), .O1(ADDRESS_16BIT[8]), .O2(ADDRESS_16BIT[9]), .O3(ADDRESS_16BIT[10]), .O4(ADDRESS_16BIT[11]),
    .O8(ADDRESS_16BIT[12]), .O7(ADDRESS_16BIT[13]), .O6(ADDRESS_16BIT[14]), .O5(ADDRESS_16BIT[15]),
    .NOE(nRCST), .I1(VCC), .I2(VCC), .I3(VCC), .I4(VCC), .I5(VCC), .I6(VCC), .I7(VCC), .I8(VCC),
    .VCC_5V(VCC), .LE(nCLK));

  // Other names for the same wires on the sheet: CLK = CLOCK; CST_AD1 = CSTAD_DAT[0]; CST_AD2 = CSTAD_DAT[1];
  //   CST_AD3 = CSTAD_DAT[2]; CST_AD4 = CSTAD_DAT[3]; DIN81 = DAT_IN[0]; DIN82 = DAT_IN[1]; DIN83 = DAT_IN[2];
  //   DIN84 = DAT_IN[3]; DIN85 = DAT_IN[4]; DIN86 = DAT_IN[5]; DIN87 = DAT_IN[6]; DIN88 = DAT_IN[7]; ILD = I_LD;
  //   DAT161 = PC_DATIN[0]; DAT162 = PC_DATIN[1]; DAT163 = PC_DATIN[2]; DAT164 = PC_DATIN[3]; DAT165 = PC_DATIN[4];
  //   DAT166 = PC_DATIN[5]; DAT167 = PC_DATIN[6]; DAT168 = PC_DATIN[7]; DAT169 = PC_DATIN[8]; DAT1610 = PC_DATIN[9];
  //   DAT1611 = PC_DATIN[10]; DAT1612 = PC_DATIN[11]; DAT1613 = PC_DATIN[12]; DAT1614 = PC_DATIN[13];
  //   DAT1615 = PC_DATIN[14]; DAT1616 = PC_DATIN[15]; PCH = ePCH; PCL = ePCL; RCST = READ_CST; RST = RESET

  // Notes on the sheet:
  //   SN74AC08N AND: 2
  //   SN74AC573N D-LATCH: 11
  //   CD74AC138E DEMUX: 0
  //   SN74AC04N NOT: 3
  //   SN74AC32N OR: 0
  //   CD74AC02EE4 NOR: 0
  //   ATF22V10C CPLD: 0
  //   Taken from the ID module =>
  //   Taken from the ALU module =>
  //   Taken from the Status Module =>
  //   CD74HC85E MAGCOMP: 0
  //   74AC11257 MUX: 0
  //   CD74AC238E ADDR: 2
  //   SN74AC00N NAND: 3
  //   CD74HC27N TNOR: 0
  //   CD74AC139E DEMUX2: 0
  //   CD74AC163E COUNTER: 6
  //   ADD BUFFER/DIODE/OR/3 STATE
  //   <= Taken from the registers module
  //   <= Taken from the registers module
endmodule

module Addresser (
  input  Vcc,
  input  CLOCK,
  input  [15:0] BIT16_D,
  input  READ,
  input  WRITE,
  input  [7:0] DATIN,
  output WOUT,
  output ROUT,
  output [15:0] ADOUT,
  output [7:0] DOUT,
  output GND
);

  wire nCLK, nWRT, sn74ac04n_not_1_y5, sn74ac04n_not_1_y6, undriven, undriven_2;

  SN74AC04N_NOT sn74ac04n_not_1 (
    .Y1(nCLK), .Y2(nWRT), .Y5(sn74ac04n_not_1_y5), .Y6(sn74ac04n_not_1_y6), .A1(CLOCK), .A2(WRITE),
    .A5(undriven_2), .A6(undriven));  // open: Y3, GND, Y4, A3, VCC, A4
  SN74AC573N_Latch sn74ac573n_latch_1 (
    .GND(GND), .O1(DOUT[0]), .O2(DOUT[1]), .O3(DOUT[2]), .O4(DOUT[3]), .O8(DOUT[4]), .O7(DOUT[5]),
    .O6(DOUT[6]), .O5(DOUT[7]), .NOE(nWRT), .I1(DATIN[0]), .I2(DATIN[1]), .I3(DATIN[2]), .I4(DATIN[3]),
    .I5(DATIN[4]), .I6(DATIN[5]), .I7(DATIN[6]), .I8(DATIN[7]), .VCC_5V(Vcc), .LE(nCLK));
  // SN74AC573N_Latch sn74ac573n_latch_2: pin names not known
  // SN74AC573N_Latch sn74ac573n_latch_3: pin names not known

  assign ADOUT = BIT16_D;
  assign ROUT = READ;
  assign WOUT = WRITE;

  // Other names for the same wires on the sheet: AD1 = BIT16_D[0]; AD2 = BIT16_D[1]; AD3 = BIT16_D[2];
  //   AD4 = BIT16_D[3]; AD5 = BIT16_D[4]; AD6 = BIT16_D[5]; AD7 = BIT16_D[6]; AD8 = BIT16_D[7]; AD9 = BIT16_D[8];
  //   AD10 = BIT16_D[9]; AD11 = BIT16_D[10]; AD12 = BIT16_D[11]; AD13 = BIT16_D[12]; AD14 = BIT16_D[13];
  //   AD15 = BIT16_D[14]; AD16 = BIT16_D[15]; CLK = CLOCK; IN1 = DATIN[0]; IN2 = DATIN[1]; IN3 = DATIN[2];
  //   IN4 = DATIN[3]; IN5 = DATIN[4]; IN6 = DATIN[5]; IN7 = DATIN[6]; IN8 = DATIN[7]; OUT1 = DOUT[0]; OUT2 = DOUT[1];
  //   OUT3 = DOUT[2]; OUT4 = DOUT[3]; OUT7 = DOUT[4]; OUT8 = DOUT[5]; OUT5 = DOUT[6]; OUT6 = DOUT[7]; RED = READ;
  //   WRT = WRITE

  // Notes on the sheet:
  //   SN74AC573N D-LATCH: 1
  //   CD74AC138E DEMUX: 0
  //   SN74AC04N NOT: 1
  //   SN74AC08N AND: 0
  //   SN74AC32N OR: 0
  //   CD74AC02EE4 NOR: 0
  //   CD74HC85E MAGCOMP: 0
  //   74AC11257 MUX: 0
  //   CD74AC238E ADDR: 0
  //   ATF22V10C CPLD: 0
  //   CD74HC27N TNOR: 0
  //   CD74AC139E DEMUX2: 0
  //   CD74AC163E COUNTER: 0
  //   SN74AC00N NAND: 0
  //   STD_CPU
endmodule

module CPU_CLOCK (
  input  Vcc,
  input  I_CLOCK,
  input  O_CLOCK,
  input  H_IN,
  output CLOCK_OUT,
  output GND
);

  wire sn74ac04n_not_1_y1, sn74ac04n_not_1_y2, sn74ac08n_and_1_y1, sn74ac08n_and_1_y2, sn74ac08n_and_1_y4;

  SN74AC08N_AND sn74ac08n_and_1 (
    .Y1(sn74ac08n_and_1_y1), .Y2(sn74ac08n_and_1_y2), .GND(GND), .Y4(sn74ac08n_and_1_y4), .A1(I_CLOCK),
    .B1(sn74ac04n_not_1_y1), .A2(sn74ac04n_not_1_y2), .B2(H_IN), .VCC(Vcc), .B4(O_CLOCK),
    .A4(sn74ac08n_and_1_y2));  // open: Y3, B3, A3
  SN74AC04N_NOT sn74ac04n_not_1 (
    .Y1(sn74ac04n_not_1_y1), .Y2(sn74ac04n_not_1_y2), .GND(GND), .A1(sn74ac08n_and_1_y2),
    .A2(sn74ac08n_and_1_y1), .VCC(Vcc));  // open: Y3, Y4, Y5, Y6, A3, A4, A5, A6
  SN74AC32N_OR sn74ac32n_or_1 (
    .Y1(CLOCK_OUT), .GND(GND), .A1(sn74ac08n_and_1_y4), .B1(sn74ac08n_and_1_y1), .VCC(Vcc));  // open: Y2, Y4, Y3, A2, B2, B4, A4, B3, A3

  // Notes on the sheet:
  //   SN74AC573N D-LATCH: 0
  //   CD74AC138E DEMUX: 0
  //   SN74AC04N NOT: 1
  //   SN74AC08N AND: 1
  //   SN74AC32N OR: 1
  //   CD74AC02EE4 NOR: 0
  //   CD74HC85E MAGCOMP: 0
  //   74AC11257 MUX: 0
  //   CD74AC238E ADDR: 0
  //   ATF22V10C CPLD: 0
  //   CD74HC27N TNOR: 0
  //   CD74AC139E DEMUX2: 0
  //   CD74AC163E COUNTER: 0
  //   SN74AC00N NAND: 0
endmodule

module Status_Transceiver (
  input  VCC,
  input  CLOCK,
  input  RESET,
  input  INTP_D,
  input  IRQE_D,
  input  ERR,
  input  UN_D,
  input  INTP_E,
  input  IRQE_E,
  input  RESET_CPU,
  input  HALT,
  output GND,
  output VCC_OUT,
  output INTP,
  output IRQE,
  output ERROR,
  output UUSD,
  output RSTCPU,
  output HALT_OUT
);

  wire INTP_D_t, INTP_E_t, INTP_R, IRQE_D_t, IRQE_E_t, IRQE_R, nCLK, nINTP_D, nIRQE_D, nIRQE_E, nRST,
       sn74ac00n_nand_1_y1, sn74ac00n_nand_1_y2, sn74ac00n_nand_1_y3, sn74ac00n_nand_1_y4,
       sn74ac00n_nand_2_y2, sn74ac00n_nand_2_y3, sn74ac04n_not_1_y4, sn74ac08n_and_1_y3,
       sn74ac573n_latch_1_o5, sn74ac573n_latch_1_o6, sn74ac573n_latch_1_o7, sn74ac573n_latch_1_o8, undriven,
       undriven_2;

  SN74AC32N_OR sn74ac32n_or_1 (
    .Y1(IRQE_E_t), .Y2(INTP_E_t), .GND(GND), .A1(IRQE_E), .B1(RESET), .A2(IRQE_E_t), .B2(INTP_E), .VCC(VCC),
    .B4(undriven), .A4(undriven), .B3(undriven_2), .A3(undriven_2));  // open: Y4, Y3
  SN74AC08N_AND sn74ac08n_and_1 (
    .Y1(INTP_D_t), .Y2(IRQE_D_t), .GND(GND), .Y3(sn74ac08n_and_1_y3), .A1(INTP_D), .B1(nIRQE_E), .A2(IRQE_D),
    .B2(nRST), .VCC(VCC), .B4(sn74ac08n_and_1_y3));  // open: Y4, A4, B3, A3
  SN74AC04N_NOT sn74ac04n_not_1 (
    .Y1(nINTP_D), .Y2(nIRQE_D), .Y3(nCLK), .GND(GND), .Y4(sn74ac04n_not_1_y4), .Y5(nRST), .Y6(nIRQE_E),
    .A1(INTP_D_t), .A2(IRQE_D_t), .A3(CLOCK), .VCC(VCC), .A4(GND), .A5(RESET), .A6(IRQE_E_t));
  SN74AC00N_NAND sn74ac00n_nand_1 (
    .Y1(sn74ac00n_nand_1_y1), .Y2(sn74ac00n_nand_1_y2), .GND(GND), .Y4(sn74ac00n_nand_1_y4),
    .Y3(sn74ac00n_nand_1_y3), .A1(INTP_E_t), .B1(INTP_D_t), .A2(INTP_E_t), .B2(nINTP_D), .VCC(VCC),
    .B4(IRQE_D_t), .A4(IRQE_E_t), .B3(nIRQE_D), .A3(IRQE_E_t));
  SN74AC00N_NAND sn74ac00n_nand_2 (
    .Y1(INTP_R), .Y2(sn74ac00n_nand_2_y2), .GND(GND), .Y4(IRQE_R), .Y3(sn74ac00n_nand_2_y3),
    .A1(sn74ac00n_nand_2_y2), .B1(sn74ac00n_nand_1_y1), .A2(INTP_R), .B2(sn74ac00n_nand_1_y2), .VCC(VCC),
    .B4(sn74ac00n_nand_2_y3), .A4(sn74ac00n_nand_1_y4), .B3(IRQE_R), .A3(sn74ac00n_nand_1_y3));
  SN74AC573N_Latch sn74ac573n_latch_1 (
    .GND(GND), .O1(INTP), .O2(IRQE), .O3(ERROR), .O4(UUSD), .O8(sn74ac573n_latch_1_o8),
    .O7(sn74ac573n_latch_1_o7), .O6(sn74ac573n_latch_1_o6), .O5(sn74ac573n_latch_1_o5), .NOE(GND),
    .I1(INTP_R), .I2(IRQE_R), .I3(ERR), .I4(UN_D), .I5(GND), .I6(GND), .I7(GND), .I8(GND), .VCC_5V(VCC),
    .LE(nCLK));
  // NoConnect on sn74ac04n_not_1_y4
  // NoConnect on sn74ac573n_latch_1_o8
  // NoConnect on sn74ac573n_latch_1_o7
  // NoConnect on sn74ac573n_latch_1_o6
  // NoConnect on sn74ac573n_latch_1_o5

  assign HALT_OUT = HALT;
  assign RSTCPU = RESET_CPU;
  assign VCC_OUT = VCC;

  // Other names for the same wires on the sheet: CLK = CLOCK; IPD = INTP_D; IPE = INTP_E; IQD = IRQE_D; IQE = IRQE_E;
  //   RST = RESET

  // Notes on the sheet:
  //   AREG
  //   STD_CPU
  //   STD_CPU
  //   SN74AC573N D-LATCH: 1
  //   CD74AC138E DEMUX: 0
  //   SN74AC04N NOT: 1
  //   SN74AC08N AND: 1
  //   SN74AC32N OR: 1
  //   CD74AC02EE4 NOR: 0
  //   CD74HC85E MAGCOMP: 0
  //   74AC11257 MUX: 0
  //   CD74AC238E ADDR: 0
  //   ATF22V10C CPLD: 0
  //   CD74HC27N TNOR: 0
  //   CD74AC139E DEMUX2: 0
  //   CD74AC163E COUNTER: 0
  //   SN74AC00N NAND: 2
endmodule

module GPU (
  input  Vcc,
  input  CLK,
  input  Write_Enable,
  input  [7:0] DIN,
  input  [13:0] Address_IN
);

  wire CLK_t, eC3C, eHREAD, eREAD, eVREAD, eWDATA, eWH, eWL, GND, H200, H210, H242, H264, HC1, HC2, HC4, HC8,
       HC16, HC32, HC64, HC128, HC256, HSYNC, nCLK, nDIN5, neREAD, nH264, nHC1, nHC2, nHC4, nHC8, nHC16,
       nHC32, nVC1, nVC2, nVC4, nVC8, nVC32, pull_resistor_1_node, pull_resistor_2_node,
       pull_resistor_3_node, pull_resistor_4_node, RCO1_2, RCO2_3i, RCO2_3o, RCO3_4i, RCO3_4o, RCO4_5i,
       RCO4_5o, sn74ac00n_nand_2_y1, sn74ac00n_nand_2_y3, sn74ac00n_nand_3_y1, sn74ac00n_nand_3_y3, V600,
       V601, V605, V628, VC1, VC2, VC4, VC8, VC16, VC32, VC64, VC128, VC256, VC512, VD1A, VD1B, VD1C, VD1D,
       VD2A, VD2B, VD2C, VD2D, VSYNC, WD1, WD2, WD3, WD4, WD5, WD6, WD7, WD8;
  wire [7:0] ram_1_dout;

  Clock clock_1 (.out(CLK_t));
  CD74AC163E_Counter cd74ac163e_counter_1 (
    .GND(GND), .RCO(RCO1_2), .QA(HC1), .QB(HC2), .QC(HC4), .QD(HC8), .nCLR(H264), .CLK(nCLK), .A(GND),
    .B(GND), .C(GND), .D(GND), .ENP(Vcc), .VCC(Vcc), .ENT(Vcc), .nLD(Vcc));
  CD74AC163E_Counter cd74ac163e_counter_2 (
    .GND(GND), .RCO(RCO2_3o), .QA(HC16), .QB(HC32), .QC(HC64), .QD(HC128), .nCLR(H264), .CLK(nCLK), .A(GND),
    .B(GND), .C(GND), .D(GND), .ENP(RCO1_2), .VCC(Vcc), .ENT(Vcc), .nLD(Vcc));
  CD74AC163E_Counter cd74ac163e_counter_3 (
    .GND(GND), .RCO(RCO3_4o), .QA(HC256), .QB(VC1), .QC(VC2), .QD(VC4), .nCLR(V628), .CLK(nCLK), .A(GND),
    .B(GND), .C(GND), .D(GND), .ENP(eC3C), .VCC(Vcc), .ENT(Vcc), .nLD(Vcc));
  CD74AC163E_Counter cd74ac163e_counter_4 (
    .GND(GND), .RCO(RCO4_5o), .QA(VC8), .QB(VC16), .QC(VC32), .QD(VC64), .nCLR(V628), .CLK(nCLK), .A(GND),
    .B(GND), .C(GND), .D(GND), .ENP(RCO3_4i), .VCC(Vcc), .ENT(Vcc), .nLD(Vcc));
  CD74AC163E_Counter cd74ac163e_counter_5 (
    .GND(GND), .QA(VC128), .QB(VC256), .QC(VC512), .nCLR(V628), .CLK(nCLK), .A(GND), .B(GND), .C(GND),
    .D(GND), .ENP(RCO4_5i), .VCC(Vcc), .ENT(Vcc), .nLD(Vcc));  // open: RCO, QD
  SN74AC04N_NOT maybe (
    .Y1(neREAD), .Y2(nCLK), .Y3(nDIN5), .A1(eREAD), .A2(CLK_t), .A3(DIN[4]));  // open: GND, Y4, Y5, Y6, VCC, A4, A5, A6
  SN74AC04N_NOT sn74ac04n_not_1 (
    .Y1(nHC32), .Y2(nHC16), .Y3(nHC8), .GND(GND), .Y4(nHC1), .Y5(nHC2), .Y6(nHC4), .A1(HC32), .A2(HC16),
    .A3(HC8), .VCC(Vcc), .A4(HC1), .A5(HC2), .A6(HC4));
  SN74AC00N_NAND sn74ac00n_nand_1 (
    .Y1(H264), .Y2(eREAD), .GND(GND), .Y4(eWDATA), .A1(HC256), .B1(HC8), .A2(eVREAD), .B2(eHREAD), .VCC(Vcc),
    .B4(HC1), .A4(Write_Enable));  // open: Y3, B3, A3
  SN74AC04N_NOT sn74ac04n_not_2 (
    .Y1(nVC32), .Y2(nVC8), .Y3(nVC4), .GND(GND), .Y4(nH264), .Y5(nVC1), .Y6(nVC2), .A1(VC32), .A2(VC8),
    .A3(VC4), .VCC(Vcc), .A4(H264), .A5(VC1), .A6(VC2));
  SN74AC32N_OR sn74ac32n_or_1 (
    .Y1(eC3C), .GND(GND), .A1(RCO2_3i), .B1(nH264), .VCC(Vcc));  // open: Y2, Y4, Y3, A2, B2, B4, A4, B3, A3
  SN74AC00N_NAND sn74ac00n_nand_2 (
    .Y1(sn74ac00n_nand_2_y1), .Y2(eHREAD), .GND(GND), .Y4(HSYNC), .Y3(sn74ac00n_nand_2_y3), .A1(eHREAD),
    .B1(H200), .A2(sn74ac00n_nand_2_y1), .B2(H264), .VCC(Vcc), .B4(sn74ac00n_nand_2_y3), .A4(H210),
    .B3(HSYNC), .A3(H242));
  SN74AC00N_NAND sn74ac00n_nand_3 (
    .Y1(sn74ac00n_nand_3_y1), .Y2(eVREAD), .GND(GND), .Y4(VSYNC), .Y3(sn74ac00n_nand_3_y3), .A1(eVREAD),
    .B1(V600), .A2(sn74ac00n_nand_3_y1), .B2(V628), .VCC(Vcc), .B4(sn74ac00n_nand_3_y3), .A4(V601),
    .B3(VSYNC), .A3(V605));
  SN74AC08N_AND sn74ac08n_and_1 (
    .Y1(RCO2_3i), .Y2(RCO3_4i), .GND(GND), .Y4(eWH), .Y3(eWL), .A1(RCO1_2), .B1(RCO2_3o), .A2(eC3C),
    .B2(RCO3_4o), .VCC(Vcc), .B4(DIN[4]), .A4(Write_Enable), .B3(Write_Enable), .A3(nDIN5));
  SN74AC08N_AND sn74ac08n_and_2 (
    .Y1(RCO4_5i), .GND(GND), .A1(RCO3_4i), .B1(RCO4_5o), .VCC(Vcc));  // open: Y2, Y4, Y3, A2, B2, B4, A4, B3, A3
  Pull_Resistor pull_resistor_1 (.node(pull_resistor_1_node));
  Pull_Resistor pull_resistor_2 (.node(pull_resistor_2_node));
  Pull_Resistor pull_resistor_3 (.node(pull_resistor_3_node));
  _7430 #(.ShowInternalStructure("true")) u_7430_1 (
    .pin1(nHC4), .pin2(HC8), .pin3(nHC16), .pin4(nHC32), .pin5(HC64), .pin6(HC128), .pin12(nHC2),
    .pin11(nHC1), .pin8(H200));  // open: pin13, pin10, pin9
  _7430 #(.ShowInternalStructure("true")) u_7430_2 (
    .pin1(nHC4), .pin2(nHC8), .pin3(HC16), .pin4(nHC32), .pin5(HC64), .pin6(HC128), .pin12(HC2),
    .pin11(nHC1), .pin8(H210));  // open: pin13, pin10, pin9
  _7430 #(.ShowInternalStructure("true")) u_7430_3 (
    .pin1(nHC4), .pin2(nHC8), .pin3(HC16), .pin4(HC32), .pin5(HC64), .pin6(HC128), .pin12(HC2), .pin11(nHC1),
    .pin8(H242));  // open: pin13, pin10, pin9
  _7430 #(.ShowInternalStructure("true")) u_7430_4 (
    .pin1(nVC4), .pin2(VC8), .pin3(VC16), .pin4(nVC32), .pin5(VC64), .pin6(VC512), .pin12(nVC2),
    .pin11(nVC1), .pin8(V600));  // open: pin13, pin10, pin9
  _7430 #(.ShowInternalStructure("true")) u_7430_5 (
    .pin1(nVC4), .pin2(VC8), .pin3(VC16), .pin4(nVC32), .pin5(VC64), .pin6(VC512), .pin12(nVC2), .pin11(VC1),
    .pin8(V601));  // open: pin13, pin10, pin9
  _7430 #(.ShowInternalStructure("true")) u_7430_6 (
    .pin1(VC4), .pin2(VC8), .pin3(VC16), .pin4(nVC32), .pin5(VC64), .pin6(VC512), .pin12(nVC2), .pin11(VC1),
    .pin8(V605));  // open: pin13, pin10, pin9
  _7430 #(.ShowInternalStructure("true")) u_7430_7 (
    .pin1(VC4), .pin2(nVC8), .pin3(VC16), .pin4(VC32), .pin5(VC64), .pin6(VC512), .pin12(nVC2), .pin11(nVC1),
    .pin8(V628));  // open: pin13, pin10, pin9
  Pull_Resistor pull_resistor_4 (.node(pull_resistor_4_node));
  MUX_74AC11257 mux_74ac11257_1 (
    .Y1(pull_resistor_4_node), .Y2(pull_resistor_2_node), .GND1(GND), .GND2(GND), .GND3(GND), .GND4(GND),
    .Y3(pull_resistor_3_node), .Y4(pull_resistor_1_node), .nOE(GND), .nA_B(HC1), .A1(VD1A), .B1(VD2A),
    .A2(VD1B), .B2(VD2B), .VCC1_5V(Vcc), .VCC2_5V(Vcc), .A3(VD1C), .B3(VD2C), .A4(VD1D), .B4(VD2D));
  MUX_74AC11257 mux_74ac11257_2 (
    .Y1(WD1), .Y2(WD2), .GND1(GND), .GND2(GND), .GND3(GND), .GND4(GND), .Y3(WD3), .Y4(WD4), .nOE(GND),
    .nA_B(eWH), .A1(DIN[0]), .B1(VD1A), .A2(DIN[1]), .B2(VD1B), .VCC1_5V(Vcc), .VCC2_5V(Vcc), .A3(DIN[2]),
    .B3(VD1C), .A4(DIN[3]), .B4(VD1D));
  MUX_74AC11257 mux_74ac11257_3 (
    .Y1(WD5), .Y2(WD6), .GND1(GND), .GND2(GND), .GND3(GND), .GND4(GND), .Y3(WD7), .Y4(WD8), .nOE(GND),
    .nA_B(eWL), .A1(DIN[0]), .B1(VD2A), .A2(DIN[1]), .B2(VD2B), .VCC1_5V(Vcc), .VCC2_5V(Vcc), .A3(DIN[2]),
    .B3(VD2C), .A4(DIN[3]), .B4(VD2D));
  SN74AC573N_Latch sn74ac573n_latch_1 (
    .GND(GND), .NOE(eWDATA), .I1(Address_IN[0]), .I2(Address_IN[1]), .I3(Address_IN[2]), .I4(Address_IN[3]),
    .I5(Address_IN[4]), .I6(Address_IN[5]), .I7(Address_IN[6]), .I8(Address_IN[7]), .VCC_5V(Vcc), .LE(Vcc));  // open: O1, O2, O3, O4, O8, O7, O6, O5
  SN74AC573N_Latch sn74ac573n_latch_2 (
    .GND(GND), .NOE(eWDATA), .I1(Address_IN[8]), .I2(Address_IN[9]), .I3(Address_IN[10]),
    .I4(Address_IN[11]), .I5(Address_IN[12]), .I6(Address_IN[13]), .I7(DIN[6]), .I8(DIN[7]), .VCC_5V(Vcc),
    .LE(Vcc));  // open: O1, O2, O3, O4, O8, O7, O6, O5
  RAM #(.addrWidth(15), .trigger("high")) ram_1 (
    .addr({VC512, VC256, VC128, VC64, VC32, VC16, VC8, VC4, HC128, HC64, HC32, HC16, HC8, HC4, HC2}),
    .din({WD8, WD7, WD6, WD5, WD4, WD3, WD2, WD1}), .dout(ram_1_dout));  // open: we, oe
  SN74AC573N_Latch sn74ac573n_latch_3 (
    .GND(GND), .O1(VD1A), .O2(VD1B), .O3(VD1C), .O4(VD1D), .O8(VD2A), .O7(VD2B), .O6(VD2C), .O5(VD2D),
    .NOE(GND), .I1(ram_1_dout[0]), .I2(ram_1_dout[1]), .I3(ram_1_dout[2]), .I4(ram_1_dout[3]),
    .I5(ram_1_dout[4]), .I6(ram_1_dout[5]), .I7(ram_1_dout[6]), .I8(ram_1_dout[7]), .VCC_5V(Vcc), .LE(nHC1));
  RAM #(.addrWidth(15), .trigger("high")) ram_2 (
    .addr({VC512, VC256, VC128, VC64, VC32, VC16, VC8, VC4, HC128, HC64, HC32, HC16, HC8, HC4, HC2}),
    .din({WD8, WD7, WD6, WD5, WD4, WD3, WD2, WD1}), .dout(ram_1_dout));  // open: we, oe

  // Other names for the same wires on the sheet: ADIN1 = Address_IN[0]; ADIN2 = Address_IN[1]; ADIN3 = Address_IN[2];
  //   ADIN4 = Address_IN[3]; ADIN5 = Address_IN[4]; ADIN6 = Address_IN[5]; ADIN7 = Address_IN[6];
  //   ADIN8 = Address_IN[7]; ADIN9 = Address_IN[8]; ADIN10 = Address_IN[9]; ADIN11 = Address_IN[10];
  //   ADIN12 = Address_IN[11]; ADIN13 = Address_IN[12]; ADIN14 = Address_IN[13]; DIN1 = DIN[0]; DIN2 = DIN[1];
  //   DIN3 = DIN[2]; DIN4 = DIN[3]; DIN5 = DIN[4]; DIN6 = DIN[5]; DIN7 = DIN[6]; DIN8 = DIN[7]; eDINW = Write_Enable

  // Notes on the sheet:
  //   Flip-Flops ???
endmodule

module GPU2 (
  input  Vcc,
  input  CLK_10MHz,
  input  [7:0] DIN,
  input  [13:0] Address_IN,
  input  Write_Enable,
  input  MEM_ENABLE,
  input  READ_ENABLE,
  input  CLR,
  output HSYNC,
  output VSYNC,
  output RED,
  output GREEN,
  output BLUE,
  output LIGHT,
  output [7:0] DOUT
);

  wire and_1_out, and_2_out, and_3_out, and_4_out, eC3C, eHRS, eLD, eOPT_ADD, eREAD, eVRS, eWH, eWL, eWRITE,
       GND, H264, HC1, HC2, HC4, HC8, HC16, HC32, HC64, HC128, HC256, HVRE, LCHVD, nCLK, nCLR, nDIN5, neREAD,
       nH200, nH210, nH242, nH264, nHC1, nHC2, nHC4, nHC8, nHC16, nHC32, nLCHVD, nV600, nV601, nV605, nV628,
       nVC1, nVC2, nVC4, nVC8, nVC32, RCO1_2, RCO2_3i, RCO2_3o, RCO3_4i, RCO3_4o, RCO4_5i, RCO4_5o,
       sn74ac00n_nand_1_y2, sn74ac00n_nand_1_y3, sn74ac00n_nand_2_y2, sn74ac00n_nand_2_y3, VC1, VC2, VC4,
       VC8, VC16, VC32, VC64, VC128, VC256, VC512, VD1A, VD1B, VD1C, VD1D, VD2A, VD2B, VD2C, VD2D, VMAD1,
       VMAD2, VMAD3, VMAD4, VMAD5, VMAD6, VMAD7, VMAD8, VMAD9, VMAD10, VMAD11, VMAD12, VMAD13, VMAD14,
       VMAD15, VMAD16, WD1, WD2, WD3, WD4, WD5, WD6, WD7, WD8;
  wire [7:0] ram_1_dout;

  Clock clock_1 ();  // open: out
  not not_1 (nCLR, CLR);
  CD74AC163E_Counter cd74ac163e_counter_1 (
    .GND(GND), .RCO(RCO1_2), .QA(HC1), .QB(HC2), .QC(HC4), .QD(HC8), .nCLR(nH264), .CLK(CLK_10MHz), .A(GND),
    .B(GND), .C(GND), .D(GND), .ENP(Vcc), .VCC(Vcc), .ENT(Vcc), .nLD(Vcc));
  CD74AC163E_Counter cd74ac163e_counter_2 (
    .GND(GND), .RCO(RCO2_3o), .QA(HC16), .QB(HC32), .QC(HC64), .QD(HC128), .nCLR(nH264), .CLK(CLK_10MHz),
    .A(GND), .B(GND), .C(GND), .D(GND), .ENP(RCO1_2), .VCC(Vcc), .ENT(Vcc), .nLD(Vcc));
  CD74AC163E_Counter cd74ac163e_counter_3 (
    .GND(GND), .RCO(RCO3_4o), .QA(HC256), .QB(VC1), .QC(VC2), .QD(VC4), .nCLR(nV628), .CLK(CLK_10MHz),
    .A(GND), .B(GND), .C(GND), .D(GND), .ENP(eC3C), .VCC(Vcc), .ENT(Vcc), .nLD(Vcc));
  CD74AC163E_Counter cd74ac163e_counter_4 (
    .GND(GND), .RCO(RCO4_5o), .QA(VC8), .QB(VC16), .QC(VC32), .QD(VC64), .nCLR(nV628), .CLK(CLK_10MHz),
    .A(GND), .B(GND), .C(GND), .D(GND), .ENP(RCO3_4i), .VCC(Vcc), .ENT(Vcc), .nLD(Vcc));
  CD74AC163E_Counter cd74ac163e_counter_5 (
    .GND(GND), .QA(VC128), .QB(VC256), .QC(VC512), .nCLR(nV628), .CLK(CLK_10MHz), .A(GND), .B(GND), .C(GND),
    .D(GND), .ENP(RCO4_5i), .VCC(Vcc), .ENT(Vcc), .nLD(Vcc));  // open: RCO, QD
  // SN74AC573N_Latch sn74ac573n_latch_1: pin names not known
  SN74AC04N_NOT sn74ac04n_not_1 (
    .Y1(nHC1), .Y2(nHC2), .Y3(nHC4), .GND(GND), .Y4(nHC32), .Y5(nHC16), .Y6(nHC8), .A1(HC1), .A2(HC2),
    .A3(HC4), .VCC(Vcc), .A4(HC32), .A5(HC16), .A6(HC8));
  SN74AC04N_NOT sn74ac04n_not_2 (
    .Y1(nVC1), .Y2(nVC2), .Y3(nVC4), .GND(GND), .Y4(nCLK), .Y5(nVC32), .Y6(nVC8), .A1(VC1), .A2(VC2),
    .A3(VC4), .VCC(Vcc), .A4(CLK_10MHz), .A5(VC32), .A6(VC8));
  SN74AC08N_AND sn74ac08n_and_1 (
    .Y1(RCO2_3i), .Y2(RCO3_4i), .GND(GND), .Y4(RCO4_5i), .Y3(H264), .A1(RCO2_3o), .B1(RCO1_2), .A2(RCO3_4o),
    .B2(eC3C), .VCC(Vcc), .B4(RCO3_4i), .A4(RCO4_5o), .B3(HC256), .A3(HC8));
  SN74AC32N_OR sn74ac32n_or_1 (
    .Y1(eC3C), .GND(GND), .A1(RCO2_3i), .B1(H264), .VCC(Vcc));  // open: Y2, Y4, Y3, A2, B2, B4, A4, B3, A3
  SN74AC04N_NOT sn74ac04n_not_3 (
    .Y1(nLCHVD), .GND(GND), .Y4(nDIN5), .Y5(neREAD), .Y6(nH264), .A1(LCHVD), .VCC(Vcc), .A4(DIN[4]),
    .A5(eREAD), .A6(H264));  // open: Y2, Y3, A2, A3
  SN74AC08N_AND sn74ac08n_and_2 (
    .Y1(eLD), .Y2(HVRE), .GND(GND), .Y4(LCHVD), .Y3(eREAD), .A1(nHC1), .B1(CLK_10MHz), .A2(eHRS), .B2(eVRS),
    .VCC(Vcc), .B4(eLD), .A4(HVRE), .B3(READ_ENABLE), .A3(nCLK));
  SN74AC08N_AND sn74ac08n_and_3 (
    .Y1(eWRITE), .Y2(eOPT_ADD), .GND(GND), .Y4(eWH), .Y3(eWL), .A1(Write_Enable), .B1(nCLK), .A2(nCLK),
    .B2(MEM_ENABLE), .VCC(Vcc), .B4(eWRITE), .A4(DIN[4]), .B3(eWRITE), .A3(nDIN5));
  _7430 #(.ShowInternalStructure("true")) u_7430_1 (
    .pin1(nHC4), .pin2(HC8), .pin3(nHC16), .pin4(nHC32), .pin5(HC64), .pin6(HC128), .pin12(nHC2),
    .pin11(nHC1), .pin8(nH200));  // open: pin13, pin10, pin9
  _7430 #(.ShowInternalStructure("true")) u_7430_2 (
    .pin1(nHC4), .pin2(nHC8), .pin3(HC16), .pin4(nHC32), .pin5(HC64), .pin6(HC128), .pin12(HC2),
    .pin11(nHC1), .pin8(nH210));  // open: pin13, pin10, pin9
  _7430 #(.ShowInternalStructure("true")) u_7430_3 (
    .pin1(nHC4), .pin2(nHC8), .pin3(HC16), .pin4(HC32), .pin5(HC64), .pin6(HC128), .pin12(HC2), .pin11(nHC1),
    .pin8(nH242));  // open: pin13, pin10, pin9
  _7430 #(.ShowInternalStructure("true")) u_7430_4 (
    .pin1(nVC4), .pin2(VC8), .pin3(VC16), .pin4(nVC32), .pin5(VC64), .pin6(VC512), .pin12(nVC2),
    .pin11(nVC1), .pin8(nV600));  // open: pin13, pin10, pin9
  _7430 #(.ShowInternalStructure("true")) u_7430_5 (
    .pin1(nVC4), .pin2(VC8), .pin3(VC16), .pin4(nVC32), .pin5(VC64), .pin6(VC512), .pin12(nVC2), .pin11(VC1),
    .pin8(nV601));  // open: pin13, pin10, pin9
  _7430 #(.ShowInternalStructure("true")) u_7430_6 (
    .pin1(VC4), .pin2(VC8), .pin3(VC16), .pin4(nVC32), .pin5(VC64), .pin6(VC512), .pin12(nVC2), .pin11(VC1),
    .pin8(nV605));  // open: pin13, pin10, pin9
  _7430 #(.ShowInternalStructure("true")) u_7430_7 (
    .pin1(VC4), .pin2(nVC8), .pin3(VC16), .pin4(VC32), .pin5(VC64), .pin6(VC512), .pin12(nVC2), .pin11(nVC1),
    .pin8(nV628));  // open: pin13, pin10, pin9
  MUX_74AC11257 mux_74ac11257_1 (
    .Y1(VMAD1), .Y2(VMAD2), .GND1(GND), .GND2(GND), .GND3(GND), .GND4(GND), .Y3(VMAD3), .Y4(VMAD4),
    .nOE(GND), .nA_B(eOPT_ADD), .A1(HC2), .B1(Address_IN[0]), .A2(HC4), .B2(Address_IN[1]), .VCC1_5V(Vcc),
    .VCC2_5V(Vcc), .A3(HC8), .B3(Address_IN[2]), .A4(HC16), .B4(Address_IN[3]));
  MUX_74AC11257 mux_74ac11257_2 (
    .Y1(VMAD5), .Y2(VMAD6), .GND1(GND), .GND2(GND), .GND3(GND), .GND4(GND), .Y3(VMAD7), .Y4(VMAD8),
    .nOE(GND), .nA_B(eOPT_ADD), .A1(HC32), .B1(Address_IN[4]), .A2(HC64), .B2(Address_IN[5]), .VCC1_5V(Vcc),
    .VCC2_5V(Vcc), .A3(HC128), .B3(Address_IN[6]), .A4(VC4), .B4(Address_IN[7]));
  MUX_74AC11257 mux_74ac11257_3 (
    .Y1(VMAD9), .Y2(VMAD10), .GND1(GND), .GND2(GND), .GND3(GND), .GND4(GND), .Y3(VMAD11), .Y4(VMAD12),
    .nOE(GND), .nA_B(eOPT_ADD), .A1(VC8), .B1(Address_IN[8]), .A2(VC16), .B2(Address_IN[9]), .VCC1_5V(Vcc),
    .VCC2_5V(Vcc), .A3(VC32), .B3(Address_IN[10]), .A4(VC64), .B4(Address_IN[11]));
  MUX_74AC11257 mux_74ac11257_4 (
    .Y1(VMAD13), .Y2(VMAD14), .GND1(GND), .GND2(GND), .GND3(GND), .GND4(GND), .Y3(VMAD15), .Y4(VMAD16),
    .nOE(GND), .nA_B(eOPT_ADD), .A1(VC128), .B1(Address_IN[12]), .A2(VC256), .B2(Address_IN[13]),
    .VCC1_5V(Vcc), .VCC2_5V(Vcc), .A3(VC512), .B3(DIN[6]), .A4(HC256), .B4(DIN[7]));
  MUX_74AC11257 mux_74ac11257_5 (
    .Y1(WD1), .Y2(WD2), .GND1(GND), .GND2(GND), .GND3(GND), .GND4(GND), .Y3(WD3), .Y4(WD4), .nOE(GND),
    .nA_B(eWH), .A1(DIN[0]), .B1(VD1A), .A2(DIN[1]), .B2(VD1B), .VCC1_5V(Vcc), .VCC2_5V(Vcc), .A3(DIN[2]),
    .B3(VD1C), .A4(DIN[3]), .B4(VD1D));
  MUX_74AC11257 mux_74ac11257_6 (
    .Y1(WD5), .Y2(WD6), .GND1(GND), .GND2(GND), .GND3(GND), .GND4(GND), .Y3(WD7), .Y4(WD8), .nOE(GND),
    .nA_B(eWL), .A1(DIN[0]), .B1(VD2A), .A2(DIN[1]), .B2(VD2B), .VCC1_5V(Vcc), .VCC2_5V(Vcc), .A3(DIN[2]),
    .B3(VD2C), .A4(DIN[3]), .B4(VD2D));
  MUX_74AC11257 mux_74ac11257_7 (
    .Y1(BLUE), .Y2(GREEN), .GND1(GND), .GND2(GND), .GND3(GND), .GND4(GND), .Y3(RED), .Y4(LIGHT), .nOE(GND),
    .nA_B(HC1), .A1(VD1A), .B1(VD2A), .A2(VD1B), .B2(VD2B), .VCC1_5V(Vcc), .VCC2_5V(Vcc), .A3(VD1C),
    .B3(VD2C), .A4(VD1D), .B4(VD2D));
  SN74AC00N_NAND sn74ac00n_nand_1 (
    .Y1(HSYNC), .Y2(sn74ac00n_nand_1_y2), .GND(GND), .Y4(eHRS), .Y3(sn74ac00n_nand_1_y3),
    .A1(sn74ac00n_nand_1_y2), .B1(nH210), .A2(HSYNC), .B2(and_1_out), .VCC(Vcc), .B4(sn74ac00n_nand_1_y3),
    .A4(nH264), .B3(eHRS), .A3(and_3_out));
  and and_1 (and_1_out, nH242, nCLR);
  SN74AC00N_NAND sn74ac00n_nand_2 (
    .Y1(VSYNC), .Y2(sn74ac00n_nand_2_y2), .GND(GND), .Y4(eVRS), .Y3(sn74ac00n_nand_2_y3),
    .A1(sn74ac00n_nand_2_y2), .B1(nV601), .A2(VSYNC), .B2(and_2_out), .VCC(Vcc), .B4(sn74ac00n_nand_2_y3),
    .A4(nV628), .B3(eVRS), .A3(and_4_out));
  and and_2 (and_2_out, nV605, nCLR);
  and and_3 (and_3_out, nH200, nCLR);
  and and_4 (and_4_out, nV600, nCLR);
  RAM #(.addrWidth(15), .trigger("high")) ram_1 (
    .addr({VMAD15, VMAD14, VMAD13, VMAD12, VMAD11, VMAD10, VMAD9, VMAD8, VMAD7, VMAD6, VMAD5, VMAD4, VMAD3, VMAD2, VMAD1}),
    .we(eWRITE), .oe(Vcc), .din({WD8, WD7, WD6, WD5, WD4, WD3, WD2, WD1}), .dout(ram_1_dout));
  SN74AC573N_Latch sn74ac573n_latch_2 (
    .GND(GND), .O1(VD1A), .O2(VD1B), .O3(VD1C), .O4(VD1D), .O8(VD2A), .O7(VD2B), .O6(VD2C), .O5(VD2D),
    .NOE(nLCHVD), .I1(ram_1_dout[0]), .I2(ram_1_dout[1]), .I3(ram_1_dout[2]), .I4(ram_1_dout[3]),
    .I5(ram_1_dout[4]), .I6(ram_1_dout[5]), .I7(ram_1_dout[6]), .I8(ram_1_dout[7]), .VCC_5V(Vcc), .LE(LCHVD));
  SN74AC573N_Latch sn74ac573n_latch_3 (
    .GND(GND), .O1(DOUT[0]), .O2(DOUT[1]), .O3(DOUT[2]), .O4(DOUT[3]), .O8(DOUT[4]), .O7(DOUT[5]),
    .O6(DOUT[6]), .O5(DOUT[7]), .NOE(neREAD), .I1(ram_1_dout[0]), .I2(ram_1_dout[1]), .I3(ram_1_dout[2]),
    .I4(ram_1_dout[3]), .I5(ram_1_dout[4]), .I6(ram_1_dout[5]), .I7(ram_1_dout[6]), .I8(ram_1_dout[7]),
    .VCC_5V(Vcc), .LE(eREAD));

  // Other names for the same wires on the sheet: ADIN1 = Address_IN[0]; ADIN2 = Address_IN[1]; ADIN3 = Address_IN[2];
  //   ADIN4 = Address_IN[3]; ADIN5 = Address_IN[4]; ADIN6 = Address_IN[5]; ADIN7 = Address_IN[6];
  //   ADIN8 = Address_IN[7]; ADIN9 = Address_IN[8]; ADIN10 = Address_IN[9]; ADIN11 = Address_IN[10];
  //   ADIN12 = Address_IN[11]; ADIN13 = Address_IN[12]; ADIN14 = Address_IN[13]; B = BLUE; CLK = CLK_10MHz;
  //   DIN1 = DIN[0]; DIN2 = DIN[1]; DIN3 = DIN[2]; DIN4 = DIN[3]; DIN5 = DIN[4]; DIN6 = DIN[5]; DIN7 = DIN[6];
  //   DIN8 = DIN[7]; DOUT1 = DOUT[0]; DOUT2 = DOUT[1]; DOUT3 = DOUT[2]; DOUT4 = DOUT[3]; DOUT5 = DOUT[4];
  //   DOUT6 = DOUT[5]; DOUT7 = DOUT[6]; DOUT8 = DOUT[7]; G = GREEN; L = LIGHT; MENAB = MEM_ENABLE; R = RED;
  //   READ = READ_ENABLE; WRITE = Write_Enable

  // Notes on the sheet:
  //   CD74AC138E DEMUX: 0
  //   SN74AC04N NOT: 3
  //   SN74AC08N AND: 3
  //   SN74AC32N OR: 1
  //   CD74AC02EE4 NOR: 0
  //   SN74AC573N D-LATCH: 2
  //   RAM: 2x16
  //   CD74AC238E ADDR: 0
  //   ATF22V10C CPLD: 0
  //   74AHC30D ONAND: 7
  //   CD74HC85E MAGCOMP: 0
  //   74AC11257 MUX: 7
  //   CD74HC27N TNOR: 0
  //   CD74AC139E DEMUX2: 0
  //   CD74AC163E COUNTER: 5
  //   SN74AC00N NAND: 2
endmodule

module STD_COMP (
  input  VCC,
  input  E_CLOCK,
  input  [7:0] MDATIN,
  input  [7:0] IO_DATIN,
  input  HIRQ,
  input  NMI,
  input  RST,
  input  HALT,
  input  TEMP_STOP_OSCILLATION,
  output [15:0] ADDR_OUT,
  output MRW_OUT,
  output [7:0] MDAT_OUT,
  output GND,
  output MREAD,
  output MWRITE,
  output [7:0] DAT_OUT,
  output INTP,
  output IRQE,
  output ERR,
  output UUSD,
  output [7:0] IODAT,
  output IOWRITE,
  output IOREAD,
  output PCS
);

  wire AFULL, and_1_out, and_2_out, ARREAD, B_FULL, CIRQ, CLBB, clock_1_out, CNMI, CRST, CST_AD1, CST_AD2,
       CST_AD3, CST_AD4, CST_READ, DB_PSH, DBOT, eARG1, eARG2, eCPC, eERR, eIRQ, ePCH, ePCL, eRHL, eRST, eSP,
       eUUSD, eWFLG, I_LD, IB_RDY, INT, IRT, IRTV_BUS, LD_XF, LDY, MREAD_t, MWRITE_t, nB_FULL, nDB_PLL,
       not_1_out, not_2_out, not_3_out, not_4_out, not_5_out, ntEQUAL, ntINTP, ntJNE, or_1_out,
       pull_resistor_3_node, pull_resistor_4_node, RREAD, RRES, RWRITE, tHIRQ, tHLT, tIRQ, tMBOE, tNMI, tPCH,
       tPCL, tRST;
  wire [2:0] AOPC_BUS, RAD_BUS;
  wire [7:0] controlled_buffer_1_out, controlled_buffer_3_out, controlled_buffer_4_out, D_BUS, F_BUS,
       INST_BUS, pull_resistor_1_node, ram_1_dout, ram_2_dout, rom_1_data;
  wire [13:0] pull_resistor_6_node, pull_resistor_7_node;
  wire [14:0] controlled_buffer_9_out, pull_resistor_2_node;
  wire [15:0] AD16_BUS;

  Clock clock_1 (.out(clock_1_out));
  assign controlled_buffer_1_out = not_1_out ? pull_resistor_1_node : 8'bz;  // Controlled_Buffer controlled_buffer_1
  not not_1 (not_1_out, MWRITE);
  SN74AC32N_OR sn74ac32n_or_1 (
    .Y1(eCPC), .A1(ntEQUAL), .B1(ntJNE));  // open: Y2, GND, Y4, Y3, A2, B2, VCC, B4, A4, B3, A3
  SN74AC08N_AND sn74ac08n_and_1 (
    .Y1(ePCH), .Y2(ePCL), .A1(tPCH), .B1(eCPC), .A2(tPCL), .B2(eCPC));  // open: GND, Y4, Y3, VCC, B4, A4, B3, A3
  SN74AC08N_AND sn74ac08n_and_2 (
    .Y1(tMBOE), .Y4(eIRQ), .Y3(tHIRQ), .A1(B_FULL), .B1(MREAD_t), .B4(ntINTP), .A4(IRQE), .B3(eIRQ), .A3(HIRQ));  // open: Y2, GND, A2, B2, VCC
  SN74AC04N_NOT sn74ac04n_not_1 (
    .Y1(ntEQUAL), .Y3(nB_FULL), .Y6(ntINTP), .A1(F_BUS[2]), .A3(B_FULL), .A6(INTP));  // open: Y2, GND, Y4, Y5, A2, VCC, A4, A5
  assign DAT_OUT = MWRITE ? controlled_buffer_3_out : 8'bz;  // Controlled_Buffer controlled_buffer_2
  assign controlled_buffer_3_out = not_1_out ? controlled_buffer_1_out : 8'bz;  // Controlled_Buffer controlled_buffer_3
  Scheduler scheduler_1 (
    .Vcc(VCC), .CLOCK(PCS), .MBUS_OE(tMBOE), .STB_BUFF(nB_FULL), .DATIN(controlled_buffer_3_out),
    .CLR_BUFF(CLBB), .ARG1_E(eARG1), .ARG2_E(eARG2), .S_IRQ(INT), .H_IRQ(tHIRQ), .C_IRQ(CIRQ), .NMI(NMI),
    .C_NMI(CNMI), .RST(eRST), .C_RST(CRST), .DBU_TRUE(DBOT), .CLR(TEMP_STOP_OSCILLATION), .MBUS_DOUT(D_BUS),
    .INSTRUCTION(INST_BUS), .ARG_8(D_BUS), .ARG_16(AD16_BUS), .REG_ADD(RAD_BUS), .ALU_OPC(AOPC_BUS),
    .IRT_VAL(IRTV_BUS), .RDY(IB_RDY), .BUFF_FULL(B_FULL), .ERR(eERR), .RST_T(tRST), .IRQ_T(tIRQ),
    .NMI_T(tNMI), .AFULL(AFULL), .UUSD(eUUSD), .GND(GND));
  ALU alu_1 (
    .CLOCK(PCS), .VCC(VCC), .RRES(RRES), .R_FLGS(eWFLG), .LD_XF(LD_XF), .LDY(LDY), .AOPC(AOPC_BUS),
    .FDIN(F_BUS), .DIN(D_BUS), .FOUT(F_BUS), .DOUT(D_BUS), .GND(GND));
  REGISTERS registers_1 (
    .CLOCK(PCS), .VCC(VCC), .WRITE(RWRITE), .READ(RREAD), .ADDRESS(RAD_BUS), .DAT_IN(D_BUS), .RHL(eRHL),
    .FLG_IN(F_BUS), .EFIN(eWFLG), .DAT_OUT(D_BUS), .HL_OUT(AD16_BUS), .F_OUT(F_BUS), .GND(GND));
  AUX_Registers aux_registers_1 (
    .VCC(VCC), .CLOCK(PCS), .RESET(CRST), .PC_DATIN(AD16_BUS), .DAT_IN(D_BUS), .ePCH(ePCH), .ePCL(ePCL),
    .eSP(eSP), .I_LD(I_LD), .READ(ARREAD), .READ_CST(CST_READ),
    .CSTAD_DAT({CST_AD4, CST_AD3, CST_AD2, CST_AD1}), .ADDRESS_16BIT(AD16_BUS), .PC8_OUT(D_BUS), .GND(GND));
  or or_1 (or_1_out, TEMP_STOP_OSCILLATION, IRT);
  SN74AC573N_Latch sn74ac573n_latch_1 (
    .GND(GND), .O1(D_BUS[0]), .O2(D_BUS[1]), .O3(D_BUS[2]), .O4(D_BUS[3]), .O8(D_BUS[4]), .O7(D_BUS[5]),
    .O6(D_BUS[6]), .O5(D_BUS[7]), .NOE(nDB_PLL), .I1(D_BUS[0]), .I2(D_BUS[1]), .I3(D_BUS[2]), .I4(D_BUS[3]),
    .I5(D_BUS[4]), .I6(D_BUS[5]), .I7(D_BUS[6]), .I8(D_BUS[7]), .VCC_5V(VCC), .LE(DB_PSH));
  CPU_CLOCK cpu_clock_1 (.Vcc(VCC), .I_CLOCK(clock_1_out), .O_CLOCK(E_CLOCK), .H_IN(tHLT), .CLOCK_OUT(PCS), .GND(GND));
  Addresser addresser_1 ();  // open: Vcc, CLOCK, BIT16_D, READ, WRITE, DATIN, WOUT, ROUT, ADOUT, DOUT, GND
  Status_Transceiver status_transceiver_1 (
    .VCC(VCC), .CLOCK(PCS), .RESET(CRST), .INTP_D(AFULL), .IRQE_D(IRTV_BUS), .ERR(eERR), .UN_D(eUUSD),
    .INTP_E(AFULL), .IRQE_E(or_1_out), .RESET_CPU(RST), .HALT(HALT), .GND(GND), .INTP(INTP), .IRQE(IRQE),
    .ERROR(ERR), .UUSD(UUSD), .RSTCPU(eRST), .HALT_OUT(tHLT));  // open: VCC_OUT
  AUX_Registers aux_registers_2 ();  // open: VCC, CLOCK, RESET, PC_DATIN, DAT_IN, ePCH, ePCL, eSP, I_LD, READ, READ_CST, CSTAD_DAT, ADDRESS_16BIT, PC8_OUT, GND
  assign controlled_buffer_4_out = IOREAD ? IO_DATIN : 8'bz;  // Controlled_Buffer controlled_buffer_4
  assign IODAT = IOWRITE ? D_BUS : 8'bz;  // Controlled_Buffer controlled_buffer_5
  assign D_BUS = IOREAD ? controlled_buffer_4_out : 8'bz;  // Controlled_Buffer controlled_buffer_6
  Addresser addresser_2 (
    .Vcc(VCC), .CLOCK(PCS), .BIT16_D(AD16_BUS), .READ(MREAD_t), .WRITE(MWRITE_t), .DATIN(D_BUS),
    .WOUT(MWRITE), .ROUT(MREAD), .ADOUT(ADDR_OUT), .DOUT(controlled_buffer_3_out), .GND(GND));
  Instruction_Decoder instruction_decoder_1 (
    .VCC(VCC), .CLOCK(PCS), .INST_IN(INST_BUS), .EXEC(B_FULL), .RST_DCR(IB_RDY), .IRQ(tIRQ), .NMI(tNMI),
    .RST_CPU(tRST), .AFULL_IN(AFULL), .CLR_BF(CLBB), .CIRQ(CIRQ), .CNMI(CNMI), .CRST(CRST), .eARG1(eARG1),
    .eARG2(eARG2), .RRES(RRES), .LD_XF(LD_XF), .LDY(LDY), .RREAD(RREAD), .RWRITE(RWRITE), .eRHL(eRHL),
    .eWFLG(eWFLG), .ARREAD(ARREAD), .PCH(tPCH), .PCL(tPCL), .ESP(eSP), .I_LD(I_LD), .DB_PSH(DB_PSH),
    .nDB_PLL(nDB_PLL), .MREAD(MREAD_t), .MWRITE(MWRITE_t), .INT(INT), .IRT(IRT), .IOB_IN(IOREAD),
    .IOB_OUT(IOWRITE), .DBOT(DBOT), .ntJNE(ntJNE), .CST_READ(CST_READ), .CST_AD1(CST_AD1), .CST_AD2(CST_AD2),
    .CST_AD3(CST_AD3), .CST_AD4(CST_AD4), .GND(GND));
  REGISTERS registers_2 ();  // open: CLOCK, VCC, WRITE, READ, ADDRESS, DAT_IN, RHL, FLG_IN, EFIN, DAT_OUT, HL_OUT, F_OUT, GND
  ALU alu_2 ();  // open: CLOCK, VCC, RRES, R_FLGS, LD_XF, LDY, AOPC, FDIN, DIN, FOUT, DOUT, GND
  // SN74AC573N_Latch sn74ac573n_latch_2: pin names not known
  Instruction_Decoder instruction_decoder_2 ();  // open: VCC, CLOCK, INST_IN, EXEC, RST_DCR, IRQ, NMI, RST_CPU, AFULL_IN, CLR_BF, CIRQ, CNMI, CRST, eARG1, eARG2, RRES, LD_XF, LDY, RREAD, RWRITE, eRHL, eWFLG, ARREAD, PCH, PCL, ESP, I_LD, DB_PSH, nDB_PLL, MREAD, MWRITE, INT, IRT, IOB_IN, IOB_OUT, DBOT, ntJNE, CST_READ, CST_AD1, CST_AD2, CST_AD3, CST_AD4, GND
  not not_2 (not_2_out, MREAD);
  Pull_Resistor pull_resistor_1 (.node(pull_resistor_1_node));
  Pull_Resistor pull_resistor_2 (.node(pull_resistor_2_node));
  assign pull_resistor_2_node = ADDR_OUT[15] ? ADDR_OUT[14:0] : 15'bz;  // Controlled_Buffer controlled_buffer_7
  Pull_Resistor pull_resistor_3 (.node(pull_resistor_3_node));
  assign pull_resistor_3_node = and_1_out ? MREAD : 1'bz;  // Controlled_Buffer controlled_buffer_8
  assign controlled_buffer_9_out = not_3_out ? ADDR_OUT[14:0] : 15'bz;  // Controlled_Buffer controlled_buffer_9
  not not_3 (not_3_out, ADDR_OUT[15]);
  not not_4 (not_4_out, pull_resistor_2_node[14]);
  Pull_Resistor pull_resistor_4 (.node(pull_resistor_4_node));
  assign pull_resistor_4_node = pull_resistor_2_node[14] ? MREAD : 1'bz;  // Controlled_Buffer controlled_buffer_10
  ROM #(.addrWidth(15)) rom_1 (.addr(controlled_buffer_9_out), .data(rom_1_data));
  Pull_Resistor pull_resistor_5 (.node(controlled_buffer_9_out));
  and and_1 (and_1_out, ADDR_OUT[15], not_4_out);
  RAM #(.addrWidth(14), .trigger("high")) ram_1 (
    .addr(pull_resistor_6_node), .we(pull_resistor_3_node), .oe(not_2_out), .din(DAT_OUT), .dout(ram_1_dout));
  Pull_Resistor pull_resistor_6 (.node(pull_resistor_6_node));
  assign pull_resistor_6_node = and_1_out ? pull_resistor_2_node[13:0] : 14'bz;  // Controlled_Buffer controlled_buffer_11
  RAM #(.addrWidth(14), .trigger("high")) ram_2 (
    .addr(pull_resistor_7_node), .we(pull_resistor_4_node), .oe(not_2_out), .din(DAT_OUT), .dout(ram_2_dout));
  Pull_Resistor pull_resistor_7 (.node(pull_resistor_7_node));
  assign pull_resistor_7_node = pull_resistor_2_node[14] ? pull_resistor_2_node[13:0] : 14'bz;  // Controlled_Buffer controlled_buffer_12
  assign pull_resistor_1_node = not_3_out ? rom_1_data : 8'bz;  // Controlled_Buffer controlled_buffer_13
  assign pull_resistor_1_node = and_1_out ? ram_1_dout : 8'bz;  // Controlled_Buffer controlled_buffer_14
  assign pull_resistor_1_node = pull_resistor_2_node[14] ? ram_2_dout : 8'bz;  // Controlled_Buffer controlled_buffer_15
  not not_5 (not_5_out, ADDR_OUT[14]);
  and and_2 (and_2_out, not_5_out, ADDR_OUT[15]);
  // NOT_Gate not_6 has open pins: in=and_2_out, out=open
  ROM #(.addrWidth(15)) rom_2 ();  // open: addr, data
  RAM #(.addrWidth(15), .trigger("high")) ram_3 (.we(MWRITE), .oe(MREAD));  // open: addr, clk, din, dout
  RAM #(.addrWidth(15), .trigger("high"), .\type ("nonvolatile")) nvSRAM ();  // open: addr, we, oe, clk, din, dout
  // SN74AC573N_Latch sn74ac573n_latch_3: pin names not known
  GPU2 gpu2_1 (.CLR(TEMP_STOP_OSCILLATION));  // open: Vcc, CLK_10MHz, DIN, Address_IN, Write_Enable, MEM_ENABLE, READ_ENABLE, HSYNC, VSYNC, RED, GREEN, BLUE, LIGHT, DOUT

  assign MDAT_OUT = DAT_OUT;
  assign MRW_OUT = MREAD;

  // Other names for the same wires on the sheet: ECLK = E_CLOCK; tEQUAL = F_BUS[2]; HIRQ_IN = HIRQ; HLT_IN = HALT;
  //   iCLK = PCS; IOBIN = IOREAD; IOBOUT = IOWRITE; IODATIN[7:0] = IO_DATIN; MWRITE_OUT = MWRITE; RST_IN = RST;
  //   tERR = ERR; tINTP = INTP; tIRQE = IRQE; tUUSD = UUSD

  // Notes on the sheet:
  //   TOTAL: (x1.5)
  //   ORDER:
  //   SN74AC573N D-LATCH: 1
  //   CD74AC138E DEMUX: 0
  //   SN74AC04N NOT: 0
  //   SN74AC08N AND: 0
  //   SN74AC32N OR: 0
  //   CD74AC02EE4 NOR: 0
  //   (EEP)ROM: 1x32
  //   RAM: 2x16
  //   SSD: 2,3,4 x16
  //   +EEPROM programmer
  //   SN74AC573N D-LATCH: 38
  //   CD74AC138E DEMUX: 4
  //   SN74AC04N NOT: 17
  //   SN74AC08N AND: 16
  //   SN74AC32N OR: 10
  //   CD74AC02EE4 NOR: 6
  //   (EEP)ROM: 1x32
  //   RAM: 4x16
  //   SSD: 2x16
  //   SN74AC573N D-LATCH: 70
  //   CD74AC138E DEMUX: 10
  //   SN74AC04N NOT: 30
  //   SN74AC08N AND: 25
  //   SN74AC32N OR: 20
  //   CD74AC02E NOR: 15
  //   (EEP)ROM: 3x32
  //   RAM: 10x16
  //   SSD: 10x16
  //   All ICs and a few components at Mouser.ch
  //   The rest of the components at digitec.ch
  //   +5 ONAND
  //   +1 D_LATCH
  //   +DECODERS
  //   +arduino
  //   +extra RAM
  //   + HUI
  //   +extra SSD
  //   100 buttons
  //   5mx4 wires
  //   200 LEDs
  //   74AC11257 MUX: 0
  //   CD74AC238E ADDR: 0
  //   ATF22V10C CPLD: 0
  //   74AHC30D ONAND: 0
  //   +extra RAM
  //   + HUI
  //   *extra ONAND
  //   +extra SSD
  //   CD74HC85E MAGCOMP: 2
  //   74AC11257 MUX: 14
  //   CD74AC238E ADDR: 6
  //   ATF22V10C CPLD: 3
  //   74AHC30D ONAND: 13
  //   *extra ONAND
  //   CD74HC85E MAGCOMP: 10
  //   74AC11257 MUX: 25
  //   CD74AC283E ADDR: 15
  //   ATF22V10C CPLD: 15
  //   74AHC30D ONAND: 50
  //   5 arduino nano
  //   10 DIP switches
  //   Package adapters
  //   CD74HC85E MAGCOMP: 0
  //   +buttons
  //   +wires
  //   +LEDs
  //   +DIP switch
  //   TL866II EEPROM programmer
  //   +buttons
  //   +wires
  //   +LEDs
  //   +DIP switch
  //   +arduino
  //   CD74HC27N TNOR: 0
  //   CD74AC139E DEMUX2: 0
  //   CD74AC163E COUNTER: 0
  //   SN74AC00N NAND: 0
  //   CD74HC27N TNOR: 2
  //   CD74AC139E DEMUX2: 1
  //   CD74AC163E COUNTER: 13
  //   SN74AC00N NAND: 13
  //   +EEPROM programmer
  //   CD74HC27N TNOR: 5
  //   CD74AC139E DEMUX2: 5
  //   CD74AC163E COUNTER: 25
  //   SN74AC00N NAND: 50
  //   CLOCK set
  //   100 resistors
  //   50 BB830 breadboads
  //   Voltage adapter
  //   Tranceiver =>
  //   STS_TRSCVR =>
  //   STS_TRSCVR =>
  //   ADDDRESSER =>
  //   ALU =>
  //   ID =>
  //   <= ADDDRESSER
  //   GPU2
  //   Tranceiver =>
  //   ST
  //   SCH
  //   contents of rom_1 (hex, n*v repeats v):
  //   e1 42 78 79 79 e9 ff f8 1 0 79 70
endmodule
