// Logisim project TI_ICS.circ as structural Verilog: 16 circuits, main circuit SN74AC373N_Latch
module SN74AC373N_Latch (
  input  VCC_6V,
  input  NOE,
  input  I1,
  input  I2,
  input  I3,
  input  I4,
  input  I5,
  input  I6,
  input  I7,
  input  I8,
  input  LE,
  output O1,
  output O2,
  output O3,
  output O4,
  output O8,
  output O7,
  output O6,
  output O5,
  output GND
);

  wire d_ff_1_q, d_ff_2_q, d_ff_3_q, d_ff_4_q, d_ff_5_q, d_ff_6_q, d_ff_7_q, d_ff_8_q, not_1_out;

  not not_1 (not_1_out, NOE);
  assign GND = VCC_6V ? ~VCC_6V : 1'bz;  // Controlled_Inverter controlled_inverter_1
  D_Flip_Flop #(.trigger("high")) d_ff_1 (.clk(LE), .D(I1), .Q(d_ff_1_q));  // open: Qn, preset, reset
  D_Flip_Flop #(.trigger("high")) d_ff_2 (.clk(LE), .D(I2), .Q(d_ff_2_q));  // open: Qn, preset, reset
  D_Flip_Flop #(.trigger("high")) d_ff_3 (.clk(LE), .D(I3), .Q(d_ff_3_q));  // open: Qn, preset, reset
  D_Flip_Flop #(.trigger("high")) d_ff_4 (.clk(LE), .D(I4), .Q(d_ff_4_q));  // open: Qn, preset, reset
  D_Flip_Flop #(.trigger("high")) d_ff_5 (.clk(LE), .D(I5), .Q(d_ff_5_q));  // open: Qn, preset, reset
  D_Flip_Flop #(.trigger("high")) d_ff_6 (.clk(LE), .D(I6), .Q(d_ff_6_q));  // open: Qn, preset, reset
  D_Flip_Flop #(.trigger("high")) d_ff_7 (.clk(LE), .D(I7), .Q(d_ff_7_q));  // open: Qn, preset, reset
  D_Flip_Flop #(.trigger("high")) d_ff_8 (.clk(LE), .D(I8), .Q(d_ff_8_q));  // open: Qn, preset, reset
  assign O1 = not_1_out ? d_ff_1_q : 1'bz;  // Controlled_Buffer controlled_buffer_1
  assign O2 = not_1_out ? d_ff_2_q : 1'bz;  // Controlled_Buffer controlled_buffer_2
  assign O3 = not_1_out ? d_ff_3_q : 1'bz;  // Controlled_Buffer controlled_buffer_3
  assign O4 = not_1_out ? d_ff_4_q : 1'bz;  // Controlled_Buffer controlled_buffer_4
  assign O8 = not_1_out ? d_ff_5_q : 1'bz;  // Controlled_Buffer controlled_buffer_5
  assign O7 = not_1_out ? d_ff_6_q : 1'bz;  // Controlled_Buffer controlled_buffer_6
  assign O6 = not_1_out ? d_ff_7_q : 1'bz;  // Controlled_Buffer controlled_buffer_7
  assign O5 = not_1_out ? d_ff_8_q : 1'bz;  // Controlled_Buffer controlled_buffer_8
endmodule

module DEMUX_74AC11138 (
  input  VCC,
  input  A,
  input  B,
  input  C,
  input  NE3,
  input  NE2,
  input  E1,
  output GND,
  output Y1,
  output Y2,
  output Y3,
  output Y4,
  output Y5,
  output Y6,
  output Y7,
  output Y8
);

  wire and_1_out, not_1_out, not_2_out, not_3_out;

  assign GND = VCC ? ~VCC : 1'bz;  // Controlled_Inverter controlled_inverter_1
  not not_1 (not_1_out, A);
  not not_2 (not_2_out, B);
  not not_3 (not_3_out, C);
  and and_1 (and_1_out, ~NE3, ~NE2, E1);  // AND_Gate
  nand nand_1 (Y1, not_1_out, not_2_out, not_3_out, and_1_out);
  nand nand_2 (Y2, A, not_2_out, not_3_out, and_1_out);
  nand nand_3 (Y3, not_1_out, B, not_3_out, and_1_out);
  nand nand_4 (Y4, A, B, not_3_out, and_1_out);
  nand nand_5 (Y5, not_1_out, not_2_out, C, and_1_out);
  nand nand_6 (Y6, A, not_2_out, C, and_1_out);
  nand nand_7 (Y7, not_1_out, B, C, and_1_out);
  nand nand_8 (Y8, A, B, C, and_1_out);
endmodule

module SN74AC00N_NAND (
  input  VCC,
  input  A1,
  input  B1,
  input  B4,
  input  A4,
  input  A2,
  input  B2,
  input  B3,
  input  A3,
  output Y1,
  output Y4,
  output Y2,
  output GND,
  output Y3
);

  nand nand_1 (Y1, B1, A1);
  nand nand_2 (Y2, B2, A2);
  assign GND = VCC ? ~VCC : 1'bz;  // Controlled_Inverter controlled_inverter_1
  nand nand_3 (Y4, B4, A4);
  nand nand_4 (Y3, B3, A3);
endmodule

module SN74AC32N_OR (
  input  VCC,
  input  A1,
  input  B1,
  input  B4,
  input  A4,
  input  A2,
  input  B2,
  input  B3,
  input  A3,
  output Y1,
  output Y4,
  output Y2,
  output GND,
  output Y3
);

  or or_1 (Y1, B1, A1);
  or or_2 (Y2, B2, A2);
  assign GND = VCC ? ~VCC : 1'bz;  // Controlled_Inverter controlled_inverter_1
  or or_3 (Y4, B4, A4);
  or or_4 (Y3, B3, A3);
endmodule

module SN74AC04N_NOT (
  input  A1,
  input  VCC,
  input  A4,
  input  A2,
  input  A5,
  input  A3,
  input  A6,
  output Y1,
  output Y4,
  output Y2,
  output Y5,
  output Y3,
  output GND,
  output Y6
);

  not not_1 (Y1, A1);
  not not_2 (Y2, A2);
  not not_3 (Y3, A3);
  assign GND = VCC ? ~VCC : 1'bz;  // Controlled_Inverter controlled_inverter_1
  not not_4 (Y4, A4);
  not not_5 (Y5, A5);
  not not_6 (Y6, A6);
endmodule

module SN74AC08N_AND (
  input  VCC,
  input  A1,
  input  B1,
  input  B4,
  input  A4,
  input  A2,
  input  B2,
  input  B3,
  input  A3,
  output Y1,
  output Y4,
  output Y2,
  output GND,
  output Y3
);

  and and_1 (Y1, B1, A1);
  and and_2 (Y2, B2, A2);
  assign GND = VCC ? ~VCC : 1'bz;  // Controlled_Inverter controlled_inverter_1
  and and_3 (Y4, B4, A4);
  and and_4 (Y3, B3, A3);
endmodule

module CD74AC02EE4_NOR (
  input  VCC,
  input  A1,
  input  B1,
  input  B4,
  input  A4,
  input  A2,
  input  B2,
  input  B3,
  input  A3,
  output Y1,
  output Y4,
  output Y2,
  output Y3,
  output GND
);

  nor nor_1 (Y1, A1, B1);
  nor nor_2 (Y2, A2, B2);
  assign GND = VCC ? ~VCC : 1'bz;  // Controlled_Inverter controlled_inverter_1
  nor nor_3 (Y4, A4, B4);
  nor nor_4 (Y3, A3, B3);
endmodule

module SN74AC573N_Latch (
  input  VCC_5V,
  input  NOE,
  input  I1,
  input  I2,
  input  I3,
  input  I4,
  input  I5,
  input  I6,
  input  I7,
  input  I8,
  input  LE,
  output O1,
  output O2,
  output O3,
  output O4,
  output O8,
  output O7,
  output O6,
  output O5,
  output GND
);

  wire d_ff_1_q, d_ff_2_q, d_ff_3_q, d_ff_4_q, d_ff_5_q, d_ff_6_q, d_ff_7_q, d_ff_8_q, not_1_out;

  not not_1 (not_1_out, NOE);
  assign GND = VCC_5V ? ~VCC_5V : 1'bz;  // Controlled_Inverter controlled_inverter_1
  D_Flip_Flop #(.trigger("high")) d_ff_1 (.clk(LE), .D(I1), .Q(d_ff_1_q));  // open: Qn, preset, reset
  D_Flip_Flop #(.trigger("high")) d_ff_2 (.clk(LE), .D(I2), .Q(d_ff_2_q));  // open: Qn, preset, reset
  D_Flip_Flop #(.trigger("high")) d_ff_3 (.clk(LE), .D(I3), .Q(d_ff_3_q));  // open: Qn, preset, reset
  D_Flip_Flop #(.trigger("high")) d_ff_4 (.clk(LE), .D(I4), .Q(d_ff_4_q));  // open: Qn, preset, reset
  D_Flip_Flop #(.trigger("high")) d_ff_5 (.clk(LE), .D(I5), .Q(d_ff_5_q));  // open: Qn, preset, reset
  D_Flip_Flop #(.trigger("high")) d_ff_6 (.clk(LE), .D(I6), .Q(d_ff_6_q));  // open: Qn, preset, reset
  D_Flip_Flop #(.trigger("high")) d_ff_7 (.clk(LE), .D(I7), .Q(d_ff_7_q));  // open: Qn, preset, reset
  D_Flip_Flop #(.trigger("high")) d_ff_8 (.clk(LE), .D(I8), .Q(d_ff_8_q));  // open: Qn, preset, reset
  assign O1 = not_1_out ? d_ff_1_q : 1'bz;  // Controlled_Buffer controlled_buffer_1
  assign O2 = not_1_out ? d_ff_2_q : 1'bz;  // Controlled_Buffer controlled_buffer_2
  assign O3 = not_1_out ? d_ff_3_q : 1'bz;  // Controlled_Buffer controlled_buffer_3
  assign O4 = not_1_out ? d_ff_4_q : 1'bz;  // Controlled_Buffer controlled_buffer_4
  assign O8 = not_1_out ? d_ff_5_q : 1'bz;  // Controlled_Buffer controlled_buffer_5
  assign O7 = not_1_out ? d_ff_6_q : 1'bz;  // Controlled_Buffer controlled_buffer_6
  assign O6 = not_1_out ? d_ff_7_q : 1'bz;  // Controlled_Buffer controlled_buffer_7
  assign O5 = not_1_out ? d_ff_8_q : 1'bz;  // Controlled_Buffer controlled_buffer_8
endmodule

module MUX_74AC11257 (
  input  nOE,
  input  nA_B,
  input  A1,
  input  B1,
  input  A2,
  input  B2,
  input  VCC1_5V,
  input  VCC2_5V,
  input  A3,
  input  B3,
  input  A4,
  input  B4,
  output Y1,
  output Y2,
  output GND1,
  output GND2,
  output GND3,
  output GND4,
  output Y3,
  output Y4
);

  wire and_1_out, and_2_out, and_3_out, and_4_out, and_5_out, and_6_out, and_7_out, and_8_out, nor_1_out,
       nor_2_out, nor_3_out, nor_4_out, not_1_out, not_2_out, not_3_out, not_4_out, not_5_out, not_6_out;

  not not_1 (not_1_out, nOE);
  not not_2 (not_2_out, nA_B);
  and and_1 (and_1_out, not_2_out, A1);
  and and_2 (and_2_out, nA_B, B1);
  and and_3 (and_3_out, not_2_out, A2);
  and and_4 (and_4_out, nA_B, B2);
  and and_5 (and_5_out, not_2_out, A3);
  and and_6 (and_6_out, nA_B, B3);
  and and_7 (and_7_out, not_2_out, A4);
  and and_8 (and_8_out, nA_B, B4);
  nor nor_1 (nor_1_out, and_1_out, and_2_out);
  nor nor_2 (nor_2_out, and_3_out, and_4_out);
  nor nor_3 (nor_3_out, and_5_out, and_6_out);
  nor nor_4 (nor_4_out, and_7_out, and_8_out);
  not not_3 (not_3_out, nor_1_out);
  assign Y1 = not_1_out ? not_3_out : 1'bz;  // Controlled_Buffer controlled_buffer_1
  not not_4 (not_4_out, nor_2_out);
  assign Y2 = not_1_out ? not_4_out : 1'bz;  // Controlled_Buffer controlled_buffer_2
  not not_5 (not_5_out, nor_3_out);
  assign Y3 = not_1_out ? not_5_out : 1'bz;  // Controlled_Buffer controlled_buffer_3
  not not_6 (not_6_out, nor_4_out);
  assign Y4 = not_1_out ? not_6_out : 1'bz;  // Controlled_Buffer controlled_buffer_4
  assign GND1 = VCC1_5V ? ~VCC1_5V : 1'bz;  // Controlled_Inverter controlled_inverter_1
  assign GND3 = VCC2_5V ? ~VCC2_5V : 1'bz;  // Controlled_Inverter controlled_inverter_2

  assign GND2 = GND1;
  assign GND4 = GND3;
endmodule

module CD74AC238E_adder (
  input  Cin,
  input  Vcc_5V,
  input  A1,
  input  B1,
  input  B2,
  input  A2,
  input  B3,
  input  A3,
  input  A4,
  input  B4,
  output S0,
  output S1,
  output S2,
  output S3,
  output Cout,
  output GND
);

  wire and_1_out, and_2_out, and_3_out, and_4_out, and_5_out, and_6_out, and_7_out, and_8_out, or_1_out,
       or_2_out, or_3_out, xor_1_out, xor_2_out, xor_3_out, xor_4_out;

  xor xor_1 (xor_1_out, A1, B1);
  and and_1 (and_1_out, A1, B1);
  xor xor_2 (xor_2_out, B2, A2);
  and and_2 (and_2_out, B2, A2);
  xor xor_3 (xor_3_out, B3, A3);
  and and_3 (and_3_out, B3, A3);
  xor xor_4 (xor_4_out, A4, B4);
  and and_4 (and_4_out, A4, B4);
  xor xor_5 (S0, Cin, xor_1_out);
  and and_5 (and_5_out, Cin, xor_1_out);
  or or_1 (or_1_out, and_5_out, and_1_out);
  xor xor_6 (S1, or_1_out, xor_2_out);
  and and_6 (and_6_out, or_1_out, xor_2_out);
  or or_2 (or_2_out, and_6_out, and_2_out);
  xor xor_7 (S2, or_2_out, xor_3_out);
  and and_7 (and_7_out, or_2_out, xor_3_out);
  or or_3 (or_3_out, and_7_out, and_3_out);
  xor xor_8 (S3, or_3_out, xor_4_out);
  and and_8 (and_8_out, or_3_out, xor_4_out);
  or or_4 (Cout, and_8_out, and_4_out);
  assign GND = Vcc_5V ? ~Vcc_5V : 1'bz;  // Controlled_Inverter controlled_inverter_1
endmodule

module CD74HC85E_MagCMP (
  input  VCC,
  input  B4,
  input  ALBin,
  input  A4,
  input  AEBin,
  input  B3,
  input  AHBin,
  input  A3,
  input  A2,
  input  B2,
  input  A1,
  input  B1,
  output AHBout,
  output AEBout,
  output ALBout,
  output GND
);

  assign GND = VCC ? ~VCC : 1'bz;  // Controlled_Inverter controlled_inverter_1
  _7485 u_7485_1 (
    .pin1(B4), .pin2(ALBin), .pin3(AEBin), .pin4(AHBin), .pin5(AHBout), .pin6(AEBout), .pin7(ALBout),
    .pin15(A4), .pin14(B3), .pin13(A3), .pin12(A2), .pin11(B2), .pin10(A1), .pin9(B1));
endmodule

module CD74AC163E_Counter (
  input  nCLR,
  input  VCC,
  input  CLK,
  input  A,
  input  B,
  input  C,
  input  D,
  input  ENP,
  input  ENT,
  input  nLD,
  output RCO,
  output QA,
  output QB,
  output QC,
  output QD,
  output GND
);

  assign GND = VCC ? ~VCC : 1'bz;  // Controlled_Inverter controlled_inverter_1
  _74163 u_74163_1 (
    .pin1(nCLR), .pin2(CLK), .pin3(A), .pin4(B), .pin5(C), .pin6(D), .pin7(ENP), .pin15(RCO), .pin14(QA),
    .pin13(QB), .pin12(QC), .pin11(QD), .pin10(ENT), .pin9(nLD));
endmodule

module CD74AC139E_DEMUX2 (
  input  VCC,
  input  nG1,
  input  A1,
  input  B1,
  input  nG2,
  input  A2,
  input  B2,
  output out_8,
  output out_9,
  output out_10,
  output out_11,
  output out_12,
  output out_13,
  output out_14,
  output out_15,
  output GND
);

  wire not_1_out, not_2_out, not_3_out, not_4_out, not_5_out, not_6_out, not_7_out, not_8_out, not_9_out,
       not_10_out;

  assign GND = VCC ? ~VCC : 1'bz;  // Controlled_Inverter controlled_inverter_1
  not not_1 (not_1_out, nG1);
  not not_2 (not_2_out, A1);
  not not_3 (not_3_out, B1);
  not not_4 (not_4_out, nG2);
  not not_5 (not_5_out, A2);
  not not_6 (not_6_out, B2);
  not not_7 (not_7_out, not_2_out);
  not not_8 (not_8_out, not_3_out);
  not not_9 (not_9_out, not_5_out);
  not not_10 (not_10_out, not_6_out);
  nand nand_1 (out_8, not_2_out, not_3_out, not_1_out);
  nand nand_2 (out_9, not_7_out, not_3_out, not_1_out);
  nand nand_3 (out_10, not_2_out, not_8_out, not_1_out);
  nand nand_4 (out_11, not_7_out, not_8_out, not_1_out);
  nand nand_5 (out_12, not_5_out, not_6_out, not_4_out);
  nand nand_6 (out_13, not_9_out, not_6_out, not_4_out);
  nand nand_7 (out_14, not_5_out, not_10_out, not_4_out);
  nand nand_8 (out_15, not_9_out, not_10_out, not_4_out);
endmodule

module CD74AC138E_DEMUX3 (
  input  VCC,
  input  A,
  input  B,
  input  C,
  input  NE3,
  input  NE2,
  input  E1,
  output GND,
  output Y1,
  output Y2,
  output Y3,
  output Y4,
  output Y5,
  output Y6,
  output Y7,
  output Y8
);

  wire and_1_out, not_1_out, not_2_out, not_3_out;

  assign GND = VCC ? ~VCC : 1'bz;  // Controlled_Inverter controlled_inverter_1
  not not_1 (not_1_out, A);
  not not_2 (not_2_out, B);
  not not_3 (not_3_out, C);
  and and_1 (and_1_out, ~NE3, ~NE2, E1);  // AND_Gate
  nand nand_1 (Y1, not_1_out, not_2_out, not_3_out, and_1_out);
  nand nand_2 (Y2, A, not_2_out, not_3_out, and_1_out);
  nand nand_3 (Y3, not_1_out, B, not_3_out, and_1_out);
  nand nand_4 (Y4, A, B, not_3_out, and_1_out);
  nand nand_5 (Y5, not_1_out, not_2_out, C, and_1_out);
  nand nand_6 (Y6, A, not_2_out, C, and_1_out);
  nand nand_7 (Y7, not_1_out, B, C, and_1_out);
  nand nand_8 (Y8, A, B, C, and_1_out);
endmodule

module SN74HC27N_TNOR (
  input  VCC,
  input  A1,
  input  B1,
  input  C1,
  input  A2,
  input  B2,
  input  C2,
  input  A3,
  input  B3,
  input  C3,
  output Y1,
  output Y2,
  output Y3,
  output GND
);

  assign GND = VCC ? ~VCC : 1'bz;  // Controlled_Inverter controlled_inverter_1
  nor nor_1 (Y1, A1, B1, C1);
  nor nor_2 (Y2, A2, B2, C2);
  nor nor_3 (Y3, A3, B3, C3);
endmodule

module TEMP_TRANSCEIVER (
  input  SEL,
  input  A1,
  input  in_3,
  input  B1,
  input  in_5,
  input  C1,
  input  in_7,
  input  D1,
  input  in_9,
  input  E1,
  input  in_11,
  input  F1,
  input  in_13,
  input  G1,
  input  in_15,
  input  H1,
  input  in_17,
  output out_18,
  output out_19,
  output out_20,
  output out_21,
  output out_22,
  output out_23,
  output out_24,
  output out_25,
  output out_26,
  output out_27,
  output out_28,
  output out_29,
  output out_30,
  output out_31,
  output out_32,
  output out_33
);
endmodule
